// Logisim project CPU_Pipeline_B2.circ as structural Verilog: 19 circuits, main circuit main
module main (
);

  wire branch, CLK, comparador, comparator_1_eq, comparator_2_eq, ex_mem_1_branch_s, ex_mem_1_mem_read_s,
       ex_mem_1_mem_to_reg_s, ex_mem_1_mem_write_s, EX_MEM_RegWrite, fowarding_unit_1_forwardingmem,
       haz_detection_1_pipelinestall, id_ex_1_alusrc_s, id_ex_1_branch_s, id_ex_1_mem_to_reg_s,
       id_ex_1_mem_write_s, ID_EX_mem_read, ID_EX_RegWrite, IF_ID_write, mem_wb_1_mem_to_reg_s,
       MEM_WB_RegWrite, not_1_out, not_2_out, PC_write, ula_1_zero;
  wire [1:0] beq_fowarding_1_forwarda, beq_fowarding_1_forwardb, Fowarding_A, Fowarding_B, id_ex_1_aluop_s;
  wire [3:0] alu_control_1_alu_input;
  wire [4:0] ex_mem_1_ex_mem_rs2, ex_mem_1_rc_addr_saida, EX_MEM_rd, id_ex_1_id_ex_rs1_s,
       id_ex_1_id_ex_rs2_s, ID_EX_rc, ID_EX_rs1, ID_EX_rs2, if_id_1_instr_saida_2, mem_wb_1_rc_addrs_saida,
       MEM_WB_rd;
  wire [6:0] if_id_1_instr_saida, multiplexer_4_out;
  wire [7:0] control_1_control_s, redutor_32x8bits_1_saida;
  wire [23:0] pc_24_bits_1_s;
  wire [31:0] adder_1_out, adder_2_out, ex_mem_1_rb_saida, EX_MEM_ALU, extsinal_1_saida, id_ex_1_imm_saida,
       id_ex_1_instr_saida, id_ex_1_pc_saida, id_ex_1_ra_saida, id_ex_1_rb_saida, if_id_1_pc_saida, imm,
       mem_wb_1_alu_result_s, mem_wb_1_read_data_s, MEM_WB_data, multiplexer_1_out, multiplexer_2_out,
       multiplexer_3_out, multiplexer_5_out, multiplexer_6_out, multiplexer_7_out, multiplexer_8_out,
       multiplexer_9_out, ram_1_dout, rom_1_data, rs1, rs2, ula_1_c;
  wire [31:12] if_id_1_instr_saida_3;

  Multiplexer #(.width(32)) multiplexer_1 (.in0(adder_1_out), .in1(adder_2_out), .out(multiplexer_1_out), .sel(branch));
  PC_24_bits pc_24_bits_1 (.E(multiplexer_1_out), .CLK(CLK), .W(PC_write), .S(pc_24_bits_1_s));
  ROM #(.dataWidth(32)) rom_1 (.addr(pc_24_bits_1_s[7:0]), .data(rom_1_data));
  extSinal extsinal_1 (.entrada(pc_24_bits_1_s), .Saida(extsinal_1_saida));
  Adder #(.width(32)) adder_1 (.a(32'h1), .b(extsinal_1_saida), .out(adder_1_out));  // open: cin, cout
  Clock clock_1 (.out(CLK));
  IF_ID if_id_1 (
    .W_enable(IF_ID_write), .PC(extsinal_1_saida), .Instr(rom_1_data), .CLK(CLK),
    .PC_saida(if_id_1_pc_saida),
    .Instr_saida({if_id_1_instr_saida_3[31:25], ID_EX_rs2, ID_EX_rs1, if_id_1_instr_saida_3[14:12], if_id_1_instr_saida_2, if_id_1_instr_saida}));  // open: Flush
  Adder #(.width(32)) adder_2 (.a(imm), .b(if_id_1_pc_saida), .out(adder_2_out));  // open: cin, cout
  Beq_Fowarding beq_fowarding_1 (
    .IF_ID_rs1(ID_EX_rs1), .IF_ID_rs2(ID_EX_rs2), .EX_MEM_rd(EX_MEM_rd), .MEM_WB_rd(MEM_WB_rd),
    .MEM_WB_RegWrite(MEM_WB_RegWrite), .EX_MEM_RegWrite(EX_MEM_RegWrite),
    .ForwardA(beq_fowarding_1_forwarda), .ForwardB(beq_fowarding_1_forwardb));
  not not_1 (not_1_out, CLK);
  Haz_Detection haz_detection_1 (
    .IF_ID_Rs2(ID_EX_rs2), .IF_ID_Rs1(ID_EX_rs1), .ID_EX_Rd(ID_EX_rc), .ID_EX_MEMRead(ID_EX_mem_read),
    .OP(if_id_1_instr_saida), .ID_EX_RegWrite(ID_EX_RegWrite), .clk(CLK),
    .PipelineStall(haz_detection_1_pipelinestall), .IF_ID_write(IF_ID_write), .PC_write(PC_write));
  Control control_1 (.OP(if_id_1_instr_saida), .comparador(comparador), .Control_s(control_1_control_s));
  Multiplexer #(.select(2), .width(32)) multiplexer_2 (
    .in0(rs1), .in1(MEM_WB_data), .in2(EX_MEM_ALU), .out(multiplexer_2_out), .sel(beq_fowarding_1_forwarda));  // open: in3
  Multiplexer #(.select(2), .width(32)) multiplexer_3 (
    .in0(rs2), .in1(MEM_WB_data), .in2(EX_MEM_ALU), .out(multiplexer_3_out));  // open: in3, sel
  Multiplexer #(.width(8)) multiplexer_4 (
    .in0(control_1_control_s), .in1({8{1'b0}}), .out({branch, multiplexer_4_out}),
    .sel(haz_detection_1_pipelinestall));
  RB_32x32bits rb_32x32bits_1 (
    .R_address_A(ID_EX_rs1), .R_address_B(ID_EX_rs2), .Write_address(mem_wb_1_rc_addrs_saida),
    .Write_data(MEM_WB_data), .Write_enable(MEM_WB_RegWrite), .Clock(not_1_out), .Saida_A(rs1), .Saida_B(rs2));
  Imm_generator imm_generator_1 (
    .Instr({if_id_1_instr_saida_3[31:25], ID_EX_rs2, ID_EX_rs1, if_id_1_instr_saida_3[14:12], if_id_1_instr_saida_2, if_id_1_instr_saida}),
    .Saida(imm));
  Comparator #(.width(32)) comparator_1 (
    .a(multiplexer_2_out), .b(multiplexer_3_out), .eq(comparator_1_eq));  // open: gt, lt
  and and_1 (comparador, comparator_1_eq, not_2_out);
  not not_2 (not_2_out, comparator_2_eq);
  Comparator #(.width(32)) comparator_2 (.a(rs1), .b({32{1'b0}}), .eq(comparator_2_eq));  // open: gt, lt
  ID_EX id_ex_1 (
    .RegWrite(multiplexer_4_out[0]), .Mem_to_Reg(multiplexer_4_out[1]), .Mem_read(multiplexer_4_out[2]),
    .Mem_write(multiplexer_4_out[3]), .ALUsrc(multiplexer_4_out[4]), .ALUop(multiplexer_4_out[6:5]),
    .W_enable(1'b1), .PC(if_id_1_pc_saida), .ra(rs1), .rb(rs2), .rc_addr(if_id_1_instr_saida_2), .Imm(imm),
    .Instr({if_id_1_instr_saida_3[31:25], ID_EX_rs2, ID_EX_rs1, if_id_1_instr_saida_3[14:12], if_id_1_instr_saida_2, if_id_1_instr_saida}),
    .CLK(CLK), .Branch(branch), .ID_EX_rs1(ID_EX_rs1), .ID_EX_rs2(ID_EX_rs2), .RegWrite_s(ID_EX_RegWrite),
    .Mem_to_Reg_s(id_ex_1_mem_to_reg_s), .Mem_read_s(ID_EX_mem_read), .Mem_write_s(id_ex_1_mem_write_s),
    .ALUsrc_s(id_ex_1_alusrc_s), .ALUop_s(id_ex_1_aluop_s), .PC_saida(id_ex_1_pc_saida),
    .ra_saida(id_ex_1_ra_saida), .rb_saida(id_ex_1_rb_saida), .Imm_saida(id_ex_1_imm_saida),
    .Instr_saida(id_ex_1_instr_saida), .rc_addr_saida(ID_EX_rc), .Branch_s(id_ex_1_branch_s),
    .ID_EX_rs1_s(id_ex_1_id_ex_rs1_s), .ID_EX_rs2_s(id_ex_1_id_ex_rs2_s));  // open: Zero, Flush, Zero_s
  Multiplexer #(.select(2), .width(32)) multiplexer_5 (
    .in0(id_ex_1_ra_saida), .in1(MEM_WB_data), .in2(EX_MEM_ALU), .out(multiplexer_5_out));  // open: in3, sel
  Multiplexer #(.select(2), .width(32)) multiplexer_6 (
    .in0(id_ex_1_rb_saida), .in1(MEM_WB_data), .in2(EX_MEM_ALU), .out(multiplexer_6_out));  // open: in3, sel
  Multiplexer #(.width(32)) multiplexer_7 (
    .in0(multiplexer_6_out), .in1(id_ex_1_imm_saida), .out(multiplexer_7_out), .sel(id_ex_1_alusrc_s));
  ALU_control alu_control_1 (
    .ALU_Op(id_ex_1_aluop_s), .Instruction(id_ex_1_instr_saida), .ALU_input(alu_control_1_alu_input));
  Fowarding_Unit fowarding_unit_1 (
    .EXMEMRs2(ex_mem_1_ex_mem_rs2), .ExMemRd(EX_MEM_rd), .IDEXRs1(id_ex_1_id_ex_rs1_s), .MemWbRd(MEM_WB_rd),
    .IDEXRt(id_ex_1_id_ex_rs2_s), .EXMEMRegWrite(EX_MEM_RegWrite), .MEMWBRegWrite(MEM_WB_RegWrite),
    .EXMEMMemWrite(ex_mem_1_mem_write_s), .ForwardA(Fowarding_A), .ForwardB(Fowarding_B),
    .ForwardingMEM(fowarding_unit_1_forwardingmem));
  ULA ula_1 (
    .A(multiplexer_5_out), .B(multiplexer_7_out), .ALUop(alu_control_1_alu_input), .C(ula_1_c),
    .Zero(ula_1_zero));
  EX_MEM ex_mem_1 (
    .RegWrite(ID_EX_RegWrite), .Mem_to_Reg(id_ex_1_mem_to_reg_s), .Mem_read(ID_EX_mem_read),
    .Mem_write(id_ex_1_mem_write_s), .W_enable(1'b1), .PC(id_ex_1_pc_saida), .ALU_result(ula_1_c),
    .zero(ula_1_zero), .rb(id_ex_1_rb_saida), .rc_addr(ID_EX_rc), .CLK(CLK), .Branch(id_ex_1_branch_s),
    .EX_MEM_rd(ID_EX_rc), .EXMEMrs2(id_ex_1_id_ex_rs2_s), .RegWrite_s(EX_MEM_RegWrite),
    .Mem_to_Reg_s(ex_mem_1_mem_to_reg_s), .Mem_read_s(ex_mem_1_mem_read_s),
    .Mem_write_s(ex_mem_1_mem_write_s), .ALU_result_s(EX_MEM_ALU), .rb_saida(ex_mem_1_rb_saida),
    .rc_addr_saida(ex_mem_1_rc_addr_saida), .Branch_s(ex_mem_1_branch_s), .EX_MEM_rd_s(EX_MEM_rd),
    .EX_MEM_rs2(ex_mem_1_ex_mem_rs2));  // open: Flush, PC_salto, zero_saida
  Redutor_32x8bits redutor_32x8bits_1 (.Entrada(EX_MEM_ALU), .Saida(redutor_32x8bits_1_saida));
  Multiplexer #(.width(32)) multiplexer_8 (
    .in0(ex_mem_1_rb_saida), .in1(MEM_WB_data), .out(multiplexer_8_out), .sel(fowarding_unit_1_forwardingmem));
  RAM #(.dataWidth(32), .enables("line")) ram_1 (
    .addr(redutor_32x8bits_1_saida), .we(ex_mem_1_mem_write_s), .clk(CLK), .din(multiplexer_8_out),
    .dout(ram_1_dout));
  Multiplexer #(.width(32)) multiplexer_9 (
    .in0({32{1'b0}}), .in1(ram_1_dout), .out(multiplexer_9_out), .sel(ex_mem_1_mem_read_s));
  MEM_WB mem_wb_1 (
    .RegWrite(EX_MEM_RegWrite), .Mem_to_Reg(ex_mem_1_mem_to_reg_s), .W_enable(1'b1),
    .Read_data(multiplexer_9_out), .ALU_result(EX_MEM_ALU), .rc_addrs(ex_mem_1_rc_addr_saida), .CLK(CLK),
    .MEM_WB_rd(ex_mem_1_rc_addr_saida), .RegWrite_s(MEM_WB_RegWrite), .Mem_to_Reg_s(mem_wb_1_mem_to_reg_s),
    .Read_data_s(mem_wb_1_read_data_s), .ALU_result_s(mem_wb_1_alu_result_s),
    .rc_addrs_saida(mem_wb_1_rc_addrs_saida), .MEM_WB_rd_s(MEM_WB_rd));  // open: Flush
  Multiplexer #(.width(32)) multiplexer_10 (
    .in0(mem_wb_1_alu_result_s), .in1(mem_wb_1_read_data_s), .out(MEM_WB_data), .sel(mem_wb_1_mem_to_reg_s));

  // Notes on the sheet:
  //   Salto
  //   branch
  //   PC + 1
  //   Pular de 1 em 1
  //   PC
  //   OP
  //   Ra
  //   Rb
  //   Rc
  //   rc
  //   resultado
  //   <---
  //   <---
  //   <---
  //   Sinais de Controle
endmodule

module registrador_32bits (
  input  [31:0] E,
  input  CLK,
  input  W,
  output [31:0] S
);

  wire multiplexer_1_out, multiplexer_2_out, multiplexer_3_out, multiplexer_4_out, multiplexer_5_out,
       multiplexer_6_out, multiplexer_7_out, multiplexer_8_out, multiplexer_9_out, multiplexer_10_out,
       multiplexer_11_out, multiplexer_12_out, multiplexer_13_out, multiplexer_14_out, multiplexer_15_out,
       multiplexer_16_out, multiplexer_17_out, multiplexer_18_out, multiplexer_19_out, multiplexer_20_out,
       multiplexer_21_out, multiplexer_22_out, multiplexer_23_out, multiplexer_24_out, multiplexer_25_out,
       multiplexer_26_out, multiplexer_27_out, multiplexer_28_out, multiplexer_29_out, multiplexer_30_out,
       multiplexer_31_out, multiplexer_32_out;

  D_Flip_Flop d_ff_1 (.D(multiplexer_1_out), .clk(CLK), .Q(S[0]));  // open: Qn, preset, reset
  Multiplexer multiplexer_1 (.in0(S[0]), .in1(E[0]), .out(multiplexer_1_out), .sel(W));
  D_Flip_Flop d_ff_2 (.D(multiplexer_2_out), .clk(CLK), .Q(S[8]));  // open: Qn, preset, reset
  Multiplexer multiplexer_2 (.in0(S[8]), .in1(E[8]), .out(multiplexer_2_out), .sel(W));
  D_Flip_Flop d_ff_3 (.D(multiplexer_3_out), .clk(CLK), .Q(S[16]));  // open: Qn, preset, reset
  Multiplexer multiplexer_3 (.in0(S[16]), .in1(E[16]), .out(multiplexer_3_out), .sel(W));
  D_Flip_Flop d_ff_4 (.D(multiplexer_4_out), .clk(CLK), .Q(S[24]));  // open: Qn, preset, reset
  Multiplexer multiplexer_4 (.in0(S[24]), .in1(E[24]), .out(multiplexer_4_out), .sel(W));
  Multiplexer multiplexer_5 (.in0(S[1]), .in1(E[1]), .out(multiplexer_5_out), .sel(W));
  Multiplexer multiplexer_6 (.in0(S[9]), .in1(E[9]), .out(multiplexer_6_out), .sel(W));
  Multiplexer multiplexer_7 (.in0(S[17]), .in1(E[17]), .out(multiplexer_7_out), .sel(W));
  Multiplexer multiplexer_8 (.in0(S[25]), .in1(E[25]), .out(multiplexer_8_out), .sel(W));
  D_Flip_Flop d_ff_5 (.D(multiplexer_5_out), .clk(CLK), .Q(S[1]));  // open: Qn, preset, reset
  D_Flip_Flop d_ff_6 (.D(multiplexer_6_out), .clk(CLK), .Q(S[9]));  // open: Qn, preset, reset
  D_Flip_Flop d_ff_7 (.D(multiplexer_7_out), .clk(CLK), .Q(S[17]));  // open: Qn, preset, reset
  D_Flip_Flop d_ff_8 (.D(multiplexer_8_out), .clk(CLK), .Q(S[25]));  // open: Qn, preset, reset
  Multiplexer multiplexer_9 (.in0(S[2]), .in1(E[2]), .out(multiplexer_9_out), .sel(W));
  Multiplexer multiplexer_10 (.in0(S[10]), .in1(E[10]), .out(multiplexer_10_out), .sel(W));
  Multiplexer multiplexer_11 (.in0(S[18]), .in1(E[18]), .out(multiplexer_11_out), .sel(W));
  Multiplexer multiplexer_12 (.in0(S[26]), .in1(E[26]), .out(multiplexer_12_out), .sel(W));
  D_Flip_Flop d_ff_9 (.D(multiplexer_9_out), .clk(CLK), .Q(S[2]));  // open: Qn, preset, reset
  D_Flip_Flop d_ff_10 (.D(multiplexer_10_out), .clk(CLK), .Q(S[10]));  // open: Qn, preset, reset
  D_Flip_Flop d_ff_11 (.D(multiplexer_11_out), .clk(CLK), .Q(S[18]));  // open: Qn, preset, reset
  D_Flip_Flop d_ff_12 (.D(multiplexer_12_out), .clk(CLK), .Q(S[26]));  // open: Qn, preset, reset
  D_Flip_Flop d_ff_13 (.D(multiplexer_13_out), .clk(CLK), .Q(S[3]));  // open: Qn, preset, reset
  Multiplexer multiplexer_13 (.in0(S[3]), .in1(E[3]), .out(multiplexer_13_out), .sel(W));
  D_Flip_Flop d_ff_14 (.D(multiplexer_14_out), .clk(CLK), .Q(S[11]));  // open: Qn, preset, reset
  Multiplexer multiplexer_14 (.in0(S[11]), .in1(E[11]), .out(multiplexer_14_out), .sel(W));
  D_Flip_Flop d_ff_15 (.D(multiplexer_15_out), .clk(CLK), .Q(S[19]));  // open: Qn, preset, reset
  Multiplexer multiplexer_15 (.in0(S[19]), .in1(E[19]), .out(multiplexer_15_out), .sel(W));
  D_Flip_Flop d_ff_16 (.D(multiplexer_16_out), .clk(CLK), .Q(S[27]));  // open: Qn, preset, reset
  Multiplexer multiplexer_16 (.in0(S[27]), .in1(E[27]), .out(multiplexer_16_out), .sel(W));
  Multiplexer multiplexer_17 (.in0(S[4]), .in1(E[4]), .out(multiplexer_17_out), .sel(W));
  Multiplexer multiplexer_18 (.in0(S[12]), .in1(E[12]), .out(multiplexer_18_out), .sel(W));
  Multiplexer multiplexer_19 (.in0(S[20]), .in1(E[20]), .out(multiplexer_19_out), .sel(W));
  Multiplexer multiplexer_20 (.in0(S[28]), .in1(E[28]), .out(multiplexer_20_out), .sel(W));
  D_Flip_Flop d_ff_17 (.D(multiplexer_17_out), .clk(CLK), .Q(S[4]));  // open: Qn, preset, reset
  D_Flip_Flop d_ff_18 (.D(multiplexer_18_out), .clk(CLK), .Q(S[12]));  // open: Qn, preset, reset
  D_Flip_Flop d_ff_19 (.D(multiplexer_19_out), .clk(CLK), .Q(S[20]));  // open: Qn, preset, reset
  D_Flip_Flop d_ff_20 (.D(multiplexer_20_out), .clk(CLK), .Q(S[28]));  // open: Qn, preset, reset
  D_Flip_Flop d_ff_21 (.D(multiplexer_21_out), .clk(CLK), .Q(S[5]));  // open: Qn, preset, reset
  Multiplexer multiplexer_21 (.in0(S[5]), .in1(E[5]), .out(multiplexer_21_out), .sel(W));
  D_Flip_Flop d_ff_22 (.D(multiplexer_22_out), .clk(CLK), .Q(S[13]));  // open: Qn, preset, reset
  Multiplexer multiplexer_22 (.in0(S[13]), .in1(E[13]), .out(multiplexer_22_out), .sel(W));
  D_Flip_Flop d_ff_23 (.D(multiplexer_23_out), .clk(CLK), .Q(S[21]));  // open: Qn, preset, reset
  Multiplexer multiplexer_23 (.in0(S[21]), .in1(E[21]), .out(multiplexer_23_out), .sel(W));
  D_Flip_Flop d_ff_24 (.D(multiplexer_24_out), .clk(CLK), .Q(S[29]));  // open: Qn, preset, reset
  Multiplexer multiplexer_24 (.in0(S[29]), .in1(E[29]), .out(multiplexer_24_out), .sel(W));
  Multiplexer multiplexer_25 (.in0(S[6]), .in1(E[6]), .out(multiplexer_25_out), .sel(W));
  Multiplexer multiplexer_26 (.in0(S[14]), .in1(E[14]), .out(multiplexer_26_out), .sel(W));
  Multiplexer multiplexer_27 (.in0(S[22]), .in1(E[22]), .out(multiplexer_27_out), .sel(W));
  Multiplexer multiplexer_28 (.in0(S[30]), .in1(E[30]), .out(multiplexer_28_out), .sel(W));
  D_Flip_Flop d_ff_25 (.D(multiplexer_25_out), .clk(CLK), .Q(S[6]));  // open: Qn, preset, reset
  D_Flip_Flop d_ff_26 (.D(multiplexer_26_out), .clk(CLK), .Q(S[14]));  // open: Qn, preset, reset
  D_Flip_Flop d_ff_27 (.D(multiplexer_27_out), .clk(CLK), .Q(S[22]));  // open: Qn, preset, reset
  D_Flip_Flop d_ff_28 (.D(multiplexer_28_out), .clk(CLK), .Q(S[30]));  // open: Qn, preset, reset
  D_Flip_Flop d_ff_29 (.D(multiplexer_29_out), .clk(CLK), .Q(S[7]));  // open: Qn, preset, reset
  Multiplexer multiplexer_29 (.in0(S[7]), .in1(E[7]), .out(multiplexer_29_out), .sel(W));
  D_Flip_Flop d_ff_30 (.D(multiplexer_30_out), .clk(CLK), .Q(S[15]));  // open: Qn, preset, reset
  Multiplexer multiplexer_30 (.in0(S[15]), .in1(E[15]), .out(multiplexer_30_out), .sel(W));
  D_Flip_Flop d_ff_31 (.D(multiplexer_31_out), .clk(CLK), .Q(S[23]));  // open: Qn, preset, reset
  Multiplexer multiplexer_31 (.in0(S[23]), .in1(E[23]), .out(multiplexer_31_out), .sel(W));
  D_Flip_Flop d_ff_32 (.D(multiplexer_32_out), .clk(CLK), .Q(S[31]));  // open: Qn, preset, reset
  Multiplexer multiplexer_32 (.in0(S[31]), .in1(E[31]), .out(multiplexer_32_out), .sel(W));

  // Other names for the same wires on the sheet: D0 = E[0]; D1 = E[1]; D2 = E[2]; D3 = E[3]; D4 = E[4]; D5 = E[5];
  //   D6 = E[6]; D7 = E[7]; D8 = E[8]; D9 = E[9]; D10 = E[10]; D11 = E[11]; D12 = E[12]; D13 = E[13]; D14 = E[14];
  //   D15 = E[15]; D16 = E[16]; D17 = E[17]; D18 = E[18]; D19 = E[19]; D20 = E[20]; D21 = E[21]; D22 = E[22];
  //   D23 = E[23]; D24 = E[24]; D25 = E[25]; D26 = E[26]; D27 = E[27]; D28 = E[28]; D29 = E[29]; D30 = E[30];
  //   D31 = E[31]

  // Notes on the sheet:
  //   Dados (entrada)
  //   CLK
  //   W0 (enable)
  //   Dados (saida)
endmodule

module ULA (
  input  [31:0] A,
  input  [31:0] B,
  input  [3:0] ALUop,
  output [31:0] C,
  output Zero
);

  wire [31:0] adder_1_out, adder_2_out, and_1_out, not_1_out, or_1_out, shifter_1_out;

  assign not_1_out = ~B;  // NOT_Gate not_1, 32 bits wide
  assign and_1_out = A & B;  // AND_Gate and_1, 32 bits wide
  assign or_1_out = A | A;  // OR_Gate or_1, 32 bits wide
  Adder #(.width(32)) adder_1 (.a(A), .b(B), .out(adder_1_out), .cin(1'b0));  // open: cout
  Adder #(.width(32)) adder_2 (.a(A), .b(not_1_out), .out(adder_2_out), .cin(1'b1));  // open: cout
  Shifter #(.width(32)) shifter_1 (.in(A), .\dist (B[4:0]), .out(shifter_1_out));
  Multiplexer #(.select(4), .width(32)) multiplexer_1 (
    .in0(and_1_out), .in1(or_1_out), .in2(adder_1_out), .in3(shifter_1_out), .in4({32{1'b0}}),
    .in5({32{1'b0}}), .in6(adder_2_out), .in7({32{1'b0}}), .in8({32{1'b0}}), .in9({32{1'b0}}),
    .in10({32{1'b0}}), .in11({32{1'b0}}), .in12({32{1'b0}}), .in13({32{1'b0}}), .in14({32{1'b0}}),
    .in15({32{1'b0}}), .out(C), .sel(ALUop));
  nor nor_1 (Zero, C[31], C[30], C[29], C[28], C[27], C[26], C[25], C[24], C[23], C[22], C[21], C[20], C[19], C[18], C[17], C[16], C[14], C[13], C[12], C[11], C[10], C[9], C[8], C[7], C[6], C[5], C[4], C[3], C[2], C[1], C[0], C[15]);

  // Notes on the sheet:
  //   And
  //   Or
  //   Add
  //   Sub
  //   Slli
endmodule

module extZero (
  input  [15:0] entrada,
  output [31:0] Saida
);


  assign Saida = {{16{1'b0}}, entrada};
endmodule

module extSinal (
  input  [23:0] entrada,
  output [31:0] Saida
);


  assign Saida = {{9{entrada[23]}}, entrada[22:0]};
endmodule

module PC_24_bits (
  input  [31:0] E,
  input  CLK,
  input  W,
  output [23:0] S
);

  wire multiplexer_1_out, multiplexer_2_out, multiplexer_3_out, multiplexer_4_out, multiplexer_5_out,
       multiplexer_6_out, multiplexer_7_out, multiplexer_8_out, multiplexer_9_out, multiplexer_10_out,
       multiplexer_11_out, multiplexer_12_out, multiplexer_13_out, multiplexer_14_out, multiplexer_15_out,
       multiplexer_16_out, multiplexer_17_out, multiplexer_18_out, multiplexer_19_out, multiplexer_20_out,
       multiplexer_21_out, multiplexer_22_out, multiplexer_23_out, multiplexer_24_out, multiplexer_25_out,
       multiplexer_26_out, multiplexer_27_out, multiplexer_28_out, multiplexer_29_out, multiplexer_30_out,
       multiplexer_31_out, multiplexer_32_out, S24, S25, S26, S27, S28, S29, S30, S31;

  D_Flip_Flop d_ff_1 (.D(multiplexer_1_out), .clk(CLK), .Q(S[0]));  // open: Qn, preset, reset
  Multiplexer multiplexer_1 (.in0(S[0]), .in1(E[0]), .out(multiplexer_1_out), .sel(W));
  D_Flip_Flop d_ff_2 (.D(multiplexer_2_out), .clk(CLK), .Q(S[8]));  // open: Qn, preset, reset
  Multiplexer multiplexer_2 (.in0(S[8]), .in1(E[8]), .out(multiplexer_2_out), .sel(W));
  D_Flip_Flop d_ff_3 (.D(multiplexer_3_out), .clk(CLK), .Q(S[16]));  // open: Qn, preset, reset
  Multiplexer multiplexer_3 (.in0(S[16]), .in1(E[16]), .out(multiplexer_3_out), .sel(W));
  D_Flip_Flop d_ff_4 (.D(multiplexer_4_out), .clk(CLK), .Q(S24));  // open: Qn, preset, reset
  Multiplexer multiplexer_4 (.in0(S24), .in1(E[24]), .out(multiplexer_4_out), .sel(W));
  Multiplexer multiplexer_5 (.in0(S[1]), .in1(E[1]), .out(multiplexer_5_out), .sel(W));
  Multiplexer multiplexer_6 (.in0(S[9]), .in1(E[9]), .out(multiplexer_6_out), .sel(W));
  Multiplexer multiplexer_7 (.in0(S[17]), .in1(E[17]), .out(multiplexer_7_out), .sel(W));
  Multiplexer multiplexer_8 (.in0(S25), .in1(E[25]), .out(multiplexer_8_out), .sel(W));
  D_Flip_Flop d_ff_5 (.D(multiplexer_5_out), .clk(CLK), .Q(S[1]));  // open: Qn, preset, reset
  D_Flip_Flop d_ff_6 (.D(multiplexer_6_out), .clk(CLK), .Q(S[9]));  // open: Qn, preset, reset
  D_Flip_Flop d_ff_7 (.D(multiplexer_7_out), .clk(CLK), .Q(S[17]));  // open: Qn, preset, reset
  D_Flip_Flop d_ff_8 (.D(multiplexer_8_out), .clk(CLK), .Q(S25));  // open: Qn, preset, reset
  Multiplexer multiplexer_9 (.in0(S[2]), .in1(E[2]), .out(multiplexer_9_out), .sel(W));
  Multiplexer multiplexer_10 (.in0(S[10]), .in1(E[10]), .out(multiplexer_10_out), .sel(W));
  Multiplexer multiplexer_11 (.in0(S[18]), .in1(E[18]), .out(multiplexer_11_out), .sel(W));
  Multiplexer multiplexer_12 (.in0(S26), .in1(E[26]), .out(multiplexer_12_out), .sel(W));
  D_Flip_Flop d_ff_9 (.D(multiplexer_9_out), .clk(CLK), .Q(S[2]));  // open: Qn, preset, reset
  D_Flip_Flop d_ff_10 (.D(multiplexer_10_out), .clk(CLK), .Q(S[10]));  // open: Qn, preset, reset
  D_Flip_Flop d_ff_11 (.D(multiplexer_11_out), .clk(CLK), .Q(S[18]));  // open: Qn, preset, reset
  D_Flip_Flop d_ff_12 (.D(multiplexer_12_out), .clk(CLK), .Q(S26));  // open: Qn, preset, reset
  D_Flip_Flop d_ff_13 (.D(multiplexer_13_out), .clk(CLK), .Q(S[3]));  // open: Qn, preset, reset
  Multiplexer multiplexer_13 (.in0(S[3]), .in1(E[3]), .out(multiplexer_13_out), .sel(W));
  D_Flip_Flop d_ff_14 (.D(multiplexer_14_out), .clk(CLK), .Q(S[11]));  // open: Qn, preset, reset
  Multiplexer multiplexer_14 (.in0(S[11]), .in1(E[11]), .out(multiplexer_14_out), .sel(W));
  D_Flip_Flop d_ff_15 (.D(multiplexer_15_out), .clk(CLK), .Q(S[19]));  // open: Qn, preset, reset
  Multiplexer multiplexer_15 (.in0(S[19]), .in1(E[19]), .out(multiplexer_15_out), .sel(W));
  D_Flip_Flop d_ff_16 (.D(multiplexer_16_out), .clk(CLK), .Q(S27));  // open: Qn, preset, reset
  Multiplexer multiplexer_16 (.in0(S27), .in1(E[27]), .out(multiplexer_16_out), .sel(W));
  Multiplexer multiplexer_17 (.in0(S[4]), .in1(E[4]), .out(multiplexer_17_out), .sel(W));
  Multiplexer multiplexer_18 (.in0(S[12]), .in1(E[12]), .out(multiplexer_18_out), .sel(W));
  Multiplexer multiplexer_19 (.in0(S[20]), .in1(E[20]), .out(multiplexer_19_out), .sel(W));
  Multiplexer multiplexer_20 (.in0(S28), .in1(E[28]), .out(multiplexer_20_out), .sel(W));
  D_Flip_Flop d_ff_17 (.D(multiplexer_17_out), .clk(CLK), .Q(S[4]));  // open: Qn, preset, reset
  D_Flip_Flop d_ff_18 (.D(multiplexer_18_out), .clk(CLK), .Q(S[12]));  // open: Qn, preset, reset
  D_Flip_Flop d_ff_19 (.D(multiplexer_19_out), .clk(CLK), .Q(S[20]));  // open: Qn, preset, reset
  D_Flip_Flop d_ff_20 (.D(multiplexer_20_out), .clk(CLK), .Q(S28));  // open: Qn, preset, reset
  D_Flip_Flop d_ff_21 (.D(multiplexer_21_out), .clk(CLK), .Q(S[5]));  // open: Qn, preset, reset
  Multiplexer multiplexer_21 (.in0(S[5]), .in1(E[5]), .out(multiplexer_21_out), .sel(W));
  D_Flip_Flop d_ff_22 (.D(multiplexer_22_out), .clk(CLK), .Q(S[13]));  // open: Qn, preset, reset
  Multiplexer multiplexer_22 (.in0(S[13]), .in1(E[13]), .out(multiplexer_22_out), .sel(W));
  D_Flip_Flop d_ff_23 (.D(multiplexer_23_out), .clk(CLK), .Q(S[21]));  // open: Qn, preset, reset
  Multiplexer multiplexer_23 (.in0(S[21]), .in1(E[21]), .out(multiplexer_23_out), .sel(W));
  D_Flip_Flop d_ff_24 (.D(multiplexer_24_out), .clk(CLK), .Q(S29));  // open: Qn, preset, reset
  Multiplexer multiplexer_24 (.in0(S29), .in1(E[29]), .out(multiplexer_24_out), .sel(W));
  Multiplexer multiplexer_25 (.in0(S[6]), .in1(E[6]), .out(multiplexer_25_out), .sel(W));
  Multiplexer multiplexer_26 (.in0(S[14]), .in1(E[14]), .out(multiplexer_26_out), .sel(W));
  Multiplexer multiplexer_27 (.in0(S[22]), .in1(E[22]), .out(multiplexer_27_out), .sel(W));
  Multiplexer multiplexer_28 (.in0(S30), .in1(E[30]), .out(multiplexer_28_out), .sel(W));
  D_Flip_Flop d_ff_25 (.D(multiplexer_25_out), .clk(CLK), .Q(S[6]));  // open: Qn, preset, reset
  D_Flip_Flop d_ff_26 (.D(multiplexer_26_out), .clk(CLK), .Q(S[14]));  // open: Qn, preset, reset
  D_Flip_Flop d_ff_27 (.D(multiplexer_27_out), .clk(CLK), .Q(S[22]));  // open: Qn, preset, reset
  D_Flip_Flop d_ff_28 (.D(multiplexer_28_out), .clk(CLK), .Q(S30));  // open: Qn, preset, reset
  D_Flip_Flop d_ff_29 (.D(multiplexer_29_out), .clk(CLK), .Q(S[7]));  // open: Qn, preset, reset
  Multiplexer multiplexer_29 (.in0(S[7]), .in1(E[7]), .out(multiplexer_29_out), .sel(W));
  D_Flip_Flop d_ff_30 (.D(multiplexer_30_out), .clk(CLK), .Q(S[15]));  // open: Qn, preset, reset
  Multiplexer multiplexer_30 (.in0(S[15]), .in1(E[15]), .out(multiplexer_30_out), .sel(W));
  D_Flip_Flop d_ff_31 (.D(multiplexer_31_out), .clk(CLK), .Q(S[23]));  // open: Qn, preset, reset
  Multiplexer multiplexer_31 (.in0(S[23]), .in1(E[23]), .out(multiplexer_31_out), .sel(W));
  D_Flip_Flop d_ff_32 (.D(multiplexer_32_out), .clk(CLK), .Q(S31));  // open: Qn, preset, reset
  Multiplexer multiplexer_32 (.in0(S31), .in1(E[31]), .out(multiplexer_32_out), .sel(W));

  // Other names for the same wires on the sheet: D0 = E[0]; D1 = E[1]; D2 = E[2]; D3 = E[3]; D4 = E[4]; D5 = E[5];
  //   D6 = E[6]; D7 = E[7]; D8 = E[8]; D9 = E[9]; D10 = E[10]; D11 = E[11]; D12 = E[12]; D13 = E[13]; D14 = E[14];
  //   D15 = E[15]; D16 = E[16]; D17 = E[17]; D18 = E[18]; D19 = E[19]; D20 = E[20]; D21 = E[21]; D22 = E[22];
  //   D23 = E[23]; D24 = E[24]; D25 = E[25]; D26 = E[26]; D27 = E[27]; D28 = E[28]; D29 = E[29]; D30 = E[30];
  //   D31 = E[31]

  // Notes on the sheet:
  //   CLK
  //   W0 (enable)
  //   Dados (saida)
endmodule

module RB_32x32bits (
  input  [4:0] R_address_A,
  input  [4:0] R_address_B,
  input  [4:0] Write_address,
  input  [31:0] Write_data,
  input  Write_enable,
  input  Clock,
  output [31:0] Saida_A,
  output [31:0] Saida_B
);

  wire r0, r1, r2, r3, r4, r5, r6, r7, r8, r9, r10, r11, r12, r13, r14, r15, r16, r17, r18, r19, r20, r21,
       r22, r23, r24, r25, r26, r27, r28, r29, r30, r31;
  wire [31:0] s0, s1, s2, s3, s4, s5, s6, s7, s8, s9, s10, s11, s12, s13, s14, s15, s16, s17, s18, s19, s20,
       s21, s22, s23, s24, s25, s26, s27, s28, s29, s30, s31;

  Demultiplexer #(.select(5)) demultiplexer_1 (
    .out0(r0), .out1(r1), .out2(r2), .out3(r3), .out4(r4), .out5(r5), .out6(r6), .out7(r7), .out8(r8),
    .out9(r9), .out10(r10), .out11(r11), .out12(r12), .out13(r13), .out14(r14), .out15(r15), .out16(r16),
    .out17(r17), .out18(r18), .out19(r19), .out20(r20), .out21(r21), .out22(r22), .out23(r23), .out24(r24),
    .out25(r25), .out26(r26), .out27(r27), .out28(r28), .out29(r29), .out30(r30), .out31(r31),
    .in(Write_enable), .sel(Write_address));
  registrador_32bits registrador_32bits_1 (.E({32{1'b0}}), .CLK(Clock), .W(r0), .S(s0));
  registrador_32bits registrador_32bits_2 (.E(Write_data), .CLK(Clock), .W(r1), .S(s1));
  registrador_32bits registrador_32bits_3 (.E(Write_data), .CLK(Clock), .W(r2), .S(s2));
  registrador_32bits registrador_32bits_4 (.E(Write_data), .CLK(Clock), .W(r3), .S(s3));
  registrador_32bits registrador_32bits_5 (.E(Write_data), .CLK(Clock), .W(r4), .S(s4));
  registrador_32bits registrador_32bits_6 (.E(Write_data), .CLK(Clock), .W(r5), .S(s5));
  registrador_32bits registrador_32bits_7 (.E(Write_data), .CLK(Clock), .W(r6), .S(s6));
  registrador_32bits registrador_32bits_8 (.E(Write_data), .CLK(Clock), .W(r7), .S(s7));
  registrador_32bits registrador_32bits_9 (.E(Write_data), .CLK(Clock), .W(r8), .S(s8));
  registrador_32bits registrador_32bits_10 (.E(Write_data), .CLK(Clock), .W(r9), .S(s9));
  registrador_32bits registrador_32bits_11 (.E(Write_data), .CLK(Clock), .W(r10), .S(s10));
  registrador_32bits registrador_32bits_12 (.E(Write_data), .CLK(Clock), .W(r11), .S(s11));
  registrador_32bits registrador_32bits_13 (.E(Write_data), .CLK(Clock), .W(r12), .S(s12));
  registrador_32bits registrador_32bits_14 (.E(Write_data), .CLK(Clock), .W(r13), .S(s13));
  registrador_32bits registrador_32bits_15 (.E(Write_data), .CLK(Clock), .W(r14), .S(s14));
  registrador_32bits registrador_32bits_16 (.E(Write_data), .CLK(Clock), .W(r15), .S(s15));
  registrador_32bits registrador_32bits_17 (.E(Write_data), .CLK(Clock), .W(r16), .S(s16));
  registrador_32bits registrador_32bits_18 (.E(Write_data), .CLK(Clock), .W(r17), .S(s17));
  registrador_32bits registrador_32bits_19 (.E(Write_data), .CLK(Clock), .W(r18), .S(s18));
  registrador_32bits registrador_32bits_20 (.E(Write_data), .CLK(Clock), .W(r19), .S(s19));
  registrador_32bits registrador_32bits_21 (.E(Write_data), .CLK(Clock), .W(r20), .S(s20));
  registrador_32bits registrador_32bits_22 (.E(Write_data), .CLK(Clock), .W(r21), .S(s21));
  registrador_32bits registrador_32bits_23 (.E(Write_data), .CLK(Clock), .W(r22), .S(s22));
  registrador_32bits registrador_32bits_24 (.E(Write_data), .CLK(Clock), .W(r23), .S(s23));
  registrador_32bits registrador_32bits_25 (.E(Write_data), .CLK(Clock), .W(r24), .S(s24));
  registrador_32bits registrador_32bits_26 (.E(Write_data), .CLK(Clock), .W(r25), .S(s25));
  registrador_32bits registrador_32bits_27 (.E(Write_data), .CLK(Clock), .W(r26), .S(s26));
  registrador_32bits registrador_32bits_28 (.E(Write_data), .CLK(Clock), .W(r27), .S(s27));
  registrador_32bits registrador_32bits_29 (.E(Write_data), .CLK(Clock), .W(r28), .S(s28));
  registrador_32bits registrador_32bits_30 (.E(Write_data), .CLK(Clock), .W(r29), .S(s29));
  registrador_32bits registrador_32bits_31 (.E(Write_data), .CLK(Clock), .W(r30), .S(s30));
  registrador_32bits registrador_32bits_32 (.E(Write_data), .CLK(Clock), .W(r31), .S(s31));
  Multiplexer #(.select(5), .width(32)) multiplexer_1 (
    .in0({32{1'b0}}), .in1(s1), .in2(s2), .in3(s3), .in4(s4), .in5(s5), .in6(s6), .in7(s7), .in8(s8),
    .in9(s9), .in10(s10), .in11(s11), .in12(s12), .in13(s13), .in14(s14), .in15(s15), .in16(s16), .in17(s17),
    .in18(s18), .in19(s19), .in20(s20), .in21(s21), .in22(s22), .in23(s23), .in24(s24), .in25(s25),
    .in26(s26), .in27(s27), .in28(s28), .in29(s29), .in30(s30), .in31(s31), .out(Saida_A), .sel(R_address_A));
  Multiplexer #(.select(5), .width(32)) multiplexer_2 (
    .in0({32{1'b0}}), .in1(s1), .in2(s2), .in3(s3), .in4(s4), .in5(s5), .in6(s6), .in7(s7), .in8(s8),
    .in9(s9), .in10(s10), .in11(s11), .in12(s12), .in13(s13), .in14(s14), .in15(s15), .in16(s16), .in17(s17),
    .in18(s18), .in19(s19), .in20(s20), .in21(s21), .in22(s22), .in23(s23), .in24(s24), .in25(s25),
    .in26(s26), .in27(s27), .in28(s28), .in29(s29), .in30(s30), .in31(s31), .out(Saida_B), .sel(R_address_B));

  // Other names for the same wires on the sheet: clk = Clock; Data[31:0] = Write_data
endmodule

module Imm_generator (
  input  [31:0] Instr,
  output [31:0] Saida
);

  wire [31:0] ext_sinal_12x32_1_saida, ext_sinal_12x32_2_saida, ext_sinal_12x32_3_saida;

  Ext_Sinal_12x32 ext_sinal_12x32_1 (.entrada(Instr[31:20]), .Saida(ext_sinal_12x32_1_saida));
  Ext_Sinal_12x32 ext_sinal_12x32_2 (.entrada({Instr[31:25], Instr[11:7]}), .Saida(ext_sinal_12x32_2_saida));
  Ext_Sinal_12x32 ext_sinal_12x32_3 (
    .entrada({Instr[31], Instr[7], Instr[30:25], Instr[11:8]}), .Saida(ext_sinal_12x32_3_saida));
  Multiplexer #(.select(3), .width(32)) multiplexer_1 (
    .in0(ext_sinal_12x32_1_saida), .in1(ext_sinal_12x32_1_saida), .in2(ext_sinal_12x32_2_saida),
    .in3({32{1'b0}}), .in4({32{1'b0}}), .in5({32{1'b0}}), .in6(ext_sinal_12x32_3_saida), .in7({32{1'b0}}),
    .out(Saida), .sel(Instr[6:4]));

  // Notes on the sheet:
  //   OP
  //   Type I
  //   Type S
  //   Type B
  //   Imm Gen = Usa o OP para selecionar o imm da instrução
endmodule

module Control (
  input  [6:0] OP,
  input  comparador,
  output [7:0] Control_s
);

  wire ALU_op_1, ALU_op_2, ALU_src_4, and_1_out, and_2_out, and_3_out, and_4_out, and_8_out, and_9_out,
       and_10_out, Branch_0, Mem_read_7, Mem_write_5, not_1_out, not_2_out, not_3_out, not_4_out, not_5_out,
       not_6_out, not_7_out, not_8_out, not_9_out, not_10_out, not_11_out, not_12_out, not_13_out,
       not_14_out, not_15_out, not_16_out, not_17_out, not_18_out, not_19_out, not_20_out, not_21_out,
       not_22_out, not_23_out, not_24_out, not_25_out, or_1_out, or_2_out, or_3_out, or_4_out, Reg_Write_3;

  not not_1 (not_1_out, OP[4]);
  not not_2 (not_2_out, OP[4]);
  not not_3 (not_3_out, OP[5]);
  not not_4 (not_4_out, OP[6]);
  not not_5 (not_5_out, OP[4]);
  not not_6 (not_6_out, OP[5]);
  not not_7 (not_7_out, OP[6]);
  not not_8 (not_8_out, OP[5]);
  not not_9 (not_9_out, OP[5]);
  not not_10 (not_10_out, OP[6]);
  not not_11 (not_11_out, OP[5]);
  not not_12 (not_12_out, OP[5]);
  not not_13 (not_13_out, OP[6]);
  and and_1 (and_1_out, not_1_out, OP[5], OP[6]);
  and and_2 (and_2_out, not_2_out, not_3_out, not_4_out);
  and and_3 (and_3_out, not_5_out, OP[5], OP[6]);
  and and_4 (and_4_out, OP[4], not_6_out, not_7_out);
  or or_1 (or_1_out, OP[4], not_8_out, OP[6]);
  or or_2 (or_2_out, OP[4], not_9_out, not_10_out);
  or or_3 (or_3_out, OP[4], not_11_out, OP[6]);
  or or_4 (or_4_out, OP[4], not_12_out, not_13_out);
  and and_5 (Branch_0, comparador, and_1_out);
  or or_5 (ALU_op_1, and_2_out, and_3_out, and_4_out);
  and and_6 (ALU_op_2, or_1_out, or_2_out);
  and and_7 (Reg_Write_3, or_3_out, or_4_out);
  not not_14 (not_14_out, OP[4]);
  not not_15 (not_15_out, OP[5]);
  not not_16 (not_16_out, OP[6]);
  not not_17 (not_17_out, OP[4]);
  not not_18 (not_18_out, OP[6]);
  not not_19 (not_19_out, OP[5]);
  not not_20 (not_20_out, OP[6]);
  not not_21 (not_21_out, OP[4]);
  not not_22 (not_22_out, OP[6]);
  not not_23 (not_23_out, OP[4]);
  not not_24 (not_24_out, OP[5]);
  not not_25 (not_25_out, OP[6]);
  and and_8 (and_8_out, not_14_out, not_15_out, not_16_out);
  and and_9 (and_9_out, not_17_out, OP[5], not_18_out);
  and and_10 (and_10_out, OP[4], not_19_out, not_20_out);
  and and_11 (Mem_write_5, not_21_out, OP[5], not_22_out);
  and and_12 (Mem_read_7, not_23_out, not_24_out, not_25_out);
  or or_6 (ALU_src_4, and_8_out, and_9_out, and_10_out);
  assign Control_s = {Branch_0, ALU_op_2, ALU_op_1, ALU_src_4, Mem_write_5, {2{Mem_read_7}}, Reg_Write_3} & {8{OP[0]}};  // AND_Gate and_13, 8 bits wide

  // Other names for the same wires on the sheet: Mem_to_reg_6 = Mem_read_7; OP_0 = OP[0]; OP_4 = OP[4]; OP_5 = OP[5];
  //   OP_6 = OP[6]
endmodule

module Redutor_32x8bits (
  input  [31:0] Entrada,
  output [7:0] Saida
);


  assign Saida = Entrada[7:0];
endmodule

module ALU_control (
  input  [1:0] ALU_Op,
  input  [31:0] Instruction,
  output [3:0] ALU_input
);

  wire and_1_out, and_2_out, and_3_out, and_4_out, not_1_out, not_2_out, not_3_out, not_4_out, not_5_out,
       not_6_out, not_7_out, not_8_out, not_9_out, not_10_out, not_11_out, not_12_out, not_13_out,
       not_14_out, not_15_out, not_16_out, not_17_out, not_18_out, not_19_out, or_1_out, or_2_out;

  not not_1 (not_1_out, Instruction[13]);
  not not_2 (not_2_out, Instruction[14]);
  not not_3 (not_3_out, Instruction[12]);
  not not_4 (not_4_out, Instruction[13]);
  not not_5 (not_5_out, Instruction[14]);
  not not_6 (not_6_out, ALU_Op[1]);
  not not_7 (not_7_out, Instruction[12]);
  not not_8 (not_8_out, Instruction[13]);
  not not_9 (not_9_out, Instruction[14]);
  not not_10 (not_10_out, ALU_Op[1]);
  not not_11 (not_11_out, Instruction[12]);
  not not_12 (not_12_out, Instruction[13]);
  not not_13 (not_13_out, Instruction[14]);
  not not_14 (not_14_out, ALU_Op[1]);
  not not_15 (not_15_out, Instruction[12]);
  not not_16 (not_16_out, Instruction[13]);
  not not_17 (not_17_out, Instruction[14]);
  not not_18 (not_18_out, ALU_Op[0]);
  not not_19 (not_19_out, ALU_Op[0]);
  and and_1 (and_1_out, Instruction[12], not_1_out, not_2_out, ALU_Op[0], ALU_Op[1]);
  and and_2 (and_2_out, not_3_out, Instruction[13], Instruction[14], not_18_out, ALU_Op[1]);
  or or_1 (or_1_out, Instruction[12], not_4_out, not_5_out, ALU_Op[0], not_6_out);
  or or_2 (or_2_out, not_7_out, not_8_out, not_9_out, ALU_Op[0], not_10_out);
  and and_3 (and_3_out, not_11_out, not_12_out, not_13_out, ALU_Op[0], not_14_out);
  and and_4 (and_4_out, not_15_out, not_16_out, not_17_out, not_19_out, ALU_Op[1], Instruction[30]);
  or or_3 (ALU_input[0], and_1_out, and_2_out);
  and and_5 (ALU_input[1], or_1_out, or_2_out);
  or or_4 (ALU_input[2], and_3_out, and_4_out);

  assign ALU_input[3] = 1'b0;

  // Other names for the same wires on the sheet: C0 = ALU_input[0]; C1 = ALU_input[1]; C2 = ALU_input[2];
  //   OP_0 = ALU_Op[0]; OP_1 = ALU_Op[1]; B0 = Instruction[12]; Funct3[2:0] = Instruction[14:12];
  //   B1 = Instruction[13]; B2 = Instruction[14]; A0 = Instruction[25]; Funct7[6:0] = Instruction[31:25];
  //   A1 = Instruction[26]; A2 = Instruction[27]; A3 = Instruction[28]; A4 = Instruction[29]; A5 = Instruction[30];
  //   A6 = Instruction[31]
endmodule

module Ext_Sinal_12x32 (
  input  [11:0] entrada,
  output [31:0] Saida
);


  assign Saida = {{21{entrada[11]}}, entrada[10:0]};
endmodule

module IF_ID (
  input  W_enable,
  input  Flush,
  input  [31:0] PC,
  input  [31:0] Instr,
  input  CLK,
  output [31:0] PC_saida,
  output [31:0] Instr_saida
);

  Register #(.width(32)) register_1 (.D(PC), .en(W_enable), .clk(CLK), .Q(PC_saida), .clr(Flush));
  Register #(.width(32)) register_2 (.D(Instr), .en(W_enable), .clk(CLK), .Q(Instr_saida), .clr(Flush));

  // Notes on the sheet:
  //   66 bits
endmodule

module ID_EX (
  input  RegWrite,
  input  Mem_to_Reg,
  input  Mem_read,
  input  Mem_write,
  input  Zero,
  input  ALUsrc,
  input  [1:0] ALUop,
  input  W_enable,
  input  Flush,
  input  [31:0] PC,
  input  [31:0] ra,
  input  [31:0] rb,
  input  [4:0] rc_addr,
  input  [31:0] Imm,
  input  [31:0] Instr,
  input  CLK,
  input  Branch,
  input  [4:0] ID_EX_rs1,
  input  [4:0] ID_EX_rs2,
  output RegWrite_s,
  output Mem_to_Reg_s,
  output Mem_read_s,
  output Mem_write_s,
  output Zero_s,
  output ALUsrc_s,
  output [1:0] ALUop_s,
  output [31:0] PC_saida,
  output [31:0] ra_saida,
  output [31:0] rb_saida,
  output [31:0] Imm_saida,
  output [31:0] Instr_saida,
  output [4:0] rc_addr_saida,
  output Branch_s,
  output [4:0] ID_EX_rs1_s,
  output [4:0] ID_EX_rs2_s
);

  Register #(.width(1)) register_1 (.D(Mem_read), .en(W_enable), .clk(CLK), .Q(Mem_read_s), .clr(Flush));
  Register #(.width(1)) register_2 (.D(Mem_write), .en(W_enable), .clk(CLK), .Q(Mem_write_s), .clr(Flush));
  Register #(.width(1)) register_3 (.D(Zero), .en(W_enable), .clk(CLK), .Q(Zero_s), .clr(Flush));
  Register #(.width(1)) register_4 (.D(ALUsrc), .en(W_enable), .clk(CLK), .Q(ALUsrc_s), .clr(Flush));
  Register #(.width(2)) register_5 (.D(ALUop), .en(W_enable), .clk(CLK), .Q(ALUop_s), .clr(Flush));
  Register #(.width(1)) register_6 (.D(RegWrite), .en(W_enable), .clk(CLK), .Q(RegWrite_s), .clr(Flush));
  Register #(.width(1)) register_7 (.D(Mem_to_Reg), .en(W_enable), .clk(CLK), .Q(Mem_to_Reg_s), .clr(Flush));
  Register #(.width(32)) register_8 (.D(PC), .en(W_enable), .clk(CLK), .Q(PC_saida));  // open: clr
  Register #(.width(32)) register_9 (.D(ra), .en(W_enable), .clk(CLK), .Q(ra_saida));  // open: clr
  Register #(.width(32)) register_10 (.D(rb), .en(W_enable), .clk(CLK), .Q(rb_saida));  // open: clr
  Register #(.width(5)) register_11 (.D(rc_addr), .en(W_enable), .clk(CLK), .Q(rc_addr_saida));  // open: clr
  Register #(.width(32)) register_12 (.D(Imm), .en(W_enable), .clk(CLK), .Q(Imm_saida), .clr(Flush));
  Register #(.width(32)) register_13 (.D(Instr), .en(W_enable), .clk(CLK), .Q(Instr_saida), .clr(Flush));
  Register #(.width(5)) register_14 (.D(ID_EX_rs1), .en(W_enable), .clk(CLK), .Q(ID_EX_rs1_s), .clr(Flush));
  Register #(.width(5)) register_15 (.D(ID_EX_rs2), .en(W_enable), .clk(CLK), .Q(ID_EX_rs2_s), .clr(Flush));
  Register #(.width(1)) register_16 (.D(Branch), .en(W_enable), .clk(CLK), .Q(Branch_s), .clr(Flush));

  // Other names for the same wires on the sheet: rc_addr_t[4:0] = rc_addr_saida

  // Notes on the sheet:
  //   Controle de Hazard
  //   EX- Sinais de controle do Pipeline ID/EX
  //   WB - Sinais de controle do Pipeline MEM/WB
  //   M- Sinais de controle do Pipeline EX/MEM
  //   Registradores do Pipeline
  //   se (ID/EX.RegistradorRS == EX/MEM.RegistradorRD) então Entrada1ALU = EX.MEM/DadoRD
endmodule

module EX_MEM (
  input  RegWrite,
  input  Mem_to_Reg,
  input  Mem_read,
  input  Mem_write,
  input  W_enable,
  input  Flush,
  input  [31:0] PC,
  input  [31:0] ALU_result,
  input  zero,
  input  [31:0] rb,
  input  [4:0] rc_addr,
  input  CLK,
  input  Branch,
  input  [4:0] EX_MEM_rd,
  input  [4:0] EXMEMrs2,
  output RegWrite_s,
  output Mem_to_Reg_s,
  output Mem_read_s,
  output Mem_write_s,
  output [31:0] PC_salto,
  output [31:0] ALU_result_s,
  output zero_saida,
  output [31:0] rb_saida,
  output [4:0] rc_addr_saida,
  output Branch_s,
  output [4:0] EX_MEM_rd_s,
  output [4:0] EX_MEM_rs2
);

  Register #(.width(1)) register_1 (.D(Mem_read), .en(W_enable), .clk(CLK), .Q(Mem_read_s), .clr(Flush));
  Register #(.width(1)) register_2 (.D(Mem_write), .en(W_enable), .clk(CLK), .Q(Mem_write_s), .clr(Flush));
  Register #(.width(1)) register_3 (.D(RegWrite), .en(W_enable), .clk(CLK), .Q(RegWrite_s), .clr(Flush));
  Register #(.width(1)) register_4 (.D(Mem_to_Reg), .en(W_enable), .clk(CLK), .Q(Mem_to_Reg_s), .clr(Flush));
  Register #(.width(32)) register_5 (.D(PC), .en(W_enable), .clk(CLK), .Q(PC_salto), .clr(Flush));
  Register #(.width(32)) register_6 (.D(ALU_result), .en(W_enable), .clk(CLK), .Q(ALU_result_s), .clr(Flush));
  Register #(.width(1)) register_7 (.D(zero), .en(W_enable), .clk(CLK), .Q(zero_saida), .clr(Flush));
  Register #(.width(32)) register_8 (.D(rb), .en(W_enable), .clk(CLK), .Q(rb_saida));  // open: clr
  Register #(.width(5)) register_9 (.D(rc_addr), .en(W_enable), .clk(CLK), .Q(rc_addr_saida), .clr(Flush));
  Register #(.width(5)) register_10 (.D(EX_MEM_rd), .en(W_enable), .clk(CLK), .Q(EX_MEM_rd_s), .clr(Flush));
  Register #(.width(5)) register_11 (.D(EXMEMrs2), .en(W_enable), .clk(CLK), .Q(EX_MEM_rs2), .clr(Flush));
  Register #(.width(1)) register_12 (.D(Branch), .en(W_enable), .clk(CLK), .Q(Branch_s), .clr(Flush));

  // Notes on the sheet:
  //   Controle de Hazard
  //   WB - Sinais de controle do Pipeline MEM/WB
  //   M- Sinais de controle do Pipeline EX/MEM
  //   Registradores do Pipeline
  //   se (ID/EX.RegistradorRS == EX/MEM.RegistradorRD) então Entrada1ALU = EX.MEM/DadoRD
endmodule

module MEM_WB (
  input  RegWrite,
  input  Mem_to_Reg,
  input  Flush,
  input  W_enable,
  input  [31:0] Read_data,
  input  [31:0] ALU_result,
  input  [4:0] rc_addrs,
  input  CLK,
  input  [4:0] MEM_WB_rd,
  output RegWrite_s,
  output Mem_to_Reg_s,
  output [31:0] Read_data_s,
  output [31:0] ALU_result_s,
  output [4:0] rc_addrs_saida,
  output [4:0] MEM_WB_rd_s
);

  Register #(.width(1)) register_1 (.D(RegWrite), .en(W_enable), .clk(CLK), .Q(RegWrite_s), .clr(Flush));
  Register #(.width(1)) register_2 (.D(Mem_to_Reg), .en(W_enable), .clk(CLK), .Q(Mem_to_Reg_s), .clr(Flush));
  Register #(.width(32)) register_3 (.D(Read_data), .en(W_enable), .clk(CLK), .Q(Read_data_s), .clr(Flush));
  Register #(.width(32)) register_4 (.D(ALU_result), .en(W_enable), .clk(CLK), .Q(ALU_result_s), .clr(Flush));
  Register #(.width(5)) register_5 (.D(MEM_WB_rd), .en(W_enable), .clk(CLK), .Q(MEM_WB_rd_s), .clr(Flush));
  Register #(.width(5)) register_6 (.D(rc_addrs), .en(W_enable), .clk(CLK), .Q(rc_addrs_saida), .clr(Flush));

  // Notes on the sheet:
  //   Controle de Hazard
  //   WB - Sinais de controle do Pipeline MEM/WB
  //   Registradores do Pipeline
  //   se (ID/EX.RegistradorRS == EX/MEM.RegistradorRD) então Entrada1ALU = EX.MEM/DadoRD
endmodule

module Haz_Detection (
  input  [4:0] IF_ID_Rs2,
  input  [4:0] IF_ID_Rs1,
  input  [4:0] ID_EX_Rd,
  input  ID_EX_MEMRead,
  input  [6:0] OP,
  input  ID_EX_RegWrite,
  input  clk,
  output PipelineStall,
  output IF_ID_write,
  output PC_write
);

  wire and_1_out, and_2_out, and_3_out, and_4_out, and_5_out, comparator_1_eq, comparator_2_eq,
       comparator_3_eq, comparator_4_eq, comparator_5_eq, comparator_6_eq, or_1_out, or_2_out, or_3_out,
       or_4_out, or_5_out, register_1_q;

  Comparator #(.width(5)) comparator_1 (.a(ID_EX_Rd), .b(IF_ID_Rs1), .eq(comparator_1_eq));  // open: gt, lt
  Comparator #(.width(5)) comparator_2 (.a(ID_EX_Rd), .b(IF_ID_Rs2), .eq(comparator_2_eq));  // open: gt, lt
  and and_1 (and_1_out, OP[6], ID_EX_RegWrite);
  Comparator #(.width(5)) comparator_3 (.a(ID_EX_Rd), .b(IF_ID_Rs1), .eq(comparator_3_eq));  // open: gt, lt
  Comparator #(.width(5)) comparator_4 (.a(ID_EX_Rd), .b(IF_ID_Rs2), .eq(comparator_4_eq));  // open: gt, lt
  or or_1 (or_1_out, comparator_1_eq, comparator_2_eq);
  and and_2 (and_2_out, ID_EX_MEMRead, OP[6]);
  or or_2 (or_2_out, comparator_3_eq, comparator_4_eq);
  Comparator #(.width(5)) comparator_5 (.a(IF_ID_Rs1), .b(ID_EX_Rd), .eq(comparator_5_eq));  // open: gt, lt
  Comparator #(.width(5)) comparator_6 (.a(IF_ID_Rs2), .b(ID_EX_Rd), .eq(comparator_6_eq));  // open: gt, lt
  and and_3 (and_3_out, or_1_out, and_2_out);
  or or_3 (or_3_out, comparator_5_eq, comparator_6_eq);
  and and_4 (and_4_out, and_1_out, or_2_out);
  Register #(.width(1)) register_1 (.D(and_3_out), .en(1'b1), .clk(clk), .Q(register_1_q));  // open: clr
  and and_5 (and_5_out, or_3_out, ID_EX_MEMRead);
  or or_4 (or_4_out, and_4_out, or_5_out);
  or or_5 (or_5_out, register_1_q, and_3_out);
  or or_6 (PipelineStall, and_5_out, or_4_out);
  not not_1 (IF_ID_write, PipelineStall);

  assign PC_write = IF_ID_write;

  // Other names for the same wires on the sheet: OP_6 = OP[6]

  // Notes on the sheet:
  //   Lw seguido de branch
endmodule

module Fowarding_Unit (
  input  [4:0] EXMEMRs2,
  input  [4:0] ExMemRd,
  input  [4:0] IDEXRs1,
  input  [4:0] MemWbRd,
  input  [4:0] IDEXRt,
  input  EXMEMRegWrite,
  input  MEMWBRegWrite,
  input  EXMEMMemWrite,
  output [1:0] ForwardA,
  output [1:0] ForwardB,
  output ForwardingMEM
);

  wire and_1_out, and_2_out, comparator_1_eq, comparator_2_lt, comparator_3_eq, comparator_4_eq,
       comparator_5_gt, comparator_6_lt, comparator_7_eq, comparator_8_eq, comparator_9_gt, not_1_out,
       not_2_out;

  Comparator #(.width(5)) comparator_1 (.a(MemWbRd), .b(EXMEMRs2), .eq(comparator_1_eq));  // open: gt, lt
  Comparator #(.width(5)) comparator_2 (.a({5{1'b0}}), .b(ExMemRd), .lt(comparator_2_lt));  // open: gt, eq
  Comparator #(.width(5)) comparator_3 (.a(ExMemRd), .b(IDEXRs1), .eq(comparator_3_eq));  // open: gt, lt
  Comparator #(.width(5)) comparator_4 (.a(MemWbRd), .b(IDEXRs1), .eq(comparator_4_eq));  // open: gt, lt
  Comparator #(.width(5)) comparator_5 (.a(IDEXRs1), .b({5{1'b0}}), .gt(comparator_5_gt));  // open: eq, lt
  Comparator #(.width(5)) comparator_6 (.a({5{1'b0}}), .b(ExMemRd), .lt(comparator_6_lt));  // open: gt, eq
  Comparator #(.width(5)) comparator_7 (.a(ExMemRd), .b(IDEXRt), .eq(comparator_7_eq));  // open: gt, lt
  Comparator #(.width(5)) comparator_8 (.a(MemWbRd), .b(IDEXRt), .eq(comparator_8_eq));  // open: gt, lt
  Comparator #(.width(5)) comparator_9 (.a(IDEXRt), .b({5{1'b0}}), .gt(comparator_9_gt));  // open: eq, lt
  and and_1 (and_1_out, comparator_4_eq, comparator_5_gt, MEMWBRegWrite);
  and and_2 (and_2_out, comparator_8_eq, comparator_9_gt, MEMWBRegWrite);
  and and_3 (ForwardingMEM, EXMEMMemWrite, MEMWBRegWrite, comparator_1_eq);
  and and_4 (ForwardA[1], comparator_2_lt, comparator_3_eq, EXMEMRegWrite);
  and and_5 (ForwardB[1], comparator_6_lt, comparator_7_eq, EXMEMRegWrite);
  not not_1 (not_1_out, ForwardA[1]);
  not not_2 (not_2_out, ForwardB[1]);
  and and_6 (ForwardA[0], not_1_out, and_1_out);
  and and_7 (ForwardB[0], not_2_out, and_2_out);
endmodule

module Beq_Fowarding (
  input  [4:0] IF_ID_rs1,
  input  [4:0] IF_ID_rs2,
  input  [4:0] EX_MEM_rd,
  input  [4:0] MEM_WB_rd,
  input  MEM_WB_RegWrite,
  input  EX_MEM_RegWrite,
  output [1:0] ForwardA,
  output [1:0] ForwardB
);

  wire and_1_out, and_2_out, comparator_1_lt, comparator_2_eq, comparator_3_eq, comparator_4_gt,
       comparator_5_lt, comparator_6_eq, comparator_7_eq, comparator_8_gt, not_1_out, not_2_out;

  Comparator #(.width(5)) comparator_1 (.a({5{1'b0}}), .b(EX_MEM_rd), .lt(comparator_1_lt));  // open: gt, eq
  Comparator #(.width(5)) comparator_2 (.a(EX_MEM_rd), .b(IF_ID_rs1), .eq(comparator_2_eq));  // open: gt, lt
  Comparator #(.width(5)) comparator_3 (.a(MEM_WB_rd), .b(IF_ID_rs1), .eq(comparator_3_eq));  // open: gt, lt
  Comparator #(.width(5)) comparator_4 (.a(IF_ID_rs1), .b({5{1'b0}}), .gt(comparator_4_gt));  // open: eq, lt
  Comparator #(.width(5)) comparator_5 (.a({5{1'b0}}), .b(EX_MEM_rd), .lt(comparator_5_lt));  // open: gt, eq
  Comparator #(.width(5)) comparator_6 (.a(EX_MEM_rd), .b(IF_ID_rs2), .eq(comparator_6_eq));  // open: gt, lt
  Comparator #(.width(5)) comparator_7 (.a(MEM_WB_rd), .b(IF_ID_rs2), .eq(comparator_7_eq));  // open: gt, lt
  Comparator #(.width(5)) comparator_8 (.a(IF_ID_rs2), .b({5{1'b0}}), .gt(comparator_8_gt));  // open: eq, lt
  and and_1 (and_1_out, comparator_3_eq, comparator_4_gt, MEM_WB_RegWrite);
  and and_2 (and_2_out, comparator_7_eq, comparator_8_gt, MEM_WB_RegWrite);
  and and_3 (ForwardA[1], comparator_1_lt, comparator_2_eq, EX_MEM_RegWrite);
  not not_1 (not_1_out, ForwardA[1]);
  and and_4 (ForwardB[1], comparator_5_lt, comparator_6_eq, EX_MEM_RegWrite);
  not not_2 (not_2_out, ForwardB[1]);
  and and_5 (ForwardA[0], not_1_out, and_1_out);
  and and_6 (ForwardB[0], not_2_out, and_2_out);
endmodule
