// Logisim project CPU_Monociclo.circ as structural Verilog: 20 circuits, main circuit main
module main (
);

  wire and_1_out, control_1_branch, ula_1_zero, undriven, undriven_2, undriven_4, undriven_5, undriven_6;
  wire [3:0] undriven_3;
  wire [4:0] rom_1_data_2, rom_1_data_4, rom_1_data_5;
  wire [6:0] rom_1_data;
  wire [7:0] redutor_32x8bits_1_saida;
  wire [23:0] pc_24_bits_1_s;
  wire [31:0] extsinal_1_saida, full_adder_32bits_1_soma, full_adder_32bits_2_soma, imm_generator_1_saida,
       multiplexer_1_out, multiplexer_2_out, multiplexer_3_out, ram_1_dout, rb_32x32bits_1_saida_a,
       rb_32x32bits_1_saida_b, ula_1_c;
  wire [31:12] rom_1_data_3;

  PC_24_bits pc_24_bits_1 (.E(multiplexer_2_out), .S(pc_24_bits_1_s));  // open: CLK, W
  ROM #(.addrWidth(24), .dataWidth(32)) rom_1 (
    .addr(pc_24_bits_1_s),
    .data({rom_1_data_3[31:25], rom_1_data_5, rom_1_data_4, rom_1_data_3[14:12], rom_1_data_2, rom_1_data}));
  extSinal extsinal_1 (.entrada(pc_24_bits_1_s), .Saida(extsinal_1_saida));
  Full_Adder_32bits full_adder_32bits_1 (
    .A(extsinal_1_saida), .B(32'h4), .Soma(full_adder_32bits_1_soma));  // open: C_in, C_out, Zero
  Control control_1 (
    .OP(rom_1_data), .Branch(control_1_branch));  // open: MemRead, MemtoReg, MemWrite, ALUsrc, RegWrite, ALUop
  RB_32x32bits rb_32x32bits_1 (
    .R_address_A(rom_1_data_4), .R_address_B(rom_1_data_5), .Write_address(rom_1_data_2),
    .Write_data(multiplexer_3_out), .Write_enable(undriven), .Saida_A(rb_32x32bits_1_saida_a),
    .Saida_B(rb_32x32bits_1_saida_b));  // open: Clock
  Imm_generator imm_generator_1 (
    .Instr({rom_1_data_3[31:25], rom_1_data_5, rom_1_data_4, rom_1_data_3[14:12], rom_1_data_2, rom_1_data}),
    .Saida(imm_generator_1_saida));
  Multiplexer #(.width(32)) multiplexer_1 (
    .in0(rb_32x32bits_1_saida_b), .in1(imm_generator_1_saida), .out(multiplexer_1_out), .sel(undriven_2));
  Full_Adder_32bits full_adder_32bits_2 (
    .A(extsinal_1_saida), .B(imm_generator_1_saida), .Soma(full_adder_32bits_2_soma));  // open: C_in, C_out, Zero
  ULA ula_1 (.A(rb_32x32bits_1_saida_a), .B(multiplexer_1_out), .ALUop(undriven_3), .C(ula_1_c), .Zero(ula_1_zero));
  and and_1 (and_1_out, control_1_branch, ula_1_zero);
  Multiplexer #(.width(32)) multiplexer_2 (
    .in0(full_adder_32bits_1_soma), .in1(full_adder_32bits_2_soma), .out(multiplexer_2_out), .sel(and_1_out));
  Redutor_32x8bits redutor_32x8bits_1 (.Entrada(ula_1_c), .Saida(redutor_32x8bits_1_saida));
  RAM #(.dataWidth(32)) ram_1 (
    .addr(redutor_32x8bits_1_saida), .we(undriven_5), .oe(undriven_4), .din(rb_32x32bits_1_saida_b),
    .dout(ram_1_dout));  // open: clk
  Multiplexer #(.width(32)) multiplexer_3 (.in0(ram_1_dout), .in1(ula_1_c), .out(multiplexer_3_out), .sel(undriven_6));

  // Notes on the sheet:
  //   24
  //   Pular de 1 em 1
  //   32
  //   OP
  //   Ra
  //   Rb
  //   Rc
  //   Imm
  //   0-31
  //   RegWrite
  //   ALUsrc
  //   ALUop
  //   Branch
  //   Zero
  //   Zero
  //   W_enable
  //   R_enable
  //   MemtoReg
endmodule

module registrador_32bits (
  input  [31:0] E,
  input  CLK,
  input  W,
  output [31:0] S
);

  wire multiplexer_1_out, multiplexer_2_out, multiplexer_3_out, multiplexer_4_out, multiplexer_5_out,
       multiplexer_6_out, multiplexer_7_out, multiplexer_8_out, multiplexer_9_out, multiplexer_10_out,
       multiplexer_11_out, multiplexer_12_out, multiplexer_13_out, multiplexer_14_out, multiplexer_15_out,
       multiplexer_16_out, multiplexer_17_out, multiplexer_18_out, multiplexer_19_out, multiplexer_20_out,
       multiplexer_21_out, multiplexer_22_out, multiplexer_23_out, multiplexer_24_out, multiplexer_25_out,
       multiplexer_26_out, multiplexer_27_out, multiplexer_28_out, multiplexer_29_out, multiplexer_30_out,
       multiplexer_31_out, multiplexer_32_out;

  D_Flip_Flop d_ff_1 (.D(multiplexer_1_out), .clk(CLK), .Q(S[0]));  // open: Qn, preset, reset
  Multiplexer multiplexer_1 (.in0(S[0]), .in1(E[0]), .out(multiplexer_1_out), .sel(W));
  D_Flip_Flop d_ff_2 (.D(multiplexer_2_out), .clk(CLK), .Q(S[8]));  // open: Qn, preset, reset
  Multiplexer multiplexer_2 (.in0(S[8]), .in1(E[8]), .out(multiplexer_2_out), .sel(W));
  D_Flip_Flop d_ff_3 (.D(multiplexer_3_out), .clk(CLK), .Q(S[16]));  // open: Qn, preset, reset
  Multiplexer multiplexer_3 (.in0(S[16]), .in1(E[16]), .out(multiplexer_3_out), .sel(W));
  D_Flip_Flop d_ff_4 (.D(multiplexer_4_out), .clk(CLK), .Q(S[24]));  // open: Qn, preset, reset
  Multiplexer multiplexer_4 (.in0(S[24]), .in1(E[24]), .out(multiplexer_4_out), .sel(W));
  Multiplexer multiplexer_5 (.in0(S[1]), .in1(E[1]), .out(multiplexer_5_out), .sel(W));
  Multiplexer multiplexer_6 (.in0(S[9]), .in1(E[9]), .out(multiplexer_6_out), .sel(W));
  Multiplexer multiplexer_7 (.in0(S[17]), .in1(E[17]), .out(multiplexer_7_out), .sel(W));
  Multiplexer multiplexer_8 (.in0(S[25]), .in1(E[25]), .out(multiplexer_8_out), .sel(W));
  D_Flip_Flop d_ff_5 (.D(multiplexer_5_out), .clk(CLK), .Q(S[1]));  // open: Qn, preset, reset
  D_Flip_Flop d_ff_6 (.D(multiplexer_6_out), .clk(CLK), .Q(S[9]));  // open: Qn, preset, reset
  D_Flip_Flop d_ff_7 (.D(multiplexer_7_out), .clk(CLK), .Q(S[17]));  // open: Qn, preset, reset
  D_Flip_Flop d_ff_8 (.D(multiplexer_8_out), .clk(CLK), .Q(S[25]));  // open: Qn, preset, reset
  Multiplexer multiplexer_9 (.in0(S[2]), .in1(E[2]), .out(multiplexer_9_out), .sel(W));
  Multiplexer multiplexer_10 (.in0(S[10]), .in1(E[10]), .out(multiplexer_10_out), .sel(W));
  Multiplexer multiplexer_11 (.in0(S[18]), .in1(E[18]), .out(multiplexer_11_out), .sel(W));
  Multiplexer multiplexer_12 (.in0(S[26]), .in1(E[26]), .out(multiplexer_12_out), .sel(W));
  D_Flip_Flop d_ff_9 (.D(multiplexer_9_out), .clk(CLK), .Q(S[2]));  // open: Qn, preset, reset
  D_Flip_Flop d_ff_10 (.D(multiplexer_10_out), .clk(CLK), .Q(S[10]));  // open: Qn, preset, reset
  D_Flip_Flop d_ff_11 (.D(multiplexer_11_out), .clk(CLK), .Q(S[18]));  // open: Qn, preset, reset
  D_Flip_Flop d_ff_12 (.D(multiplexer_12_out), .clk(CLK), .Q(S[26]));  // open: Qn, preset, reset
  D_Flip_Flop d_ff_13 (.D(multiplexer_13_out), .clk(CLK), .Q(S[3]));  // open: Qn, preset, reset
  Multiplexer multiplexer_13 (.in0(S[3]), .in1(E[3]), .out(multiplexer_13_out), .sel(W));
  D_Flip_Flop d_ff_14 (.D(multiplexer_14_out), .clk(CLK), .Q(S[11]));  // open: Qn, preset, reset
  Multiplexer multiplexer_14 (.in0(S[11]), .in1(E[11]), .out(multiplexer_14_out), .sel(W));
  D_Flip_Flop d_ff_15 (.D(multiplexer_15_out), .clk(CLK), .Q(S[19]));  // open: Qn, preset, reset
  Multiplexer multiplexer_15 (.in0(S[19]), .in1(E[19]), .out(multiplexer_15_out), .sel(W));
  D_Flip_Flop d_ff_16 (.D(multiplexer_16_out), .clk(CLK), .Q(S[27]));  // open: Qn, preset, reset
  Multiplexer multiplexer_16 (.in0(S[27]), .in1(E[27]), .out(multiplexer_16_out), .sel(W));
  Multiplexer multiplexer_17 (.in0(S[4]), .in1(E[4]), .out(multiplexer_17_out), .sel(W));
  Multiplexer multiplexer_18 (.in0(S[12]), .in1(E[12]), .out(multiplexer_18_out), .sel(W));
  Multiplexer multiplexer_19 (.in0(S[20]), .in1(E[20]), .out(multiplexer_19_out), .sel(W));
  Multiplexer multiplexer_20 (.in0(S[28]), .in1(E[28]), .out(multiplexer_20_out), .sel(W));
  D_Flip_Flop d_ff_17 (.D(multiplexer_17_out), .clk(CLK), .Q(S[4]));  // open: Qn, preset, reset
  D_Flip_Flop d_ff_18 (.D(multiplexer_18_out), .clk(CLK), .Q(S[12]));  // open: Qn, preset, reset
  D_Flip_Flop d_ff_19 (.D(multiplexer_19_out), .clk(CLK), .Q(S[20]));  // open: Qn, preset, reset
  D_Flip_Flop d_ff_20 (.D(multiplexer_20_out), .clk(CLK), .Q(S[28]));  // open: Qn, preset, reset
  D_Flip_Flop d_ff_21 (.D(multiplexer_21_out), .clk(CLK), .Q(S[5]));  // open: Qn, preset, reset
  Multiplexer multiplexer_21 (.in0(S[5]), .in1(E[5]), .out(multiplexer_21_out), .sel(W));
  D_Flip_Flop d_ff_22 (.D(multiplexer_22_out), .clk(CLK), .Q(S[13]));  // open: Qn, preset, reset
  Multiplexer multiplexer_22 (.in0(S[13]), .in1(E[13]), .out(multiplexer_22_out), .sel(W));
  D_Flip_Flop d_ff_23 (.D(multiplexer_23_out), .clk(CLK), .Q(S[21]));  // open: Qn, preset, reset
  Multiplexer multiplexer_23 (.in0(S[21]), .in1(E[21]), .out(multiplexer_23_out), .sel(W));
  D_Flip_Flop d_ff_24 (.D(multiplexer_24_out), .clk(CLK), .Q(S[29]));  // open: Qn, preset, reset
  Multiplexer multiplexer_24 (.in0(S[29]), .in1(E[29]), .out(multiplexer_24_out), .sel(W));
  Multiplexer multiplexer_25 (.in0(S[6]), .in1(E[6]), .out(multiplexer_25_out), .sel(W));
  Multiplexer multiplexer_26 (.in0(S[14]), .in1(E[14]), .out(multiplexer_26_out), .sel(W));
  Multiplexer multiplexer_27 (.in0(S[22]), .in1(E[22]), .out(multiplexer_27_out), .sel(W));
  Multiplexer multiplexer_28 (.in0(S[30]), .in1(E[30]), .out(multiplexer_28_out), .sel(W));
  D_Flip_Flop d_ff_25 (.D(multiplexer_25_out), .clk(CLK), .Q(S[6]));  // open: Qn, preset, reset
  D_Flip_Flop d_ff_26 (.D(multiplexer_26_out), .clk(CLK), .Q(S[14]));  // open: Qn, preset, reset
  D_Flip_Flop d_ff_27 (.D(multiplexer_27_out), .clk(CLK), .Q(S[22]));  // open: Qn, preset, reset
  D_Flip_Flop d_ff_28 (.D(multiplexer_28_out), .clk(CLK), .Q(S[30]));  // open: Qn, preset, reset
  D_Flip_Flop d_ff_29 (.D(multiplexer_29_out), .clk(CLK), .Q(S[7]));  // open: Qn, preset, reset
  Multiplexer multiplexer_29 (.in0(S[7]), .in1(E[7]), .out(multiplexer_29_out), .sel(W));
  D_Flip_Flop d_ff_30 (.D(multiplexer_30_out), .clk(CLK), .Q(S[15]));  // open: Qn, preset, reset
  Multiplexer multiplexer_30 (.in0(S[15]), .in1(E[15]), .out(multiplexer_30_out), .sel(W));
  D_Flip_Flop d_ff_31 (.D(multiplexer_31_out), .clk(CLK), .Q(S[23]));  // open: Qn, preset, reset
  Multiplexer multiplexer_31 (.in0(S[23]), .in1(E[23]), .out(multiplexer_31_out), .sel(W));
  D_Flip_Flop d_ff_32 (.D(multiplexer_32_out), .clk(CLK), .Q(S[31]));  // open: Qn, preset, reset
  Multiplexer multiplexer_32 (.in0(S[31]), .in1(E[31]), .out(multiplexer_32_out), .sel(W));

  // Other names for the same wires on the sheet: D0 = E[0]; D1 = E[1]; D2 = E[2]; D3 = E[3]; D4 = E[4]; D5 = E[5];
  //   D6 = E[6]; D7 = E[7]; D8 = E[8]; D9 = E[9]; D10 = E[10]; D11 = E[11]; D12 = E[12]; D13 = E[13]; D14 = E[14];
  //   D15 = E[15]; D16 = E[16]; D17 = E[17]; D18 = E[18]; D19 = E[19]; D20 = E[20]; D21 = E[21]; D22 = E[22];
  //   D23 = E[23]; D24 = E[24]; D25 = E[25]; D26 = E[26]; D27 = E[27]; D28 = E[28]; D29 = E[29]; D30 = E[30];
  //   D31 = E[31]

  // Notes on the sheet:
  //   Dados (entrada)
  //   CLK
  //   W0 (enable)
  //   Dados (saida)
endmodule

module ULA (
  input  [31:0] A,
  input  [31:0] B,
  input  [3:0] ALUop,
  output [31:0] C,
  output Zero
);

  wire [31:0] and_1_out, full_adder_32bits_1_soma, full_adder_32bits_2_soma, multiplier_1_out, not_1_out,
       or_1_out, xor_1_out;

  assign not_1_out = ~B;  // NOT_Gate not_1, 32 bits wide
  Multiplier #(.width(32)) multiplier_1 (.a(A), .b(B), .out(multiplier_1_out));  // open: cin, cout
  assign and_1_out = A & B;  // AND_Gate and_1, 32 bits wide
  assign or_1_out = A | B;  // OR_Gate or_1, 32 bits wide
  assign xor_1_out = A ^ B;  // XOR_Gate xor_1, 32 bits wide
  Full_Adder_32bits full_adder_32bits_1 (
    .A(A), .B(B), .C_in(1'b0), .Soma(full_adder_32bits_1_soma));  // open: C_out, Zero
  Full_Adder_32bits full_adder_32bits_2 (
    .A(A), .B(not_1_out), .C_in(1'b1), .Soma(full_adder_32bits_2_soma));  // open: C_out, Zero
  Multiplexer #(.select(4), .width(32)) multiplexer_1 (
    .in0(full_adder_32bits_1_soma), .in1(full_adder_32bits_2_soma), .in2(multiplier_1_out), .in3(and_1_out),
    .in4(or_1_out), .in5(xor_1_out), .out(C), .sel(ALUop));  // open: in6, in7, in8, in9, in10, in11, in12, in13, in14, in15
  nor nor_1 (Zero, C[31], C[30], C[29], C[28], C[27], C[26], C[25], C[24], C[23], C[22], C[21], C[20], C[19], C[18], C[17], C[16], C[14], C[13], C[12], C[11], C[10], C[9], C[8], C[7], C[6], C[5], C[4], C[3], C[2], C[1], C[0], C[15]);

  // Notes on the sheet:
  //   Somador
  //   Subtrator
  //   Multiplicador
  //   AND
  //   OR
  //   XOR
endmodule

module Full_Adder_32bits (
  input  [31:0] A,
  input  [31:0] B,
  input  C_in,
  output C_out,
  output [31:0] Soma,
  output Zero
);

  wire C_in8, C_in16, C_in24, full_adder_1_c_out, full_adder_2_c_out, full_adder_3_c_out, full_adder_4_c_out,
       full_adder_5_c_out, full_adder_6_c_out, full_adder_7_c_out, full_adder_8_c_out, full_adder_9_c_out,
       full_adder_10_c_out, full_adder_11_c_out, full_adder_12_c_out, full_adder_13_c_out,
       full_adder_14_c_out, full_adder_15_c_out, full_adder_16_c_out, full_adder_17_c_out,
       full_adder_18_c_out, full_adder_19_c_out, full_adder_20_c_out, full_adder_21_c_out,
       full_adder_22_c_out, full_adder_23_c_out, full_adder_24_c_out, full_adder_25_c_out,
       full_adder_26_c_out, full_adder_27_c_out, full_adder_28_c_out, full_adder_29_c_out,
       full_adder_30_c_out, full_adder_31_c_out;

  Full_Adder full_adder_1 (.A(A[0]), .B(B[0]), .C_in(C_in), .Soma(Soma[0]), .C_out(full_adder_1_c_out));
  Full_Adder full_adder_2 (.A(A[8]), .B(B[8]), .C_in(C_in8), .Soma(Soma[8]), .C_out(full_adder_2_c_out));
  Full_Adder full_adder_3 (.A(A[16]), .B(B[16]), .C_in(C_in16), .Soma(Soma[16]), .C_out(full_adder_3_c_out));
  Full_Adder full_adder_4 (.A(A[24]), .B(B[24]), .C_in(C_in24), .Soma(Soma[24]), .C_out(full_adder_4_c_out));
  Full_Adder full_adder_5 (.A(A[1]), .B(B[1]), .C_in(full_adder_1_c_out), .Soma(Soma[1]), .C_out(full_adder_5_c_out));
  Full_Adder full_adder_6 (.A(A[9]), .B(B[9]), .C_in(full_adder_2_c_out), .Soma(Soma[9]), .C_out(full_adder_6_c_out));
  Full_Adder full_adder_7 (
    .A(A[17]), .B(B[17]), .C_in(full_adder_3_c_out), .Soma(Soma[17]), .C_out(full_adder_7_c_out));
  Full_Adder full_adder_8 (
    .A(A[25]), .B(B[25]), .C_in(full_adder_4_c_out), .Soma(Soma[25]), .C_out(full_adder_8_c_out));
  nor nor_1 (Zero, Soma[31], Soma[30], Soma[29], Soma[28], Soma[27], Soma[26], Soma[25], Soma[24], Soma[23], Soma[22], Soma[21], Soma[20], Soma[19], Soma[18], Soma[17], Soma[16], Soma[14], Soma[13], Soma[12], Soma[11], Soma[10], Soma[9], Soma[8], Soma[7], Soma[6], Soma[5], Soma[4], Soma[3], Soma[2], Soma[1], Soma[0], Soma[15]);
  Full_Adder full_adder_9 (.A(A[2]), .B(B[2]), .C_in(full_adder_5_c_out), .Soma(Soma[2]), .C_out(full_adder_9_c_out));
  Full_Adder full_adder_10 (
    .A(A[10]), .B(B[10]), .C_in(full_adder_6_c_out), .Soma(Soma[10]), .C_out(full_adder_10_c_out));
  Full_Adder full_adder_11 (
    .A(A[18]), .B(B[18]), .C_in(full_adder_7_c_out), .Soma(Soma[18]), .C_out(full_adder_11_c_out));
  Full_Adder full_adder_12 (
    .A(A[26]), .B(B[26]), .C_in(full_adder_8_c_out), .Soma(Soma[26]), .C_out(full_adder_12_c_out));
  Full_Adder full_adder_13 (.A(A[3]), .B(B[3]), .C_in(full_adder_9_c_out), .Soma(Soma[3]), .C_out(full_adder_13_c_out));
  Full_Adder full_adder_14 (
    .A(A[11]), .B(B[11]), .C_in(full_adder_10_c_out), .Soma(Soma[11]), .C_out(full_adder_14_c_out));
  Full_Adder full_adder_15 (
    .A(A[19]), .B(B[19]), .C_in(full_adder_11_c_out), .Soma(Soma[19]), .C_out(full_adder_15_c_out));
  Full_Adder full_adder_16 (
    .A(A[27]), .B(B[27]), .C_in(full_adder_12_c_out), .Soma(Soma[27]), .C_out(full_adder_16_c_out));
  Full_Adder full_adder_17 (
    .A(A[4]), .B(B[4]), .C_in(full_adder_13_c_out), .Soma(Soma[4]), .C_out(full_adder_17_c_out));
  Full_Adder full_adder_18 (
    .A(A[12]), .B(B[12]), .C_in(full_adder_14_c_out), .Soma(Soma[12]), .C_out(full_adder_18_c_out));
  Full_Adder full_adder_19 (
    .A(A[20]), .B(B[20]), .C_in(full_adder_15_c_out), .Soma(Soma[20]), .C_out(full_adder_19_c_out));
  Full_Adder full_adder_20 (
    .A(A[28]), .B(B[28]), .C_in(full_adder_16_c_out), .Soma(Soma[28]), .C_out(full_adder_20_c_out));
  Full_Adder full_adder_21 (
    .A(A[5]), .B(B[5]), .C_in(full_adder_17_c_out), .Soma(Soma[5]), .C_out(full_adder_21_c_out));
  Full_Adder full_adder_22 (
    .A(A[13]), .B(B[13]), .C_in(full_adder_18_c_out), .Soma(Soma[13]), .C_out(full_adder_22_c_out));
  Full_Adder full_adder_23 (
    .A(A[21]), .B(B[21]), .C_in(full_adder_19_c_out), .Soma(Soma[21]), .C_out(full_adder_23_c_out));
  Full_Adder full_adder_24 (
    .A(A[29]), .B(B[29]), .C_in(full_adder_20_c_out), .Soma(Soma[29]), .C_out(full_adder_24_c_out));
  Full_Adder full_adder_25 (
    .A(A[6]), .B(B[6]), .C_in(full_adder_21_c_out), .Soma(Soma[6]), .C_out(full_adder_25_c_out));
  Full_Adder full_adder_26 (
    .A(A[14]), .B(B[14]), .C_in(full_adder_22_c_out), .Soma(Soma[14]), .C_out(full_adder_26_c_out));
  Full_Adder full_adder_27 (
    .A(A[22]), .B(B[22]), .C_in(full_adder_23_c_out), .Soma(Soma[22]), .C_out(full_adder_27_c_out));
  Full_Adder full_adder_28 (
    .A(A[30]), .B(B[30]), .C_in(full_adder_24_c_out), .Soma(Soma[30]), .C_out(full_adder_28_c_out));
  Full_Adder full_adder_29 (
    .A(A[7]), .B(B[7]), .C_in(full_adder_25_c_out), .Soma(Soma[7]), .C_out(full_adder_29_c_out));
  Full_Adder full_adder_30 (
    .A(A[15]), .B(B[15]), .C_in(full_adder_26_c_out), .Soma(Soma[15]), .C_out(full_adder_30_c_out));
  Full_Adder full_adder_31 (
    .A(A[23]), .B(B[23]), .C_in(full_adder_27_c_out), .Soma(Soma[23]), .C_out(full_adder_31_c_out));
  Full_Adder full_adder_32 (.A(A[31]), .B(B[31]), .C_in(full_adder_28_c_out), .Soma(Soma[31]), .C_out(C_out));

  // Other names for the same wires on the sheet: S0 = Soma[0]; S1 = Soma[1]; S2 = Soma[2]; S3 = Soma[3]; S4 = Soma[4];
  //   S5 = Soma[5]; S6 = Soma[6]; S7 = Soma[7]; S8 = Soma[8]; S9 = Soma[9]; S10 = Soma[10]; S11 = Soma[11];
  //   S12 = Soma[12]; S13 = Soma[13]; S14 = Soma[14]; S15 = Soma[15]; S16 = Soma[16]; S17 = Soma[17]; S18 = Soma[18];
  //   S19 = Soma[19]; S20 = Soma[20]; S21 = Soma[21]; S22 = Soma[22]; S23 = Soma[23]; S24 = Soma[24]; S25 = Soma[25];
  //   S26 = Soma[26]; S27 = Soma[27]; S28 = Soma[28]; S29 = Soma[29]; S30 = Soma[30]; S31 = Soma[31]
endmodule

module Full_Adder (
  input  A,
  input  B,
  input  C_in,
  output Soma,
  output C_out
);

  wire and_1_out, and_2_out, xor_1_out;

  xor xor_1 (xor_1_out, A, B);
  xor xor_2 (Soma, xor_1_out, C_in);
  and and_1 (and_1_out, xor_1_out, C_in);
  and and_2 (and_2_out, A, B);
  or or_1 (C_out, and_1_out, and_2_out);
endmodule

module extZero (
  input  [15:0] entrada,
  output [31:0] Saida
);


  assign Saida = {{16{1'b0}}, entrada};
endmodule

module extSinal (
  input  [23:0] entrada,
  output [31:0] Saida
);


  assign Saida = {{9{entrada[23]}}, entrada[22:0]};
endmodule

module Shifter_1bit (
  input  [31:0] Entrada,
  output [31:0] Saida
);


  assign Saida = {Entrada[30:0], 1'b0};

  // Other names for the same wires on the sheet: B31 = Entrada[31]; B0 = Entrada[0]; B1 = Entrada[1]; B2 = Entrada[2];
  //   B3 = Entrada[3]; B4 = Entrada[4]; B5 = Entrada[5]; B6 = Entrada[6]; B7 = Entrada[7]; B8 = Entrada[8];
  //   B9 = Entrada[9]; B10 = Entrada[10]; B11 = Entrada[11]; B12 = Entrada[12]; B13 = Entrada[13]; B14 = Entrada[14];
  //   B15 = Entrada[15]; B16 = Entrada[16]; B17 = Entrada[17]; B18 = Entrada[18]; B19 = Entrada[19];
  //   B20 = Entrada[20]; B21 = Entrada[21]; B22 = Entrada[22]; B23 = Entrada[23]; B24 = Entrada[24];
  //   B25 = Entrada[25]; B26 = Entrada[26]; B27 = Entrada[27]; B28 = Entrada[28]; B29 = Entrada[29];
  //   B30 = Entrada[30]
endmodule

module Shifter_2bit (
  input  [31:0] Entrada,
  output [31:0] Saida
);


  assign Saida = {Entrada[29:0], 2'b00};

  // Other names for the same wires on the sheet: B30 = Entrada[30]; B31 = Entrada[31]; B0 = Entrada[0];
  //   B1 = Entrada[1]; B2 = Entrada[2]; B3 = Entrada[3]; B4 = Entrada[4]; B5 = Entrada[5]; B6 = Entrada[6];
  //   B7 = Entrada[7]; B8 = Entrada[8]; B9 = Entrada[9]; B10 = Entrada[10]; B11 = Entrada[11]; B12 = Entrada[12];
  //   B13 = Entrada[13]; B14 = Entrada[14]; B15 = Entrada[15]; B16 = Entrada[16]; B17 = Entrada[17];
  //   B18 = Entrada[18]; B19 = Entrada[19]; B20 = Entrada[20]; B21 = Entrada[21]; B22 = Entrada[22];
  //   B23 = Entrada[23]; B24 = Entrada[24]; B25 = Entrada[25]; B26 = Entrada[26]; B27 = Entrada[27];
  //   B28 = Entrada[28]; B29 = Entrada[29]
endmodule

module Shifter_4bit (
  input  [31:0] Entrada,
  output [31:0] Saida
);


  assign Saida = {Entrada[27:0], 4'b0000};

  // Other names for the same wires on the sheet: B28 = Entrada[28]; B29 = Entrada[29]; B30 = Entrada[30];
  //   B31 = Entrada[31]; B0 = Entrada[0]; B1 = Entrada[1]; B2 = Entrada[2]; B3 = Entrada[3]; B4 = Entrada[4];
  //   B5 = Entrada[5]; B6 = Entrada[6]; B7 = Entrada[7]; B8 = Entrada[8]; B9 = Entrada[9]; B10 = Entrada[10];
  //   B11 = Entrada[11]; B12 = Entrada[12]; B13 = Entrada[13]; B14 = Entrada[14]; B15 = Entrada[15];
  //   B16 = Entrada[16]; B17 = Entrada[17]; B18 = Entrada[18]; B19 = Entrada[19]; B20 = Entrada[20];
  //   B21 = Entrada[21]; B22 = Entrada[22]; B23 = Entrada[23]; B24 = Entrada[24]; B25 = Entrada[25];
  //   B26 = Entrada[26]; B27 = Entrada[27]
endmodule

module Shifter_8bit (
  input  [31:0] Entrada,
  output [31:0] Saida
);


  assign Saida = {Entrada[23:0], {8{1'b0}}};

  // Other names for the same wires on the sheet: B24 = Entrada[24]; B25 = Entrada[25]; B26 = Entrada[26];
  //   B27 = Entrada[27]; B28 = Entrada[28]; B29 = Entrada[29]; B30 = Entrada[30]; B31 = Entrada[31]; B0 = Entrada[0];
  //   B1 = Entrada[1]; B2 = Entrada[2]; B3 = Entrada[3]; B4 = Entrada[4]; B5 = Entrada[5]; B6 = Entrada[6];
  //   B7 = Entrada[7]; B8 = Entrada[8]; B9 = Entrada[9]; B10 = Entrada[10]; B11 = Entrada[11]; B12 = Entrada[12];
  //   B13 = Entrada[13]; B14 = Entrada[14]; B15 = Entrada[15]; B16 = Entrada[16]; B17 = Entrada[17];
  //   B18 = Entrada[18]; B19 = Entrada[19]; B20 = Entrada[20]; B21 = Entrada[21]; B22 = Entrada[22];
  //   B23 = Entrada[23]
endmodule

module Shifter_16bits (
  input  [31:0] Entrada,
  output [31:0] Saida
);


  assign Saida = {Entrada[15:0], {16{1'b0}}};

  // Other names for the same wires on the sheet: B16 = Entrada[16]; B17 = Entrada[17]; B18 = Entrada[18];
  //   B19 = Entrada[19]; B20 = Entrada[20]; B21 = Entrada[21]; B22 = Entrada[22]; B23 = Entrada[23];
  //   B24 = Entrada[24]; B25 = Entrada[25]; B26 = Entrada[26]; B27 = Entrada[27]; B28 = Entrada[28];
  //   B29 = Entrada[29]; B30 = Entrada[30]; B31 = Entrada[31]; B0 = Entrada[0]; B1 = Entrada[1]; B2 = Entrada[2];
  //   B3 = Entrada[3]; B4 = Entrada[4]; B5 = Entrada[5]; B6 = Entrada[6]; B7 = Entrada[7]; B8 = Entrada[8];
  //   B9 = Entrada[9]; B10 = Entrada[10]; B11 = Entrada[11]; B12 = Entrada[12]; B13 = Entrada[13]; B14 = Entrada[14];
  //   B15 = Entrada[15]
endmodule

module PC_24_bits (
  input  [31:0] E,
  input  CLK,
  input  W,
  output [23:0] S
);

  wire multiplexer_1_out, multiplexer_2_out, multiplexer_3_out, multiplexer_4_out, multiplexer_5_out,
       multiplexer_6_out, multiplexer_7_out, multiplexer_8_out, multiplexer_9_out, multiplexer_10_out,
       multiplexer_11_out, multiplexer_12_out, multiplexer_13_out, multiplexer_14_out, multiplexer_15_out,
       multiplexer_16_out, multiplexer_17_out, multiplexer_18_out, multiplexer_19_out, multiplexer_20_out,
       multiplexer_21_out, multiplexer_22_out, multiplexer_23_out, multiplexer_24_out, multiplexer_25_out,
       multiplexer_26_out, multiplexer_27_out, multiplexer_28_out, multiplexer_29_out, multiplexer_30_out,
       multiplexer_31_out, multiplexer_32_out, S24, S25, S26, S27, S28, S29, S30, S31;

  D_Flip_Flop d_ff_1 (.D(multiplexer_1_out), .clk(CLK), .Q(S[0]));  // open: Qn, preset, reset
  Multiplexer multiplexer_1 (.in0(S[0]), .in1(E[0]), .out(multiplexer_1_out), .sel(W));
  D_Flip_Flop d_ff_2 (.D(multiplexer_2_out), .clk(CLK), .Q(S[8]));  // open: Qn, preset, reset
  Multiplexer multiplexer_2 (.in0(S[8]), .in1(E[8]), .out(multiplexer_2_out), .sel(W));
  D_Flip_Flop d_ff_3 (.D(multiplexer_3_out), .clk(CLK), .Q(S[16]));  // open: Qn, preset, reset
  Multiplexer multiplexer_3 (.in0(S[16]), .in1(E[16]), .out(multiplexer_3_out), .sel(W));
  D_Flip_Flop d_ff_4 (.D(multiplexer_4_out), .clk(CLK), .Q(S24));  // open: Qn, preset, reset
  Multiplexer multiplexer_4 (.in0(S24), .in1(E[24]), .out(multiplexer_4_out), .sel(W));
  Multiplexer multiplexer_5 (.in0(S[1]), .in1(E[1]), .out(multiplexer_5_out), .sel(W));
  Multiplexer multiplexer_6 (.in0(S[9]), .in1(E[9]), .out(multiplexer_6_out), .sel(W));
  Multiplexer multiplexer_7 (.in0(S[17]), .in1(E[17]), .out(multiplexer_7_out), .sel(W));
  Multiplexer multiplexer_8 (.in0(S25), .in1(E[25]), .out(multiplexer_8_out), .sel(W));
  D_Flip_Flop d_ff_5 (.D(multiplexer_5_out), .clk(CLK), .Q(S[1]));  // open: Qn, preset, reset
  D_Flip_Flop d_ff_6 (.D(multiplexer_6_out), .clk(CLK), .Q(S[9]));  // open: Qn, preset, reset
  D_Flip_Flop d_ff_7 (.D(multiplexer_7_out), .clk(CLK), .Q(S[17]));  // open: Qn, preset, reset
  D_Flip_Flop d_ff_8 (.D(multiplexer_8_out), .clk(CLK), .Q(S25));  // open: Qn, preset, reset
  Multiplexer multiplexer_9 (.in0(S[2]), .in1(E[2]), .out(multiplexer_9_out), .sel(W));
  Multiplexer multiplexer_10 (.in0(S[10]), .in1(E[10]), .out(multiplexer_10_out), .sel(W));
  Multiplexer multiplexer_11 (.in0(S[18]), .in1(E[18]), .out(multiplexer_11_out), .sel(W));
  Multiplexer multiplexer_12 (.in0(S26), .in1(E[26]), .out(multiplexer_12_out), .sel(W));
  D_Flip_Flop d_ff_9 (.D(multiplexer_9_out), .clk(CLK), .Q(S[2]));  // open: Qn, preset, reset
  D_Flip_Flop d_ff_10 (.D(multiplexer_10_out), .clk(CLK), .Q(S[10]));  // open: Qn, preset, reset
  D_Flip_Flop d_ff_11 (.D(multiplexer_11_out), .clk(CLK), .Q(S[18]));  // open: Qn, preset, reset
  D_Flip_Flop d_ff_12 (.D(multiplexer_12_out), .clk(CLK), .Q(S26));  // open: Qn, preset, reset
  D_Flip_Flop d_ff_13 (.D(multiplexer_13_out), .clk(CLK), .Q(S[3]));  // open: Qn, preset, reset
  Multiplexer multiplexer_13 (.in0(S[3]), .in1(E[3]), .out(multiplexer_13_out), .sel(W));
  D_Flip_Flop d_ff_14 (.D(multiplexer_14_out), .clk(CLK), .Q(S[11]));  // open: Qn, preset, reset
  Multiplexer multiplexer_14 (.in0(S[11]), .in1(E[11]), .out(multiplexer_14_out), .sel(W));
  D_Flip_Flop d_ff_15 (.D(multiplexer_15_out), .clk(CLK), .Q(S[19]));  // open: Qn, preset, reset
  Multiplexer multiplexer_15 (.in0(S[19]), .in1(E[19]), .out(multiplexer_15_out), .sel(W));
  D_Flip_Flop d_ff_16 (.D(multiplexer_16_out), .clk(CLK), .Q(S27));  // open: Qn, preset, reset
  Multiplexer multiplexer_16 (.in0(S27), .in1(E[27]), .out(multiplexer_16_out), .sel(W));
  Multiplexer multiplexer_17 (.in0(S[4]), .in1(E[4]), .out(multiplexer_17_out), .sel(W));
  Multiplexer multiplexer_18 (.in0(S[12]), .in1(E[12]), .out(multiplexer_18_out), .sel(W));
  Multiplexer multiplexer_19 (.in0(S[20]), .in1(E[20]), .out(multiplexer_19_out), .sel(W));
  Multiplexer multiplexer_20 (.in0(S28), .in1(E[28]), .out(multiplexer_20_out), .sel(W));
  D_Flip_Flop d_ff_17 (.D(multiplexer_17_out), .clk(CLK), .Q(S[4]));  // open: Qn, preset, reset
  D_Flip_Flop d_ff_18 (.D(multiplexer_18_out), .clk(CLK), .Q(S[12]));  // open: Qn, preset, reset
  D_Flip_Flop d_ff_19 (.D(multiplexer_19_out), .clk(CLK), .Q(S[20]));  // open: Qn, preset, reset
  D_Flip_Flop d_ff_20 (.D(multiplexer_20_out), .clk(CLK), .Q(S28));  // open: Qn, preset, reset
  D_Flip_Flop d_ff_21 (.D(multiplexer_21_out), .clk(CLK), .Q(S[5]));  // open: Qn, preset, reset
  Multiplexer multiplexer_21 (.in0(S[5]), .in1(E[5]), .out(multiplexer_21_out), .sel(W));
  D_Flip_Flop d_ff_22 (.D(multiplexer_22_out), .clk(CLK), .Q(S[13]));  // open: Qn, preset, reset
  Multiplexer multiplexer_22 (.in0(S[13]), .in1(E[13]), .out(multiplexer_22_out), .sel(W));
  D_Flip_Flop d_ff_23 (.D(multiplexer_23_out), .clk(CLK), .Q(S[21]));  // open: Qn, preset, reset
  Multiplexer multiplexer_23 (.in0(S[21]), .in1(E[21]), .out(multiplexer_23_out), .sel(W));
  D_Flip_Flop d_ff_24 (.D(multiplexer_24_out), .clk(CLK), .Q(S29));  // open: Qn, preset, reset
  Multiplexer multiplexer_24 (.in0(S29), .in1(E[29]), .out(multiplexer_24_out), .sel(W));
  Multiplexer multiplexer_25 (.in0(S[6]), .in1(E[6]), .out(multiplexer_25_out), .sel(W));
  Multiplexer multiplexer_26 (.in0(S[14]), .in1(E[14]), .out(multiplexer_26_out), .sel(W));
  Multiplexer multiplexer_27 (.in0(S[22]), .in1(E[22]), .out(multiplexer_27_out), .sel(W));
  Multiplexer multiplexer_28 (.in0(S30), .in1(E[30]), .out(multiplexer_28_out), .sel(W));
  D_Flip_Flop d_ff_25 (.D(multiplexer_25_out), .clk(CLK), .Q(S[6]));  // open: Qn, preset, reset
  D_Flip_Flop d_ff_26 (.D(multiplexer_26_out), .clk(CLK), .Q(S[14]));  // open: Qn, preset, reset
  D_Flip_Flop d_ff_27 (.D(multiplexer_27_out), .clk(CLK), .Q(S[22]));  // open: Qn, preset, reset
  D_Flip_Flop d_ff_28 (.D(multiplexer_28_out), .clk(CLK), .Q(S30));  // open: Qn, preset, reset
  D_Flip_Flop d_ff_29 (.D(multiplexer_29_out), .clk(CLK), .Q(S[7]));  // open: Qn, preset, reset
  Multiplexer multiplexer_29 (.in0(S[7]), .in1(E[7]), .out(multiplexer_29_out), .sel(W));
  D_Flip_Flop d_ff_30 (.D(multiplexer_30_out), .clk(CLK), .Q(S[15]));  // open: Qn, preset, reset
  Multiplexer multiplexer_30 (.in0(S[15]), .in1(E[15]), .out(multiplexer_30_out), .sel(W));
  D_Flip_Flop d_ff_31 (.D(multiplexer_31_out), .clk(CLK), .Q(S[23]));  // open: Qn, preset, reset
  Multiplexer multiplexer_31 (.in0(S[23]), .in1(E[23]), .out(multiplexer_31_out), .sel(W));
  D_Flip_Flop d_ff_32 (.D(multiplexer_32_out), .clk(CLK), .Q(S31));  // open: Qn, preset, reset
  Multiplexer multiplexer_32 (.in0(S31), .in1(E[31]), .out(multiplexer_32_out), .sel(W));

  // Other names for the same wires on the sheet: D0 = E[0]; D1 = E[1]; D2 = E[2]; D3 = E[3]; D4 = E[4]; D5 = E[5];
  //   D6 = E[6]; D7 = E[7]; D8 = E[8]; D9 = E[9]; D10 = E[10]; D11 = E[11]; D12 = E[12]; D13 = E[13]; D14 = E[14];
  //   D15 = E[15]; D16 = E[16]; D17 = E[17]; D18 = E[18]; D19 = E[19]; D20 = E[20]; D21 = E[21]; D22 = E[22];
  //   D23 = E[23]; D24 = E[24]; D25 = E[25]; D26 = E[26]; D27 = E[27]; D28 = E[28]; D29 = E[29]; D30 = E[30];
  //   D31 = E[31]

  // Notes on the sheet:
  //   CLK
  //   W0 (enable)
  //   Dados (saida)
endmodule

module RB_32x32bits (
  input  [4:0] R_address_A,
  input  [4:0] R_address_B,
  input  [4:0] Write_address,
  input  [31:0] Write_data,
  input  Write_enable,
  input  Clock,
  output [31:0] Saida_A,
  output [31:0] Saida_B
);

  wire r0, r1, r2, r3, r4, r5, r6, r7, r8, r9, r10, r11, r12, r13, r14, r15, r16, r17, r18, r19, r20, r21,
       r22, r23, r24, r25, r26, r27, r28, r29, r30, r31;
  wire [31:0] s0, s1, s2, s3, s4, s5, s6, s7, s8, s9, s10, s11, s12, s13, s14, s15, s16, s17, s18, s19, s20,
       s21, s22, s23, s24, s25, s26, s27, s28, s29, s30, s31;

  Demultiplexer #(.select(5)) demultiplexer_1 (
    .out0(r0), .out1(r1), .out2(r2), .out3(r3), .out4(r4), .out5(r5), .out6(r6), .out7(r7), .out8(r8),
    .out9(r9), .out10(r10), .out11(r11), .out12(r12), .out13(r13), .out14(r14), .out15(r15), .out16(r16),
    .out17(r17), .out18(r18), .out19(r19), .out20(r20), .out21(r21), .out22(r22), .out23(r23), .out24(r24),
    .out25(r25), .out26(r26), .out27(r27), .out28(r28), .out29(r29), .out30(r30), .out31(r31),
    .in(Write_enable), .sel(Write_address));
  registrador_32bits registrador_32bits_1 (.E({32{1'b0}}), .CLK(Clock), .W(r0), .S(s0));
  registrador_32bits registrador_32bits_2 (.E(Write_data), .CLK(Clock), .W(r1), .S(s1));
  registrador_32bits registrador_32bits_3 (.E(Write_data), .CLK(Clock), .W(r2), .S(s2));
  registrador_32bits registrador_32bits_4 (.E(Write_data), .CLK(Clock), .W(r3), .S(s3));
  registrador_32bits registrador_32bits_5 (.E(Write_data), .CLK(Clock), .W(r4), .S(s4));
  registrador_32bits registrador_32bits_6 (.E(Write_data), .CLK(Clock), .W(r5), .S(s5));
  registrador_32bits registrador_32bits_7 (.E(Write_data), .CLK(Clock), .W(r6), .S(s6));
  registrador_32bits registrador_32bits_8 (.E(Write_data), .CLK(Clock), .W(r7), .S(s7));
  registrador_32bits registrador_32bits_9 (.E(Write_data), .CLK(Clock), .W(r8), .S(s8));
  registrador_32bits registrador_32bits_10 (.E(Write_data), .CLK(Clock), .W(r9), .S(s9));
  registrador_32bits registrador_32bits_11 (.E(Write_data), .CLK(Clock), .W(r10), .S(s10));
  registrador_32bits registrador_32bits_12 (.E(Write_data), .CLK(Clock), .W(r11), .S(s11));
  registrador_32bits registrador_32bits_13 (.E(Write_data), .CLK(Clock), .W(r12), .S(s12));
  registrador_32bits registrador_32bits_14 (.E(Write_data), .CLK(Clock), .W(r13), .S(s13));
  registrador_32bits registrador_32bits_15 (.E(Write_data), .CLK(Clock), .W(r14), .S(s14));
  registrador_32bits registrador_32bits_16 (.E(Write_data), .CLK(Clock), .W(r15), .S(s15));
  registrador_32bits registrador_32bits_17 (.E(Write_data), .CLK(Clock), .W(r16), .S(s16));
  registrador_32bits registrador_32bits_18 (.E(Write_data), .CLK(Clock), .W(r17), .S(s17));
  registrador_32bits registrador_32bits_19 (.E(Write_data), .CLK(Clock), .W(r18), .S(s18));
  registrador_32bits registrador_32bits_20 (.E(Write_data), .CLK(Clock), .W(r19), .S(s19));
  registrador_32bits registrador_32bits_21 (.E(Write_data), .CLK(Clock), .W(r20), .S(s20));
  registrador_32bits registrador_32bits_22 (.E(Write_data), .CLK(Clock), .W(r21), .S(s21));
  registrador_32bits registrador_32bits_23 (.E(Write_data), .CLK(Clock), .W(r22), .S(s22));
  registrador_32bits registrador_32bits_24 (.E(Write_data), .CLK(Clock), .W(r23), .S(s23));
  registrador_32bits registrador_32bits_25 (.E(Write_data), .CLK(Clock), .W(r24), .S(s24));
  // registrador_32bits registrador_32bits_26: pin names not known; wires that end beside it: Write_data, Clock, r25, s25
  registrador_32bits registrador_32bits_27 (.E(Write_data), .CLK(Clock), .W(r26), .S(s26));
  registrador_32bits registrador_32bits_28 (.E(Write_data), .CLK(Clock), .W(r27), .S(s27));
  registrador_32bits registrador_32bits_29 (.E(Write_data), .CLK(Clock), .W(r28), .S(s28));
  registrador_32bits registrador_32bits_30 (.E(Write_data), .CLK(Clock), .W(r29), .S(s29));
  registrador_32bits registrador_32bits_31 (.E(Write_data), .CLK(Clock), .W(r30), .S(s30));
  registrador_32bits registrador_32bits_32 (.E(Write_data), .CLK(Clock), .W(r31), .S(s31));
  Multiplexer #(.select(5), .width(32)) multiplexer_1 (
    .in0({32{1'b0}}), .in1(s1), .in2(s2), .in3(s3), .in4(s4), .in5(s5), .in6(s6), .in7(s7), .in8(s8),
    .in9(s9), .in10(s10), .in11(s11), .in12(s12), .in13(s13), .in14(s14), .in15(s15), .in16(s16), .in17(s17),
    .in18(s18), .in19(s19), .in20(s20), .in21(s21), .in22(s22), .in23(s23), .in24(s24), .in25(s25),
    .in26(s26), .in27(s27), .in28(s28), .in29(s29), .in30(s30), .in31(s31), .out(Saida_A), .sel(R_address_A));
  Multiplexer #(.select(5), .width(32)) multiplexer_2 (
    .in0({32{1'b0}}), .in1(s1), .in2(s2), .in3(s3), .in4(s4), .in5(s5), .in6(s6), .in7(s7), .in8(s8),
    .in9(s9), .in10(s10), .in11(s11), .in12(s12), .in13(s13), .in14(s14), .in15(s15), .in16(s16), .in17(s17),
    .in18(s18), .in19(s19), .in20(s20), .in21(s21), .in22(s22), .in23(s23), .in24(s24), .in25(s25),
    .in26(s26), .in27(s27), .in28(s28), .in29(s29), .in30(s30), .in31(s31), .out(Saida_B), .sel(R_address_B));

  // Other names for the same wires on the sheet: clk = Clock; Data[31:0] = Write_data
endmodule

module Imm_generator (
  input  [31:0] Instr,
  output [31:0] Saida
);

  wire [31:0] ext_sinal_12x32_1_saida, ext_sinal_12x32_2_saida, ext_sinal_12x32_3_saida;

  Ext_Sinal_12x32 ext_sinal_12x32_1 (.entrada(Instr[31:20]), .Saida(ext_sinal_12x32_1_saida));
  Ext_Sinal_12x32 ext_sinal_12x32_2 (.entrada({Instr[31:25], Instr[11:7]}), .Saida(ext_sinal_12x32_2_saida));
  Ext_Sinal_12x32 ext_sinal_12x32_3 (.entrada({Instr[31:25], Instr[10:7], 1'b0}), .Saida(ext_sinal_12x32_3_saida));
  Multiplexer #(.select(3), .width(32)) multiplexer_1 (
    .in0(ext_sinal_12x32_1_saida), .in1(ext_sinal_12x32_1_saida), .in2(ext_sinal_12x32_2_saida),
    .in3({32{1'b0}}), .in4({32{1'b0}}), .in5({32{1'b0}}), .in6(ext_sinal_12x32_3_saida), .in7({32{1'b0}}),
    .out(Saida), .sel(Instr[6:4]));

  // Notes on the sheet:
  //   OP
  //   Type I
  //   Type S
  //   Type B
  //   Imm Gen = Usa o OP para selecionar o imm da instrução
endmodule

module mem_32reg (
  input  [31:0] Address,
  input  [31:0] Write_data,
  input  Write_enable,
  input  Read_enable,
  input  Clock,
  output [31:0] Saida
);

  wire r0, r1, r2, r3, r4, r5, r6, r7, r8, r9, r10, r11, r12, r13, r14, r15, r16, r17, r18, r19, r20, r21,
       r22, r23, r24, r25, r26, r27, r28, r29, r30, r31;
  wire [31:0] multiplexer_1_out, s0, s1, s2, s3, s4, s5, s6, s7, s8, s9, s10, s11, s12, s13, s14, s15, s16,
       s17, s18, s19, s20, s21, s22, s23, s24, s25, s26, s27, s28, s29, s30, s31;

  Demultiplexer #(.select(5)) demultiplexer_1 (
    .out0(r0), .out1(r1), .out2(r2), .out3(r3), .out4(r4), .out5(r5), .out6(r6), .out7(r7), .out8(r8),
    .out9(r9), .out10(r10), .out11(r11), .out12(r12), .out13(r13), .out14(r14), .out15(r15), .out16(r16),
    .out17(r17), .out18(r18), .out19(r19), .out20(r20), .out21(r21), .out22(r22), .out23(r23), .out24(r24),
    .out25(r25), .out26(r26), .out27(r27), .out28(r28), .out29(r29), .out30(r30), .out31(r31),
    .in(Write_enable), .sel(Address[4:0]));
  registrador_32bits registrador_32bits_1 (.E(Write_data), .CLK(Clock), .W(r0), .S(s0));
  registrador_32bits registrador_32bits_2 (.E(Write_data), .CLK(Clock), .W(r1), .S(s1));
  registrador_32bits registrador_32bits_3 (.E(Write_data), .CLK(Clock), .W(r2), .S(s2));
  registrador_32bits registrador_32bits_4 (.E(Write_data), .CLK(Clock), .W(r3), .S(s3));
  registrador_32bits registrador_32bits_5 (.E(Write_data), .CLK(Clock), .W(r4), .S(s4));
  registrador_32bits registrador_32bits_6 (.E(Write_data), .CLK(Clock), .W(r5), .S(s5));
  registrador_32bits registrador_32bits_7 (.E(Write_data), .CLK(Clock), .W(r6), .S(s6));
  registrador_32bits registrador_32bits_8 (.E(Write_data), .CLK(Clock), .W(r7), .S(s7));
  registrador_32bits registrador_32bits_9 (.E(Write_data), .CLK(Clock), .W(r8), .S(s8));
  registrador_32bits registrador_32bits_10 (.E(Write_data), .CLK(Clock), .W(r9), .S(s9));
  registrador_32bits registrador_32bits_11 (.E(Write_data), .CLK(Clock), .W(r10), .S(s10));
  registrador_32bits registrador_32bits_12 (.E(Write_data), .CLK(Clock), .W(r11), .S(s11));
  registrador_32bits registrador_32bits_13 (.E(Write_data), .CLK(Clock), .W(r12), .S(s12));
  registrador_32bits registrador_32bits_14 (.E(Write_data), .CLK(Clock), .W(r13), .S(s13));
  registrador_32bits registrador_32bits_15 (.E(Write_data), .CLK(Clock), .W(r14), .S(s14));
  registrador_32bits registrador_32bits_16 (.E(Write_data), .CLK(Clock), .W(r15), .S(s15));
  registrador_32bits registrador_32bits_17 (.E(Write_data), .CLK(Clock), .W(r16), .S(s16));
  registrador_32bits registrador_32bits_18 (.E(Write_data), .CLK(Clock), .W(r17), .S(s17));
  registrador_32bits registrador_32bits_19 (.E(Write_data), .CLK(Clock), .W(r18), .S(s18));
  registrador_32bits registrador_32bits_20 (.E(Write_data), .CLK(Clock), .W(r19), .S(s19));
  registrador_32bits registrador_32bits_21 (.E(Write_data), .CLK(Clock), .W(r20), .S(s20));
  registrador_32bits registrador_32bits_22 (.E(Write_data), .CLK(Clock), .W(r21), .S(s21));
  registrador_32bits registrador_32bits_23 (.E(Write_data), .CLK(Clock), .W(r22), .S(s22));
  registrador_32bits registrador_32bits_24 (.E(Write_data), .CLK(Clock), .W(r23), .S(s23));
  registrador_32bits registrador_32bits_25 (.E(Write_data), .CLK(Clock), .W(r24), .S(s24));
  // registrador_32bits registrador_32bits_26: pin names not known; wires that end beside it: Write_data, Clock, r25, s25
  registrador_32bits registrador_32bits_27 (.E(Write_data), .CLK(Clock), .W(r26), .S(s26));
  registrador_32bits registrador_32bits_28 (.E(Write_data), .CLK(Clock), .W(r27), .S(s27));
  registrador_32bits registrador_32bits_29 (.E(Write_data), .CLK(Clock), .W(r28), .S(s28));
  registrador_32bits registrador_32bits_30 (.E(Write_data), .CLK(Clock), .W(r29), .S(s29));
  registrador_32bits registrador_32bits_31 (.E(Write_data), .CLK(Clock), .W(r30), .S(s30));
  registrador_32bits registrador_32bits_32 (.E(Write_data), .CLK(Clock), .W(r31), .S(s31));
  Multiplexer #(.select(5), .width(32)) multiplexer_1 (
    .in0(s0), .in1(s1), .in2(s2), .in3(s3), .in4(s4), .in5(s5), .in6(s6), .in7(s7), .in8(s8), .in9(s9),
    .in10(s10), .in11(s11), .in12(s12), .in13(s13), .in14(s14), .in15(s15), .in16(s16), .in17(s17),
    .in18(s18), .in19(s19), .in20(s20), .in21(s21), .in22(s22), .in23(s23), .in24(s24), .in25(s25),
    .in26(s26), .in27(s27), .in28(s28), .in29(s29), .in30(s30), .in31(s31), .out(multiplexer_1_out),
    .sel(Address[4:0]));
  Multiplexer #(.width(32)) multiplexer_2 (.in0({32{1'b0}}), .in1(multiplexer_1_out), .out(Saida), .sel(Read_enable));

  // Other names for the same wires on the sheet: R_address_A[4:0] = Address[4:0]; Write_address[4:0] = Address[4:0];
  //   clk = Clock; Data[31:0] = Write_data
endmodule

module Control (
  input  [6:0] OP,
  output Branch,
  output MemRead,
  output MemtoReg,
  output MemWrite,
  output ALUsrc,
  output RegWrite,
  output [1:0] ALUop
);
endmodule

module Redutor_32x8bits (
  input  [31:0] Entrada,
  output [7:0] Saida
);


  assign Saida = Entrada[7:0];
endmodule

module ALU_control (
  input  [1:0] ALU_Op,
  input  [31:0] Instruction,
  output [3:0] ALU_input
);

  wire and_1_out, and_2_out, and_3_out, and_4_out, not_1_out, not_2_out, not_3_out, not_4_out, not_5_out,
       not_6_out, not_7_out, not_8_out, not_9_out, not_10_out, not_11_out, not_12_out, not_13_out,
       not_14_out, not_15_out, not_16_out, not_17_out, not_18_out, not_19_out, or_1_out, or_2_out;

  not not_1 (not_1_out, Instruction[13]);
  not not_2 (not_2_out, Instruction[14]);
  not not_3 (not_3_out, Instruction[12]);
  not not_4 (not_4_out, Instruction[13]);
  not not_5 (not_5_out, Instruction[14]);
  not not_6 (not_6_out, ALU_Op[1]);
  not not_7 (not_7_out, Instruction[12]);
  not not_8 (not_8_out, Instruction[13]);
  not not_9 (not_9_out, Instruction[14]);
  not not_10 (not_10_out, ALU_Op[1]);
  not not_11 (not_11_out, Instruction[12]);
  not not_12 (not_12_out, Instruction[13]);
  not not_13 (not_13_out, Instruction[14]);
  not not_14 (not_14_out, ALU_Op[1]);
  not not_15 (not_15_out, Instruction[12]);
  not not_16 (not_16_out, Instruction[13]);
  not not_17 (not_17_out, Instruction[14]);
  not not_18 (not_18_out, ALU_Op[0]);
  not not_19 (not_19_out, ALU_Op[0]);
  and and_1 (and_1_out, Instruction[12], not_1_out, not_2_out, ALU_Op[0], ALU_Op[1]);
  and and_2 (and_2_out, not_3_out, Instruction[13], Instruction[14], not_18_out, ALU_Op[1]);
  or or_1 (or_1_out, Instruction[12], not_4_out, not_5_out, ALU_Op[0], not_6_out);
  or or_2 (or_2_out, not_7_out, not_8_out, not_9_out, ALU_Op[0], not_10_out);
  and and_3 (and_3_out, not_11_out, not_12_out, not_13_out, ALU_Op[0], not_14_out);
  and and_4 (and_4_out, not_15_out, not_16_out, not_17_out, not_19_out, ALU_Op[1], Instruction[30]);
  or or_3 (ALU_input[0], and_1_out, and_2_out);
  and and_5 (ALU_input[1], or_1_out, or_2_out);
  or or_4 (ALU_input[2], and_3_out, and_4_out);

  assign ALU_input[3] = 1'b0;

  // Other names for the same wires on the sheet: C0 = ALU_input[0]; C1 = ALU_input[1]; C2 = ALU_input[2];
  //   OP_0 = ALU_Op[0]; OP_1 = ALU_Op[1]; B0 = Instruction[12]; Funct3[2:0] = Instruction[14:12];
  //   B1 = Instruction[13]; B2 = Instruction[14]; A0 = Instruction[25]; Funct7[6:0] = Instruction[31:25];
  //   A1 = Instruction[26]; A2 = Instruction[27]; A3 = Instruction[28]; A4 = Instruction[29]; A5 = Instruction[30];
  //   A6 = Instruction[31]
endmodule

module Ext_Sinal_12x32 (
  input  [11:0] entrada,
  output [31:0] Saida
);


  assign Saida = {{21{entrada[11]}}, entrada[10:0]};
endmodule
