// Logisim project Banco_de_registradores_16x32bits.circ as structural Verilog: 2 circuits, main circuit main
module main (
  input  [3:0] in_1,
  input  [31:0] in_2,
  input  in_3,
  input  [3:0] Writting_address,
  input  CLK,
  input  [31:0] in_6,
  input  in_7,
  input  [3:0] in_8,
  output [31:0] out_9
);

  wire demultiplexer_1_out0, demultiplexer_1_out1, demultiplexer_1_out2, demultiplexer_1_out3,
       demultiplexer_1_out4, demultiplexer_1_out5, demultiplexer_1_out6, demultiplexer_1_out7,
       demultiplexer_1_out8, demultiplexer_1_out9, demultiplexer_1_out10, demultiplexer_1_out11,
       demultiplexer_1_out12, demultiplexer_1_out13, demultiplexer_1_out14, demultiplexer_1_out15;
  wire [31:0] registrador_32bits_1_s, registrador_32bits_2_s, registrador_32bits_3_s, registrador_32bits_4_s,
       registrador_32bits_5_s, registrador_32bits_6_s, registrador_32bits_7_s, registrador_32bits_8_s,
       registrador_32bits_9_s, registrador_32bits_10_s, registrador_32bits_11_s, registrador_32bits_12_s,
       registrador_32bits_13_s, registrador_32bits_14_s, registrador_32bits_15_s, registrador_32bits_16_s;

  Demultiplexer #(.select(4)) demultiplexer_1 (
    .out0(demultiplexer_1_out0), .out1(demultiplexer_1_out1), .out2(demultiplexer_1_out2),
    .out3(demultiplexer_1_out3), .out4(demultiplexer_1_out4), .out5(demultiplexer_1_out5),
    .out6(demultiplexer_1_out6), .out7(demultiplexer_1_out7), .out8(demultiplexer_1_out8),
    .out9(demultiplexer_1_out9), .out10(demultiplexer_1_out10), .out11(demultiplexer_1_out11),
    .out12(demultiplexer_1_out12), .out13(demultiplexer_1_out13), .out14(demultiplexer_1_out14),
    .out15(demultiplexer_1_out15), .in(in_3), .sel(Writting_address));
  registrador_32bits registrador_32bits_1 (.E(in_2), .W(demultiplexer_1_out0), .CLK(CLK), .S(registrador_32bits_1_s));
  registrador_32bits registrador_32bits_2 (.E(in_2), .W(demultiplexer_1_out1), .CLK(CLK), .S(registrador_32bits_2_s));
  registrador_32bits registrador_32bits_3 (.E(in_2), .W(demultiplexer_1_out2), .CLK(CLK), .S(registrador_32bits_3_s));
  registrador_32bits registrador_32bits_4 (.E(in_2), .W(demultiplexer_1_out3), .CLK(CLK), .S(registrador_32bits_4_s));
  registrador_32bits registrador_32bits_5 (.E(in_2), .W(demultiplexer_1_out4), .CLK(CLK), .S(registrador_32bits_5_s));
  registrador_32bits registrador_32bits_6 (.E(in_2), .W(demultiplexer_1_out5), .CLK(CLK), .S(registrador_32bits_6_s));
  registrador_32bits registrador_32bits_7 (.E(in_2), .W(demultiplexer_1_out6), .CLK(CLK), .S(registrador_32bits_7_s));
  registrador_32bits registrador_32bits_8 (.E(in_2), .W(demultiplexer_1_out7), .CLK(CLK), .S(registrador_32bits_8_s));
  Multiplexer #(.enable("true"), .select(4), .width(32)) multiplexer_1 (
    .in0(registrador_32bits_1_s), .in1(registrador_32bits_2_s), .in2(registrador_32bits_3_s),
    .in3(registrador_32bits_4_s), .in4(registrador_32bits_5_s), .in5(registrador_32bits_6_s),
    .in6(registrador_32bits_7_s), .in7(registrador_32bits_8_s), .in8(registrador_32bits_16_s),
    .in9(registrador_32bits_15_s), .in10(registrador_32bits_14_s), .in11(registrador_32bits_13_s),
    .in12(registrador_32bits_12_s), .in13(registrador_32bits_11_s), .in14(registrador_32bits_10_s),
    .in15(registrador_32bits_9_s), .out(in_6), .sel(in_8), .en(in_7));
  Multiplexer #(.enable("true"), .select(4), .width(32)) multiplexer_2 (
    .in0(registrador_32bits_1_s), .in1(registrador_32bits_2_s), .in2(registrador_32bits_3_s),
    .in3(registrador_32bits_4_s), .in4(registrador_32bits_5_s), .in5(registrador_32bits_6_s),
    .in6(registrador_32bits_7_s), .in7(registrador_32bits_8_s), .in8(registrador_32bits_9_s),
    .in9(registrador_32bits_10_s), .in10(registrador_32bits_11_s), .in11(registrador_32bits_12_s),
    .in12(registrador_32bits_13_s), .in13(registrador_32bits_14_s), .in14(registrador_32bits_15_s),
    .in15(registrador_32bits_16_s), .out(out_9), .sel(in_1), .en(in_7));
  registrador_32bits registrador_32bits_9 (.E(in_2), .W(demultiplexer_1_out8), .CLK(CLK), .S(registrador_32bits_9_s));
  registrador_32bits registrador_32bits_10 (.E(in_2), .W(demultiplexer_1_out9), .CLK(CLK), .S(registrador_32bits_10_s));
  registrador_32bits registrador_32bits_11 (
    .E(in_2), .W(demultiplexer_1_out10), .CLK(CLK), .S(registrador_32bits_11_s));
  registrador_32bits registrador_32bits_12 (
    .E(in_2), .W(demultiplexer_1_out11), .CLK(CLK), .S(registrador_32bits_12_s));
  registrador_32bits registrador_32bits_13 (
    .E(in_2), .W(demultiplexer_1_out12), .CLK(CLK), .S(registrador_32bits_13_s));
  registrador_32bits registrador_32bits_14 (
    .E(in_2), .W(demultiplexer_1_out13), .CLK(CLK), .S(registrador_32bits_14_s));
  registrador_32bits registrador_32bits_15 (
    .E(in_2), .W(demultiplexer_1_out14), .CLK(CLK), .S(registrador_32bits_15_s));
  registrador_32bits registrador_32bits_16 (
    .E(in_2), .W(demultiplexer_1_out15), .CLK(CLK), .S(registrador_32bits_16_s));

  // Notes on the sheet:
  //   W (enable writing)
  //   Entrada de Dados
  //   W0 -> W15
  //   Reading Address A
  //   Saida B
  //   Reading Address B
  //   R (Enable Reading)
  //   Saida A
endmodule

module registrador_32bits (
  input  [31:0] E,
  input  W,
  input  CLK,
  output [31:0] S
);

  wire multiplexer_1_out, multiplexer_2_out, multiplexer_3_out, multiplexer_4_out, multiplexer_5_out,
       multiplexer_6_out, multiplexer_7_out, multiplexer_8_out, multiplexer_9_out, multiplexer_10_out,
       multiplexer_11_out, multiplexer_12_out, multiplexer_13_out, multiplexer_14_out, multiplexer_15_out,
       multiplexer_16_out, multiplexer_17_out, multiplexer_18_out, multiplexer_19_out, multiplexer_20_out,
       multiplexer_21_out, multiplexer_22_out, multiplexer_23_out, multiplexer_24_out, multiplexer_25_out,
       multiplexer_26_out, multiplexer_27_out, multiplexer_28_out, multiplexer_29_out, multiplexer_30_out,
       multiplexer_31_out, multiplexer_32_out;

  Multiplexer multiplexer_1 (.in0(E[0]), .in1(S[0]), .out(multiplexer_1_out), .sel(W));
  Multiplexer multiplexer_2 (.in0(E[8]), .in1(S[8]), .out(multiplexer_2_out), .sel(W));
  Multiplexer multiplexer_3 (.in0(E[16]), .in1(S[16]), .out(multiplexer_3_out), .sel(W));
  Multiplexer multiplexer_4 (.in0(E[31]), .in1(S[24]), .out(multiplexer_4_out), .sel(W));
  D_Flip_Flop d_ff_1 (.D(multiplexer_1_out), .clk(CLK), .Q(S[0]));  // open: Qn, preset, reset
  D_Flip_Flop d_ff_2 (.D(multiplexer_2_out), .clk(CLK), .Q(S[8]));  // open: Qn, preset, reset
  D_Flip_Flop d_ff_3 (.D(multiplexer_3_out), .clk(CLK), .Q(S[16]));  // open: Qn, preset, reset
  D_Flip_Flop d_ff_4 (.D(multiplexer_4_out), .clk(CLK), .Q(S[24]));  // open: Qn, preset, reset
  D_Flip_Flop d_ff_5 (.D(multiplexer_5_out), .clk(CLK), .Q(S[1]));  // open: Qn, preset, reset
  Multiplexer multiplexer_5 (.in0(E[1]), .in1(S[1]), .out(multiplexer_5_out), .sel(W));
  D_Flip_Flop d_ff_6 (.D(multiplexer_6_out), .clk(CLK), .Q(S[9]));  // open: Qn, preset, reset
  Multiplexer multiplexer_6 (.in0(E[9]), .in1(S[9]), .out(multiplexer_6_out), .sel(W));
  D_Flip_Flop d_ff_7 (.D(multiplexer_7_out), .clk(CLK), .Q(S[17]));  // open: Qn, preset, reset
  Multiplexer multiplexer_7 (.in0(E[17]), .in1(S[17]), .out(multiplexer_7_out), .sel(W));
  D_Flip_Flop d_ff_8 (.D(multiplexer_8_out), .clk(CLK), .Q(S[25]));  // open: Qn, preset, reset
  Multiplexer multiplexer_8 (.in0(E[30]), .in1(S[25]), .out(multiplexer_8_out), .sel(W));
  D_Flip_Flop d_ff_9 (.D(multiplexer_9_out), .clk(CLK), .Q(S[2]));  // open: Qn, preset, reset
  Multiplexer multiplexer_9 (.in0(E[2]), .in1(S[2]), .out(multiplexer_9_out), .sel(W));
  Multiplexer multiplexer_10 (.in0(E[10]), .in1(S[10]), .out(multiplexer_10_out), .sel(W));
  D_Flip_Flop d_ff_10 (.D(multiplexer_11_out), .clk(CLK), .Q(S[18]));  // open: Qn, preset, reset
  Multiplexer multiplexer_11 (.in0(E[18]), .in1(S[18]), .out(multiplexer_11_out), .sel(W));
  Multiplexer multiplexer_12 (.in0(E[29]), .in1(S[26]), .out(multiplexer_12_out), .sel(W));
  D_Flip_Flop d_ff_11 (.D(multiplexer_10_out), .clk(CLK), .Q(S[10]));  // open: Qn, preset, reset
  D_Flip_Flop d_ff_12 (.D(multiplexer_12_out), .clk(CLK), .Q(S[26]));  // open: Qn, preset, reset
  Multiplexer multiplexer_13 (.in0(E[3]), .in1(S[3]), .out(multiplexer_13_out), .sel(W));
  Multiplexer multiplexer_14 (.in0(E[11]), .in1(S[11]), .out(multiplexer_14_out), .sel(W));
  Multiplexer multiplexer_15 (.in0(E[19]), .in1(S[19]), .out(multiplexer_15_out), .sel(W));
  Multiplexer multiplexer_16 (.in0(E[28]), .in1(S[27]), .out(multiplexer_16_out), .sel(W));
  D_Flip_Flop d_ff_13 (.D(multiplexer_13_out), .clk(CLK), .Q(S[3]));  // open: Qn, preset, reset
  D_Flip_Flop d_ff_14 (.D(multiplexer_14_out), .clk(CLK), .Q(S[11]));  // open: Qn, preset, reset
  D_Flip_Flop d_ff_15 (.D(multiplexer_15_out), .clk(CLK), .Q(S[19]));  // open: Qn, preset, reset
  D_Flip_Flop d_ff_16 (.D(multiplexer_16_out), .clk(CLK), .Q(S[27]));  // open: Qn, preset, reset
  D_Flip_Flop d_ff_17 (.D(multiplexer_17_out), .clk(CLK), .Q(S[4]));  // open: Qn, preset, reset
  Multiplexer multiplexer_17 (.in0(E[4]), .in1(S[4]), .out(multiplexer_17_out), .sel(W));
  D_Flip_Flop d_ff_18 (.D(multiplexer_18_out), .clk(CLK), .Q(S[12]));  // open: Qn, preset, reset
  Multiplexer multiplexer_18 (.in0(E[12]), .in1(S[12]), .out(multiplexer_18_out), .sel(W));
  D_Flip_Flop d_ff_19 (.D(multiplexer_19_out), .clk(CLK), .Q(S[20]));  // open: Qn, preset, reset
  Multiplexer multiplexer_19 (.in0(E[20]), .in1(S[20]), .out(multiplexer_19_out), .sel(W));
  D_Flip_Flop d_ff_20 (.D(multiplexer_20_out), .clk(CLK), .Q(S[28]));  // open: Qn, preset, reset
  Multiplexer multiplexer_20 (.in0(E[27]), .in1(S[28]), .out(multiplexer_20_out), .sel(W));
  D_Flip_Flop d_ff_21 (.D(multiplexer_21_out), .clk(CLK), .Q(S[5]));  // open: Qn, preset, reset
  Multiplexer multiplexer_21 (.in0(E[5]), .in1(S[5]), .out(multiplexer_21_out), .sel(W));
  Multiplexer multiplexer_22 (.in0(E[13]), .in1(S[13]), .out(multiplexer_22_out), .sel(W));
  D_Flip_Flop d_ff_22 (.D(multiplexer_23_out), .clk(CLK), .Q(S[21]));  // open: Qn, preset, reset
  Multiplexer multiplexer_23 (.in0(E[21]), .in1(S[21]), .out(multiplexer_23_out), .sel(W));
  Multiplexer multiplexer_24 (.in0(E[26]), .in1(S[29]), .out(multiplexer_24_out), .sel(W));
  D_Flip_Flop d_ff_23 (.D(multiplexer_22_out), .clk(CLK), .Q(S[13]));  // open: Qn, preset, reset
  D_Flip_Flop d_ff_24 (.D(multiplexer_24_out), .clk(CLK), .Q(S[29]));  // open: Qn, preset, reset
  Multiplexer multiplexer_25 (.in0(E[6]), .in1(S[6]), .out(multiplexer_25_out), .sel(W));
  Multiplexer multiplexer_26 (.in0(E[14]), .in1(S[14]), .out(multiplexer_26_out), .sel(W));
  Multiplexer multiplexer_27 (.in0(E[22]), .in1(S[22]), .out(multiplexer_27_out), .sel(W));
  Multiplexer multiplexer_28 (.in0(E[25]), .in1(S[30]), .out(multiplexer_28_out), .sel(W));
  D_Flip_Flop d_ff_25 (.D(multiplexer_25_out), .clk(CLK), .Q(S[6]));  // open: Qn, preset, reset
  D_Flip_Flop d_ff_26 (.D(multiplexer_26_out), .clk(CLK), .Q(S[14]));  // open: Qn, preset, reset
  D_Flip_Flop d_ff_27 (.D(multiplexer_27_out), .clk(CLK), .Q(S[22]));  // open: Qn, preset, reset
  D_Flip_Flop d_ff_28 (.D(multiplexer_28_out), .clk(CLK), .Q(S[30]));  // open: Qn, preset, reset
  D_Flip_Flop d_ff_29 (.D(multiplexer_29_out), .clk(CLK), .Q(S[7]));  // open: Qn, preset, reset
  Multiplexer multiplexer_29 (.in0(E[7]), .in1(S[7]), .out(multiplexer_29_out), .sel(W));
  D_Flip_Flop d_ff_30 (.D(multiplexer_30_out), .clk(CLK), .Q(S[15]));  // open: Qn, preset, reset
  Multiplexer multiplexer_30 (.in0(E[15]), .in1(S[15]), .out(multiplexer_30_out), .sel(W));
  D_Flip_Flop d_ff_31 (.D(multiplexer_31_out), .clk(CLK), .Q(S[23]));  // open: Qn, preset, reset
  Multiplexer multiplexer_31 (.in0(E[23]), .in1(S[23]), .out(multiplexer_31_out), .sel(W));
  D_Flip_Flop d_ff_32 (.D(multiplexer_32_out), .clk(CLK), .Q(S[31]));  // open: Qn, preset, reset
  Multiplexer multiplexer_32 (.in0(E[24]), .in1(S[31]), .out(multiplexer_32_out), .sel(W));

  // Notes on the sheet:
  //   Dados (entrada)
  //   W0 (enable)
  //   CLK
  //   D0
  //   W0
  //   D8
  //   W0
  //   D16
  //   W0
  //   D24
  //   W0
  //   D1
  //   D9
  //   D17
  //   D25
  //   D2
  //   D10
  //   D18
  //   D26
  //   D3
  //   D11
  //   D19
  //   D27
  //   D4
  //   D12
  //   D20
  //   D28
  //   D5
  //   D13
  //   D21
  //   D29
  //   D6
  //   D14
  //   D22
  //   D30
  //   D7
  //   D15
  //   D23
  //   D31
  //   Dados (saida)
endmodule
