// Logisim project registrador_32bits.circ as structural Verilog: 1 circuit, main circuit main
module main (
  input  [31:0] E,
  input  W,
  input  CLK,
  output [31:0] S
);

  wire multiplexer_1_out, multiplexer_2_out, multiplexer_3_out, multiplexer_4_out, multiplexer_5_out,
       multiplexer_6_out, multiplexer_7_out, multiplexer_8_out, multiplexer_9_out, multiplexer_10_out,
       multiplexer_11_out, multiplexer_12_out, multiplexer_13_out, multiplexer_14_out, multiplexer_15_out,
       multiplexer_16_out, multiplexer_17_out, multiplexer_18_out, multiplexer_19_out, multiplexer_20_out,
       multiplexer_21_out, multiplexer_22_out, multiplexer_23_out, multiplexer_24_out, multiplexer_25_out,
       multiplexer_26_out, multiplexer_27_out, multiplexer_28_out, multiplexer_29_out, multiplexer_30_out,
       multiplexer_31_out, multiplexer_32_out;

  Multiplexer multiplexer_1 (.in0(E[0]), .in1(S[0]), .out(multiplexer_1_out), .sel(W));
  Multiplexer multiplexer_2 (.in0(E[8]), .in1(S[8]), .out(multiplexer_2_out), .sel(W));
  Multiplexer multiplexer_3 (.in0(E[16]), .in1(S[16]), .out(multiplexer_3_out), .sel(W));
  Multiplexer multiplexer_4 (.in0(E[31]), .in1(S[24]), .out(multiplexer_4_out), .sel(W));
  D_Flip_Flop d_ff_1 (.D(multiplexer_1_out), .clk(CLK), .Q(S[0]));  // open: Qn, preset, reset
  D_Flip_Flop d_ff_2 (.D(multiplexer_2_out), .clk(CLK), .Q(S[8]));  // open: Qn, preset, reset
  D_Flip_Flop d_ff_3 (.D(multiplexer_3_out), .clk(CLK), .Q(S[16]));  // open: Qn, preset, reset
  D_Flip_Flop d_ff_4 (.D(multiplexer_4_out), .clk(CLK), .Q(S[24]));  // open: Qn, preset, reset
  Multiplexer multiplexer_5 (.in0(E[1]), .in1(S[1]), .out(multiplexer_5_out), .sel(W));
  Multiplexer multiplexer_6 (.in0(E[17]), .in1(S[17]), .out(multiplexer_6_out), .sel(W));
  D_Flip_Flop d_ff_5 (.D(multiplexer_5_out), .clk(CLK), .Q(S[1]));  // open: Qn, preset, reset
  D_Flip_Flop d_ff_6 (.D(multiplexer_7_out), .clk(CLK), .Q(S[9]));  // open: Qn, preset, reset
  Multiplexer multiplexer_7 (.in0(E[9]), .in1(S[9]), .out(multiplexer_7_out), .sel(W));
  D_Flip_Flop d_ff_7 (.D(multiplexer_6_out), .clk(CLK), .Q(S[17]));  // open: Qn, preset, reset
  D_Flip_Flop d_ff_8 (.D(multiplexer_8_out), .clk(CLK), .Q(S[25]));  // open: Qn, preset, reset
  Multiplexer multiplexer_8 (.in0(E[30]), .in1(S[25]), .out(multiplexer_8_out), .sel(W));
  D_Flip_Flop d_ff_9 (.D(multiplexer_9_out), .clk(CLK), .Q(S[2]));  // open: Qn, preset, reset
  Multiplexer multiplexer_9 (.in0(E[2]), .in1(S[2]), .out(multiplexer_9_out), .sel(W));
  D_Flip_Flop d_ff_10 (.D(multiplexer_10_out), .clk(CLK), .Q(S[10]));  // open: Qn, preset, reset
  Multiplexer multiplexer_10 (.in0(E[10]), .in1(S[10]), .out(multiplexer_10_out), .sel(W));
  D_Flip_Flop d_ff_11 (.D(multiplexer_11_out), .clk(CLK), .Q(S[18]));  // open: Qn, preset, reset
  Multiplexer multiplexer_11 (.in0(E[18]), .in1(S[18]), .out(multiplexer_11_out), .sel(W));
  D_Flip_Flop d_ff_12 (.D(multiplexer_12_out), .clk(CLK), .Q(S[26]));  // open: Qn, preset, reset
  Multiplexer multiplexer_12 (.in0(E[29]), .in1(S[26]), .out(multiplexer_12_out), .sel(W));
  Multiplexer multiplexer_13 (.in0(E[3]), .in1(S[3]), .out(multiplexer_13_out), .sel(W));
  Multiplexer multiplexer_14 (.in0(E[11]), .in1(S[11]), .out(multiplexer_14_out), .sel(W));
  Multiplexer multiplexer_15 (.in0(E[19]), .in1(S[19]), .out(multiplexer_15_out), .sel(W));
  Multiplexer multiplexer_16 (.in0(E[28]), .in1(S[27]), .out(multiplexer_16_out), .sel(W));
  D_Flip_Flop d_ff_13 (.D(multiplexer_13_out), .clk(CLK), .Q(S[3]));  // open: Qn, preset, reset
  D_Flip_Flop d_ff_14 (.D(multiplexer_14_out), .clk(CLK), .Q(S[11]));  // open: Qn, preset, reset
  D_Flip_Flop d_ff_15 (.D(multiplexer_15_out), .clk(CLK), .Q(S[19]));  // open: Qn, preset, reset
  D_Flip_Flop d_ff_16 (.D(multiplexer_16_out), .clk(CLK), .Q(S[27]));  // open: Qn, preset, reset
  Multiplexer multiplexer_17 (.in0(E[4]), .in1(S[4]), .out(multiplexer_17_out), .sel(W));
  Multiplexer multiplexer_18 (.in0(E[20]), .in1(S[20]), .out(multiplexer_18_out), .sel(W));
  D_Flip_Flop d_ff_17 (.D(multiplexer_17_out), .clk(CLK), .Q(S[4]));  // open: Qn, preset, reset
  D_Flip_Flop d_ff_18 (.D(multiplexer_19_out), .clk(CLK), .Q(S[12]));  // open: Qn, preset, reset
  Multiplexer multiplexer_19 (.in0(E[12]), .in1(S[12]), .out(multiplexer_19_out), .sel(W));
  D_Flip_Flop d_ff_19 (.D(multiplexer_18_out), .clk(CLK), .Q(S[20]));  // open: Qn, preset, reset
  D_Flip_Flop d_ff_20 (.D(multiplexer_20_out), .clk(CLK), .Q(S[28]));  // open: Qn, preset, reset
  Multiplexer multiplexer_20 (.in0(E[27]), .in1(S[28]), .out(multiplexer_20_out), .sel(W));
  D_Flip_Flop d_ff_21 (.D(multiplexer_21_out), .clk(CLK), .Q(S[5]));  // open: Qn, preset, reset
  Multiplexer multiplexer_21 (.in0(E[5]), .in1(S[5]), .out(multiplexer_21_out), .sel(W));
  D_Flip_Flop d_ff_22 (.D(multiplexer_22_out), .clk(CLK), .Q(S[13]));  // open: Qn, preset, reset
  Multiplexer multiplexer_22 (.in0(E[13]), .in1(S[13]), .out(multiplexer_22_out), .sel(W));
  D_Flip_Flop d_ff_23 (.D(multiplexer_23_out), .clk(CLK), .Q(S[21]));  // open: Qn, preset, reset
  Multiplexer multiplexer_23 (.in0(E[21]), .in1(S[21]), .out(multiplexer_23_out), .sel(W));
  D_Flip_Flop d_ff_24 (.D(multiplexer_24_out), .clk(CLK), .Q(S[29]));  // open: Qn, preset, reset
  Multiplexer multiplexer_24 (.in0(E[26]), .in1(S[29]), .out(multiplexer_24_out), .sel(W));
  Multiplexer multiplexer_25 (.in0(E[6]), .in1(S[6]), .out(multiplexer_25_out), .sel(W));
  Multiplexer multiplexer_26 (.in0(E[14]), .in1(S[14]), .out(multiplexer_26_out), .sel(W));
  Multiplexer multiplexer_27 (.in0(E[22]), .in1(S[22]), .out(multiplexer_27_out), .sel(W));
  Multiplexer multiplexer_28 (.in0(E[25]), .in1(S[30]), .out(multiplexer_28_out), .sel(W));
  D_Flip_Flop d_ff_25 (.D(multiplexer_25_out), .clk(CLK), .Q(S[6]));  // open: Qn, preset, reset
  D_Flip_Flop d_ff_26 (.D(multiplexer_26_out), .clk(CLK), .Q(S[14]));  // open: Qn, preset, reset
  D_Flip_Flop d_ff_27 (.D(multiplexer_27_out), .clk(CLK), .Q(S[22]));  // open: Qn, preset, reset
  D_Flip_Flop d_ff_28 (.D(multiplexer_28_out), .clk(CLK), .Q(S[30]));  // open: Qn, preset, reset
  Multiplexer multiplexer_29 (.in0(E[7]), .in1(S[7]), .out(multiplexer_29_out), .sel(W));
  Multiplexer multiplexer_30 (.in0(E[23]), .in1(S[23]), .out(multiplexer_30_out), .sel(W));
  D_Flip_Flop d_ff_29 (.D(multiplexer_29_out), .clk(CLK), .Q(S[7]));  // open: Qn, preset, reset
  D_Flip_Flop d_ff_30 (.D(multiplexer_31_out), .clk(CLK), .Q(S[15]));  // open: Qn, preset, reset
  Multiplexer multiplexer_31 (.in0(E[15]), .in1(S[15]), .out(multiplexer_31_out), .sel(W));
  D_Flip_Flop d_ff_31 (.D(multiplexer_30_out), .clk(CLK), .Q(S[23]));  // open: Qn, preset, reset
  D_Flip_Flop d_ff_32 (.D(multiplexer_32_out), .clk(CLK), .Q(S[31]));  // open: Qn, preset, reset
  Multiplexer multiplexer_32 (.in0(E[24]), .in1(S[31]), .out(multiplexer_32_out), .sel(W));

  // Notes on the sheet:
  //   Dados (entrada)
  //   W0 (enable)
  //   CLK
  //   D0
  //   W0
  //   D8
  //   W0
  //   D16
  //   W0
  //   D24
  //   W0
  //   D1
  //   D17
  //   D9
  //   D25
  //   D2
  //   D10
  //   D18
  //   D26
  //   D3
  //   D11
  //   D19
  //   D27
  //   D4
  //   D20
  //   D12
  //   D28
  //   D5
  //   D13
  //   D21
  //   D29
  //   D6
  //   D14
  //   D22
  //   D30
  //   D7
  //   D23
  //   D31
  //   D15
  //   Dados (saida)
endmodule
