// Logisim project MIPS_projeto.circ as structural Verilog: 14 circuits, main circuit main
module main (
);

  wire CLK, Enable_Display, MUX_PC, MUX_ULA, ula_1_zero, Write_Enable;
  wire [3:0] Funct_ULA;
  wire [23:0] pc_1_s_2;
  wire [31:0] banco_registradores16x32bits_1_a, banco_registradores16x32bits_1_b, extsinal_1_saida,
       extzero_1_saida, full_adder_32bits_1_soma, full_adder_32bits_2_soma, Mem_dados_data,
       multiplexer_1_out, multiplexer_2_out, ula_1_c;
  wire [31:24] pc_1_s;

  Multiplexer #(.width(32)) multiplexer_1 (
    .in0(full_adder_32bits_1_soma), .in1(full_adder_32bits_2_soma), .out(multiplexer_1_out), .sel(MUX_PC));
  Full_Adder_32bits full_adder_32bits_1 (
    .A({pc_1_s, pc_1_s_2}), .B(32'h1), .Soma(full_adder_32bits_1_soma));  // open: C_in, C_out, Zero
  Clock clock_1 (.out(CLK));
  PC pc_1 (.E(multiplexer_1_out), .CLK(CLK), .S({pc_1_s, pc_1_s_2}));  // open: W
  Full_Adder_32bits full_adder_32bits_2 (
    .A(extsinal_1_saida), .B({pc_1_s, pc_1_s_2}), .Soma(full_adder_32bits_2_soma));  // open: C_in, C_out, Zero
  ROM #(.addrWidth(24), .dataWidth(32)) Mem_dados (.addr(pc_1_s_2), .data(Mem_dados_data));
  extSinal extsinal_1 (.entrada(Mem_dados_data[31:16]), .Saida(extsinal_1_saida));
  banco_registradores16x32bits banco_registradores16x32bits_1 (
    .R_address_A(Mem_dados_data[7:4]), .Dados(ula_1_c), .W_enable(Write_Enable),
    .W_address(Mem_dados_data[15:12]), .CLK(CLK), .R_address_B(Mem_dados_data[11:8]),
    .A(banco_registradores16x32bits_1_a), .B(banco_registradores16x32bits_1_b));  // open: R
  ROM #(.addrWidth(4)) Mem_ccontrole (
    .addr(Mem_dados_data[3:0]), .data({MUX_PC, Write_Enable, Funct_ULA, MUX_ULA, Enable_Display}));
  extZero extzero_1 (.entrada(Mem_dados_data[31:16]), .Saida(extzero_1_saida));
  Multiplexer #(.width(32)) multiplexer_2 (
    .in0(banco_registradores16x32bits_1_b), .in1(extzero_1_saida), .out(multiplexer_2_out), .sel(MUX_ULA));
  ULA ula_1 (
    .A(banco_registradores16x32bits_1_a), .B(multiplexer_2_out), .Funct(Funct_ULA), .C(ula_1_c),
    .Zero(ula_1_zero));

  // Notes on the sheet:
  //   OP
  //   A
  //   B
  //   C
  //   Const
endmodule

module registrador_32bits (
  input  [31:0] E,
  input  CLK,
  input  W,
  output [31:0] S
);

  wire multiplexer_1_out, multiplexer_2_out, multiplexer_3_out, multiplexer_4_out, multiplexer_5_out,
       multiplexer_6_out, multiplexer_7_out, multiplexer_8_out, multiplexer_9_out, multiplexer_10_out,
       multiplexer_11_out, multiplexer_12_out, multiplexer_13_out, multiplexer_14_out, multiplexer_15_out,
       multiplexer_16_out, multiplexer_17_out, multiplexer_18_out, multiplexer_19_out, multiplexer_20_out,
       multiplexer_21_out, multiplexer_22_out, multiplexer_23_out, multiplexer_24_out, multiplexer_25_out,
       multiplexer_26_out, multiplexer_27_out, multiplexer_28_out, multiplexer_29_out, multiplexer_30_out,
       multiplexer_31_out, multiplexer_32_out;

  D_Flip_Flop d_ff_1 (.D(multiplexer_1_out), .clk(CLK), .Q(S[0]));  // open: Qn, preset, reset
  Multiplexer multiplexer_1 (.in0(S[0]), .in1(E[0]), .out(multiplexer_1_out), .sel(W));
  D_Flip_Flop d_ff_2 (.D(multiplexer_2_out), .clk(CLK), .Q(S[8]));  // open: Qn, preset, reset
  Multiplexer multiplexer_2 (.in0(S[8]), .in1(E[8]), .out(multiplexer_2_out), .sel(W));
  D_Flip_Flop d_ff_3 (.D(multiplexer_3_out), .clk(CLK), .Q(S[16]));  // open: Qn, preset, reset
  Multiplexer multiplexer_3 (.in0(S[16]), .in1(E[16]), .out(multiplexer_3_out), .sel(W));
  D_Flip_Flop d_ff_4 (.D(multiplexer_4_out), .clk(CLK), .Q(S[24]));  // open: Qn, preset, reset
  Multiplexer multiplexer_4 (.in0(S[24]), .in1(E[24]), .out(multiplexer_4_out), .sel(W));
  Multiplexer multiplexer_5 (.in0(S[1]), .in1(E[1]), .out(multiplexer_5_out), .sel(W));
  Multiplexer multiplexer_6 (.in0(S[9]), .in1(E[9]), .out(multiplexer_6_out), .sel(W));
  Multiplexer multiplexer_7 (.in0(S[17]), .in1(E[17]), .out(multiplexer_7_out), .sel(W));
  Multiplexer multiplexer_8 (.in0(S[25]), .in1(E[25]), .out(multiplexer_8_out), .sel(W));
  D_Flip_Flop d_ff_5 (.D(multiplexer_5_out), .clk(CLK), .Q(S[1]));  // open: Qn, preset, reset
  D_Flip_Flop d_ff_6 (.D(multiplexer_6_out), .clk(CLK), .Q(S[9]));  // open: Qn, preset, reset
  D_Flip_Flop d_ff_7 (.D(multiplexer_7_out), .clk(CLK), .Q(S[17]));  // open: Qn, preset, reset
  D_Flip_Flop d_ff_8 (.D(multiplexer_8_out), .clk(CLK), .Q(S[25]));  // open: Qn, preset, reset
  Multiplexer multiplexer_9 (.in0(S[2]), .in1(E[2]), .out(multiplexer_9_out), .sel(W));
  Multiplexer multiplexer_10 (.in0(S[10]), .in1(E[10]), .out(multiplexer_10_out), .sel(W));
  Multiplexer multiplexer_11 (.in0(S[18]), .in1(E[18]), .out(multiplexer_11_out), .sel(W));
  Multiplexer multiplexer_12 (.in0(S[26]), .in1(E[26]), .out(multiplexer_12_out), .sel(W));
  D_Flip_Flop d_ff_9 (.D(multiplexer_9_out), .clk(CLK), .Q(S[2]));  // open: Qn, preset, reset
  D_Flip_Flop d_ff_10 (.D(multiplexer_10_out), .clk(CLK), .Q(S[10]));  // open: Qn, preset, reset
  D_Flip_Flop d_ff_11 (.D(multiplexer_11_out), .clk(CLK), .Q(S[18]));  // open: Qn, preset, reset
  D_Flip_Flop d_ff_12 (.D(multiplexer_12_out), .clk(CLK), .Q(S[26]));  // open: Qn, preset, reset
  D_Flip_Flop d_ff_13 (.D(multiplexer_13_out), .clk(CLK), .Q(S[3]));  // open: Qn, preset, reset
  Multiplexer multiplexer_13 (.in0(S[3]), .in1(E[3]), .out(multiplexer_13_out), .sel(W));
  D_Flip_Flop d_ff_14 (.D(multiplexer_14_out), .clk(CLK), .Q(S[11]));  // open: Qn, preset, reset
  Multiplexer multiplexer_14 (.in0(S[11]), .in1(E[11]), .out(multiplexer_14_out), .sel(W));
  D_Flip_Flop d_ff_15 (.D(multiplexer_15_out), .clk(CLK), .Q(S[19]));  // open: Qn, preset, reset
  Multiplexer multiplexer_15 (.in0(S[19]), .in1(E[19]), .out(multiplexer_15_out), .sel(W));
  D_Flip_Flop d_ff_16 (.D(multiplexer_16_out), .clk(CLK), .Q(S[27]));  // open: Qn, preset, reset
  Multiplexer multiplexer_16 (.in0(S[27]), .in1(E[27]), .out(multiplexer_16_out), .sel(W));
  Multiplexer multiplexer_17 (.in0(S[4]), .in1(E[4]), .out(multiplexer_17_out), .sel(W));
  Multiplexer multiplexer_18 (.in0(S[12]), .in1(E[12]), .out(multiplexer_18_out), .sel(W));
  Multiplexer multiplexer_19 (.in0(S[20]), .in1(E[20]), .out(multiplexer_19_out), .sel(W));
  Multiplexer multiplexer_20 (.in0(S[28]), .in1(E[28]), .out(multiplexer_20_out), .sel(W));
  D_Flip_Flop d_ff_17 (.D(multiplexer_17_out), .clk(CLK), .Q(S[4]));  // open: Qn, preset, reset
  D_Flip_Flop d_ff_18 (.D(multiplexer_18_out), .clk(CLK), .Q(S[12]));  // open: Qn, preset, reset
  D_Flip_Flop d_ff_19 (.D(multiplexer_19_out), .clk(CLK), .Q(S[20]));  // open: Qn, preset, reset
  D_Flip_Flop d_ff_20 (.D(multiplexer_20_out), .clk(CLK), .Q(S[28]));  // open: Qn, preset, reset
  D_Flip_Flop d_ff_21 (.D(multiplexer_21_out), .clk(CLK), .Q(S[5]));  // open: Qn, preset, reset
  Multiplexer multiplexer_21 (.in0(S[5]), .in1(E[5]), .out(multiplexer_21_out), .sel(W));
  D_Flip_Flop d_ff_22 (.D(multiplexer_22_out), .clk(CLK), .Q(S[13]));  // open: Qn, preset, reset
  Multiplexer multiplexer_22 (.in0(S[13]), .in1(E[13]), .out(multiplexer_22_out), .sel(W));
  D_Flip_Flop d_ff_23 (.D(multiplexer_23_out), .clk(CLK), .Q(S[21]));  // open: Qn, preset, reset
  Multiplexer multiplexer_23 (.in0(S[21]), .in1(E[21]), .out(multiplexer_23_out), .sel(W));
  D_Flip_Flop d_ff_24 (.D(multiplexer_24_out), .clk(CLK), .Q(S[29]));  // open: Qn, preset, reset
  Multiplexer multiplexer_24 (.in0(S[29]), .in1(E[29]), .out(multiplexer_24_out), .sel(W));
  Multiplexer multiplexer_25 (.in0(S[6]), .in1(E[6]), .out(multiplexer_25_out), .sel(W));
  Multiplexer multiplexer_26 (.in0(S[14]), .in1(E[14]), .out(multiplexer_26_out), .sel(W));
  Multiplexer multiplexer_27 (.in0(S[22]), .in1(E[22]), .out(multiplexer_27_out), .sel(W));
  Multiplexer multiplexer_28 (.in0(S[30]), .in1(E[30]), .out(multiplexer_28_out), .sel(W));
  D_Flip_Flop d_ff_25 (.D(multiplexer_25_out), .clk(CLK), .Q(S[6]));  // open: Qn, preset, reset
  D_Flip_Flop d_ff_26 (.D(multiplexer_26_out), .clk(CLK), .Q(S[14]));  // open: Qn, preset, reset
  D_Flip_Flop d_ff_27 (.D(multiplexer_27_out), .clk(CLK), .Q(S[22]));  // open: Qn, preset, reset
  D_Flip_Flop d_ff_28 (.D(multiplexer_28_out), .clk(CLK), .Q(S[30]));  // open: Qn, preset, reset
  D_Flip_Flop d_ff_29 (.D(multiplexer_29_out), .clk(CLK), .Q(S[7]));  // open: Qn, preset, reset
  Multiplexer multiplexer_29 (.in0(S[7]), .in1(E[7]), .out(multiplexer_29_out), .sel(W));
  D_Flip_Flop d_ff_30 (.D(multiplexer_30_out), .clk(CLK), .Q(S[15]));  // open: Qn, preset, reset
  Multiplexer multiplexer_30 (.in0(S[15]), .in1(E[15]), .out(multiplexer_30_out), .sel(W));
  D_Flip_Flop d_ff_31 (.D(multiplexer_31_out), .clk(CLK), .Q(S[23]));  // open: Qn, preset, reset
  Multiplexer multiplexer_31 (.in0(S[23]), .in1(E[23]), .out(multiplexer_31_out), .sel(W));
  D_Flip_Flop d_ff_32 (.D(multiplexer_32_out), .clk(CLK), .Q(S[31]));  // open: Qn, preset, reset
  Multiplexer multiplexer_32 (.in0(S[31]), .in1(E[31]), .out(multiplexer_32_out), .sel(W));

  // Other names for the same wires on the sheet: D0 = E[0]; D1 = E[1]; D2 = E[2]; D3 = E[3]; D4 = E[4]; D5 = E[5];
  //   D6 = E[6]; D7 = E[7]; D8 = E[8]; D9 = E[9]; D10 = E[10]; D11 = E[11]; D12 = E[12]; D13 = E[13]; D14 = E[14];
  //   D15 = E[15]; D16 = E[16]; D17 = E[17]; D18 = E[18]; D19 = E[19]; D20 = E[20]; D21 = E[21]; D22 = E[22];
  //   D23 = E[23]; D24 = E[24]; D25 = E[25]; D26 = E[26]; D27 = E[27]; D28 = E[28]; D29 = E[29]; D30 = E[30];
  //   D31 = E[31]

  // Notes on the sheet:
  //   Dados (entrada)
  //   CLK
  //   W0 (enable)
  //   Dados (saida)
endmodule

module banco_registradores16x32bits (
  input  [3:0] R_address_A,
  input  [31:0] Dados,
  input  W_enable,
  input  [3:0] W_address,
  input  CLK,
  input  R,
  input  [3:0] R_address_B,
  output [31:0] A,
  output [31:0] B
);

  wire demultiplexer_1_out0, demultiplexer_1_out1, demultiplexer_1_out2, demultiplexer_1_out3,
       demultiplexer_1_out4, demultiplexer_1_out5, demultiplexer_1_out6, demultiplexer_1_out7,
       demultiplexer_1_out8, demultiplexer_1_out9, demultiplexer_1_out10, demultiplexer_1_out11,
       demultiplexer_1_out12, demultiplexer_1_out13, demultiplexer_1_out14, demultiplexer_1_out15;
  wire [31:0] registrador_32bits_1_s, registrador_32bits_2_s, registrador_32bits_3_s, registrador_32bits_4_s,
       registrador_32bits_5_s, registrador_32bits_6_s, registrador_32bits_7_s, registrador_32bits_8_s,
       registrador_32bits_9_s, registrador_32bits_10_s, registrador_32bits_11_s, registrador_32bits_12_s,
       registrador_32bits_13_s, registrador_32bits_14_s, registrador_32bits_15_s, registrador_32bits_16_s;

  Demultiplexer #(.select(4)) demultiplexer_1 (
    .out0(demultiplexer_1_out0), .out1(demultiplexer_1_out1), .out2(demultiplexer_1_out2),
    .out3(demultiplexer_1_out3), .out4(demultiplexer_1_out4), .out5(demultiplexer_1_out5),
    .out6(demultiplexer_1_out6), .out7(demultiplexer_1_out7), .out8(demultiplexer_1_out8),
    .out9(demultiplexer_1_out9), .out10(demultiplexer_1_out10), .out11(demultiplexer_1_out11),
    .out12(demultiplexer_1_out12), .out13(demultiplexer_1_out13), .out14(demultiplexer_1_out14),
    .out15(demultiplexer_1_out15), .in(W_enable), .sel(W_address));
  registrador_32bits registrador_32bits_1 (.E(Dados), .CLK(demultiplexer_1_out0), .W(CLK), .S(registrador_32bits_1_s));
  registrador_32bits registrador_32bits_2 (.E(Dados), .CLK(demultiplexer_1_out1), .W(CLK), .S(registrador_32bits_2_s));
  registrador_32bits registrador_32bits_3 (.E(Dados), .CLK(demultiplexer_1_out2), .W(CLK), .S(registrador_32bits_3_s));
  registrador_32bits registrador_32bits_4 (.E(Dados), .CLK(demultiplexer_1_out3), .W(CLK), .S(registrador_32bits_4_s));
  registrador_32bits registrador_32bits_5 (.E(Dados), .CLK(demultiplexer_1_out4), .W(CLK), .S(registrador_32bits_5_s));
  registrador_32bits registrador_32bits_6 (.E(Dados), .CLK(demultiplexer_1_out5), .W(CLK), .S(registrador_32bits_6_s));
  registrador_32bits registrador_32bits_7 (.E(Dados), .CLK(demultiplexer_1_out6), .W(CLK), .S(registrador_32bits_7_s));
  registrador_32bits registrador_32bits_8 (.E(Dados), .CLK(demultiplexer_1_out7), .W(CLK), .S(registrador_32bits_8_s));
  Multiplexer #(.enable("true"), .select(4), .width(32)) multiplexer_1 (
    .in0(registrador_32bits_1_s), .in1(registrador_32bits_2_s), .in2(registrador_32bits_3_s),
    .in3(registrador_32bits_4_s), .in4(registrador_32bits_5_s), .in5(registrador_32bits_6_s),
    .in6(registrador_32bits_7_s), .in7(registrador_32bits_8_s), .in8(registrador_32bits_16_s),
    .in9(registrador_32bits_15_s), .in10(registrador_32bits_14_s), .in11(registrador_32bits_13_s),
    .in12(registrador_32bits_12_s), .in13(registrador_32bits_11_s), .in14(registrador_32bits_10_s),
    .in15(registrador_32bits_9_s), .out(B), .sel(R_address_B), .en(R));
  Multiplexer #(.enable("true"), .select(4), .width(32)) multiplexer_2 (
    .in0(registrador_32bits_1_s), .in1(registrador_32bits_2_s), .in2(registrador_32bits_3_s),
    .in3(registrador_32bits_4_s), .in4(registrador_32bits_5_s), .in5(registrador_32bits_6_s),
    .in6(registrador_32bits_7_s), .in7(registrador_32bits_8_s), .in8(registrador_32bits_9_s),
    .in9(registrador_32bits_10_s), .in10(registrador_32bits_11_s), .in11(registrador_32bits_12_s),
    .in12(registrador_32bits_13_s), .in13(registrador_32bits_14_s), .in14(registrador_32bits_15_s),
    .in15(registrador_32bits_16_s), .out(A), .sel(R_address_A), .en(R));
  registrador_32bits registrador_32bits_9 (.E(Dados), .CLK(demultiplexer_1_out8), .W(CLK), .S(registrador_32bits_9_s));
  registrador_32bits registrador_32bits_10 (
    .E(Dados), .CLK(demultiplexer_1_out9), .W(CLK), .S(registrador_32bits_10_s));
  registrador_32bits registrador_32bits_11 (
    .E(Dados), .CLK(demultiplexer_1_out10), .W(CLK), .S(registrador_32bits_11_s));
  registrador_32bits registrador_32bits_12 (
    .E(Dados), .CLK(demultiplexer_1_out11), .W(CLK), .S(registrador_32bits_12_s));
  registrador_32bits registrador_32bits_13 (
    .E(Dados), .CLK(demultiplexer_1_out12), .W(CLK), .S(registrador_32bits_13_s));
  registrador_32bits registrador_32bits_14 (
    .E(Dados), .CLK(demultiplexer_1_out13), .W(CLK), .S(registrador_32bits_14_s));
  registrador_32bits registrador_32bits_15 (
    .E(Dados), .CLK(demultiplexer_1_out14), .W(CLK), .S(registrador_32bits_15_s));
  registrador_32bits registrador_32bits_16 (
    .E(Dados), .CLK(demultiplexer_1_out15), .W(CLK), .S(registrador_32bits_16_s));

  // Notes on the sheet:
  //   W (enable writing)
  //   Writting address
  //   Entrada de Dados
  //   CLK
  //   W0 -> W15
  //   Reading Address B
  //   Saida A
  //   Reading Address B
  //   R (Enable Reading)
  //   Saida B
endmodule

module ULA (
  input  [31:0] A,
  input  [31:0] B,
  input  [3:0] Funct,
  output [31:0] C,
  output Zero
);

  wire [31:0] and_1_out, full_adder_32bits_1_soma, full_adder_32bits_2_soma, multiplier_1_out, not_1_out,
       or_1_out, xor_1_out;

  Shifter_1bit shifter_1bit_1 ();  // open: Entrada, Saida
  assign not_1_out = ~B;  // NOT_Gate not_1, 32 bits wide
  Multiplier #(.width(32)) multiplier_1 (.a(A), .b(B), .out(multiplier_1_out));  // open: cin, cout
  assign and_1_out = A & B;  // AND_Gate and_1, 32 bits wide
  assign or_1_out = A | B;  // OR_Gate or_1, 32 bits wide
  assign xor_1_out = A ^ B;  // XOR_Gate xor_1, 32 bits wide
  Full_Adder_32bits full_adder_32bits_1 (
    .A(A), .B(B), .C_in(1'b0), .Soma(full_adder_32bits_1_soma));  // open: C_out, Zero
  Full_Adder_32bits full_adder_32bits_2 (
    .A(A), .B(not_1_out), .C_in(1'b1), .Soma(full_adder_32bits_2_soma));  // open: C_out, Zero
  Multiplexer #(.select(4), .width(32)) multiplexer_1 (
    .in0(full_adder_32bits_1_soma), .in1(full_adder_32bits_2_soma), .in2(multiplier_1_out), .in3(and_1_out),
    .in4(or_1_out), .in5(xor_1_out), .out(C), .sel(Funct));  // open: in6, in7, in8, in9, in10, in11, in12, in13, in14, in15
  nor nor_1 (Zero, C[31], C[30], C[29], C[28], C[27], C[26], C[25], C[24], C[23], C[22], C[21], C[20], C[19], C[18], C[17], C[16], C[14], C[13], C[12], C[11], C[10], C[9], C[8], C[7], C[6], C[5], C[4], C[3], C[2], C[1], C[0], C[15]);

  // Notes on the sheet:
  //   Somador
  //   Subtrator
  //   Multiplicador
  //   AND
  //   OR
  //   XOR
endmodule

module Full_Adder_32bits (
  input  [31:0] A,
  input  [31:0] B,
  input  C_in,
  output C_out,
  output [31:0] Soma,
  output Zero
);

  wire C_in8, C_in16, C_in24, full_adder_1_c_out, full_adder_2_c_out, full_adder_3_c_out, full_adder_4_c_out,
       full_adder_5_c_out, full_adder_6_c_out, full_adder_7_c_out, full_adder_8_c_out, full_adder_9_c_out,
       full_adder_10_c_out, full_adder_11_c_out, full_adder_12_c_out, full_adder_13_c_out,
       full_adder_14_c_out, full_adder_15_c_out, full_adder_16_c_out, full_adder_17_c_out,
       full_adder_18_c_out, full_adder_19_c_out, full_adder_20_c_out, full_adder_21_c_out,
       full_adder_22_c_out, full_adder_23_c_out, full_adder_24_c_out, full_adder_25_c_out,
       full_adder_26_c_out, full_adder_27_c_out, full_adder_28_c_out, full_adder_29_c_out,
       full_adder_30_c_out, full_adder_31_c_out;

  Full_Adder full_adder_1 (.A(A[0]), .B(B[0]), .C_in(C_in), .Soma(Soma[0]), .C_out(full_adder_1_c_out));
  Full_Adder full_adder_2 (.A(A[8]), .B(B[8]), .C_in(C_in8), .Soma(Soma[8]), .C_out(full_adder_2_c_out));
  Full_Adder full_adder_3 (.A(A[16]), .B(B[16]), .C_in(C_in16), .Soma(Soma[16]), .C_out(full_adder_3_c_out));
  Full_Adder full_adder_4 (.A(A[24]), .B(B[24]), .C_in(C_in24), .Soma(Soma[24]), .C_out(full_adder_4_c_out));
  Full_Adder full_adder_5 (.A(A[1]), .B(B[1]), .C_in(full_adder_1_c_out), .Soma(Soma[1]), .C_out(full_adder_5_c_out));
  Full_Adder full_adder_6 (.A(A[9]), .B(B[9]), .C_in(full_adder_2_c_out), .Soma(Soma[9]), .C_out(full_adder_6_c_out));
  Full_Adder full_adder_7 (
    .A(A[17]), .B(B[17]), .C_in(full_adder_3_c_out), .Soma(Soma[17]), .C_out(full_adder_7_c_out));
  Full_Adder full_adder_8 (
    .A(A[25]), .B(B[25]), .C_in(full_adder_4_c_out), .Soma(Soma[25]), .C_out(full_adder_8_c_out));
  nor nor_1 (Zero, Soma[31], Soma[30], Soma[29], Soma[28], Soma[27], Soma[26], Soma[25], Soma[24], Soma[23], Soma[22], Soma[21], Soma[20], Soma[19], Soma[18], Soma[17], Soma[16], Soma[14], Soma[13], Soma[12], Soma[11], Soma[10], Soma[9], Soma[8], Soma[7], Soma[6], Soma[5], Soma[4], Soma[3], Soma[2], Soma[1], Soma[0], Soma[15]);
  Full_Adder full_adder_9 (.A(A[2]), .B(B[2]), .C_in(full_adder_5_c_out), .Soma(Soma[2]), .C_out(full_adder_9_c_out));
  Full_Adder full_adder_10 (
    .A(A[10]), .B(B[10]), .C_in(full_adder_6_c_out), .Soma(Soma[10]), .C_out(full_adder_10_c_out));
  Full_Adder full_adder_11 (
    .A(A[18]), .B(B[18]), .C_in(full_adder_7_c_out), .Soma(Soma[18]), .C_out(full_adder_11_c_out));
  Full_Adder full_adder_12 (
    .A(A[26]), .B(B[26]), .C_in(full_adder_8_c_out), .Soma(Soma[26]), .C_out(full_adder_12_c_out));
  Full_Adder full_adder_13 (.A(A[3]), .B(B[3]), .C_in(full_adder_9_c_out), .Soma(Soma[3]), .C_out(full_adder_13_c_out));
  Full_Adder full_adder_14 (
    .A(A[11]), .B(B[11]), .C_in(full_adder_10_c_out), .Soma(Soma[11]), .C_out(full_adder_14_c_out));
  Full_Adder full_adder_15 (
    .A(A[19]), .B(B[19]), .C_in(full_adder_11_c_out), .Soma(Soma[19]), .C_out(full_adder_15_c_out));
  Full_Adder full_adder_16 (
    .A(A[27]), .B(B[27]), .C_in(full_adder_12_c_out), .Soma(Soma[27]), .C_out(full_adder_16_c_out));
  Full_Adder full_adder_17 (
    .A(A[4]), .B(B[4]), .C_in(full_adder_13_c_out), .Soma(Soma[4]), .C_out(full_adder_17_c_out));
  Full_Adder full_adder_18 (
    .A(A[12]), .B(B[12]), .C_in(full_adder_14_c_out), .Soma(Soma[12]), .C_out(full_adder_18_c_out));
  Full_Adder full_adder_19 (
    .A(A[20]), .B(B[20]), .C_in(full_adder_15_c_out), .Soma(Soma[20]), .C_out(full_adder_19_c_out));
  Full_Adder full_adder_20 (
    .A(A[28]), .B(B[28]), .C_in(full_adder_16_c_out), .Soma(Soma[28]), .C_out(full_adder_20_c_out));
  Full_Adder full_adder_21 (
    .A(A[5]), .B(B[5]), .C_in(full_adder_17_c_out), .Soma(Soma[5]), .C_out(full_adder_21_c_out));
  Full_Adder full_adder_22 (
    .A(A[13]), .B(B[13]), .C_in(full_adder_18_c_out), .Soma(Soma[13]), .C_out(full_adder_22_c_out));
  Full_Adder full_adder_23 (
    .A(A[21]), .B(B[21]), .C_in(full_adder_19_c_out), .Soma(Soma[21]), .C_out(full_adder_23_c_out));
  Full_Adder full_adder_24 (
    .A(A[29]), .B(B[29]), .C_in(full_adder_20_c_out), .Soma(Soma[29]), .C_out(full_adder_24_c_out));
  Full_Adder full_adder_25 (
    .A(A[6]), .B(B[6]), .C_in(full_adder_21_c_out), .Soma(Soma[6]), .C_out(full_adder_25_c_out));
  Full_Adder full_adder_26 (
    .A(A[14]), .B(B[14]), .C_in(full_adder_22_c_out), .Soma(Soma[14]), .C_out(full_adder_26_c_out));
  Full_Adder full_adder_27 (
    .A(A[22]), .B(B[22]), .C_in(full_adder_23_c_out), .Soma(Soma[22]), .C_out(full_adder_27_c_out));
  Full_Adder full_adder_28 (
    .A(A[30]), .B(B[30]), .C_in(full_adder_24_c_out), .Soma(Soma[30]), .C_out(full_adder_28_c_out));
  Full_Adder full_adder_29 (
    .A(A[7]), .B(B[7]), .C_in(full_adder_25_c_out), .Soma(Soma[7]), .C_out(full_adder_29_c_out));
  Full_Adder full_adder_30 (
    .A(A[15]), .B(B[15]), .C_in(full_adder_26_c_out), .Soma(Soma[15]), .C_out(full_adder_30_c_out));
  Full_Adder full_adder_31 (
    .A(A[23]), .B(B[23]), .C_in(full_adder_27_c_out), .Soma(Soma[23]), .C_out(full_adder_31_c_out));
  Full_Adder full_adder_32 (.A(A[31]), .B(B[31]), .C_in(full_adder_28_c_out), .Soma(Soma[31]), .C_out(C_out));

  // Other names for the same wires on the sheet: S0 = Soma[0]; S1 = Soma[1]; S2 = Soma[2]; S3 = Soma[3]; S4 = Soma[4];
  //   S5 = Soma[5]; S6 = Soma[6]; S7 = Soma[7]; S8 = Soma[8]; S9 = Soma[9]; S10 = Soma[10]; S11 = Soma[11];
  //   S12 = Soma[12]; S13 = Soma[13]; S14 = Soma[14]; S15 = Soma[15]; S16 = Soma[16]; S17 = Soma[17]; S18 = Soma[18];
  //   S19 = Soma[19]; S20 = Soma[20]; S21 = Soma[21]; S22 = Soma[22]; S23 = Soma[23]; S24 = Soma[24]; S25 = Soma[25];
  //   S26 = Soma[26]; S27 = Soma[27]; S28 = Soma[28]; S29 = Soma[29]; S30 = Soma[30]; S31 = Soma[31]
endmodule

module Full_Adder (
  input  A,
  input  B,
  input  C_in,
  output Soma,
  output C_out
);

  wire and_1_out, and_2_out, xor_1_out;

  xor xor_1 (xor_1_out, A, B);
  xor xor_2 (Soma, xor_1_out, C_in);
  and and_1 (and_1_out, xor_1_out, C_in);
  and and_2 (and_2_out, A, B);
  or or_1 (C_out, and_1_out, and_2_out);
endmodule

module extZero (
  input  [15:0] entrada,
  output [31:0] Saida
);


  assign Saida = {{16{1'b0}}, entrada};
endmodule

module extSinal (
  input  [15:0] entrada,
  output [31:0] Saida
);


  assign Saida = {{17{entrada[15]}}, entrada[14:0]};
endmodule

module PC (
  input  [31:0] E,
  input  CLK,
  input  W,
  output [31:0] S
);

  wire multiplexer_1_out, multiplexer_2_out, multiplexer_3_out, multiplexer_4_out, multiplexer_5_out,
       multiplexer_6_out, multiplexer_7_out, multiplexer_8_out, multiplexer_9_out, multiplexer_10_out,
       multiplexer_11_out, multiplexer_12_out, multiplexer_13_out, multiplexer_14_out, multiplexer_15_out,
       multiplexer_16_out, multiplexer_17_out, multiplexer_18_out, multiplexer_19_out, multiplexer_20_out,
       multiplexer_21_out, multiplexer_22_out, multiplexer_23_out, multiplexer_24_out, multiplexer_25_out,
       multiplexer_26_out, multiplexer_27_out, multiplexer_28_out, multiplexer_29_out, multiplexer_30_out,
       multiplexer_31_out, multiplexer_32_out;

  D_Flip_Flop d_ff_1 (.D(multiplexer_1_out), .clk(CLK), .Q(S[0]));  // open: Qn, preset, reset
  Multiplexer multiplexer_1 (.in0(S[0]), .in1(E[0]), .out(multiplexer_1_out), .sel(W));
  D_Flip_Flop d_ff_2 (.D(multiplexer_2_out), .clk(CLK), .Q(S[8]));  // open: Qn, preset, reset
  Multiplexer multiplexer_2 (.in0(S[8]), .in1(E[8]), .out(multiplexer_2_out), .sel(W));
  D_Flip_Flop d_ff_3 (.D(multiplexer_3_out), .clk(CLK), .Q(S[16]));  // open: Qn, preset, reset
  Multiplexer multiplexer_3 (.in0(S[16]), .in1(E[16]), .out(multiplexer_3_out), .sel(W));
  D_Flip_Flop d_ff_4 (.D(multiplexer_4_out), .clk(CLK), .Q(S[24]));  // open: Qn, preset, reset
  Multiplexer multiplexer_4 (.in0(S[24]), .in1(E[24]), .out(multiplexer_4_out), .sel(W));
  Multiplexer multiplexer_5 (.in0(S[1]), .in1(E[1]), .out(multiplexer_5_out), .sel(W));
  Multiplexer multiplexer_6 (.in0(S[9]), .in1(E[9]), .out(multiplexer_6_out), .sel(W));
  Multiplexer multiplexer_7 (.in0(S[17]), .in1(E[17]), .out(multiplexer_7_out), .sel(W));
  Multiplexer multiplexer_8 (.in0(S[25]), .in1(E[25]), .out(multiplexer_8_out), .sel(W));
  D_Flip_Flop d_ff_5 (.D(multiplexer_5_out), .clk(CLK), .Q(S[1]));  // open: Qn, preset, reset
  D_Flip_Flop d_ff_6 (.D(multiplexer_6_out), .clk(CLK), .Q(S[9]));  // open: Qn, preset, reset
  D_Flip_Flop d_ff_7 (.D(multiplexer_7_out), .clk(CLK), .Q(S[17]));  // open: Qn, preset, reset
  D_Flip_Flop d_ff_8 (.D(multiplexer_8_out), .clk(CLK), .Q(S[25]));  // open: Qn, preset, reset
  Multiplexer multiplexer_9 (.in0(S[2]), .in1(E[2]), .out(multiplexer_9_out), .sel(W));
  Multiplexer multiplexer_10 (.in0(S[10]), .in1(E[10]), .out(multiplexer_10_out), .sel(W));
  Multiplexer multiplexer_11 (.in0(S[18]), .in1(E[18]), .out(multiplexer_11_out), .sel(W));
  Multiplexer multiplexer_12 (.in0(S[26]), .in1(E[26]), .out(multiplexer_12_out), .sel(W));
  D_Flip_Flop d_ff_9 (.D(multiplexer_9_out), .clk(CLK), .Q(S[2]));  // open: Qn, preset, reset
  D_Flip_Flop d_ff_10 (.D(multiplexer_10_out), .clk(CLK), .Q(S[10]));  // open: Qn, preset, reset
  D_Flip_Flop d_ff_11 (.D(multiplexer_11_out), .clk(CLK), .Q(S[18]));  // open: Qn, preset, reset
  D_Flip_Flop d_ff_12 (.D(multiplexer_12_out), .clk(CLK), .Q(S[26]));  // open: Qn, preset, reset
  D_Flip_Flop d_ff_13 (.D(multiplexer_13_out), .clk(CLK), .Q(S[3]));  // open: Qn, preset, reset
  Multiplexer multiplexer_13 (.in0(S[3]), .in1(E[3]), .out(multiplexer_13_out), .sel(W));
  D_Flip_Flop d_ff_14 (.D(multiplexer_14_out), .clk(CLK), .Q(S[11]));  // open: Qn, preset, reset
  Multiplexer multiplexer_14 (.in0(S[11]), .in1(E[11]), .out(multiplexer_14_out), .sel(W));
  D_Flip_Flop d_ff_15 (.D(multiplexer_15_out), .clk(CLK), .Q(S[19]));  // open: Qn, preset, reset
  Multiplexer multiplexer_15 (.in0(S[19]), .in1(E[19]), .out(multiplexer_15_out), .sel(W));
  D_Flip_Flop d_ff_16 (.D(multiplexer_16_out), .clk(CLK), .Q(S[27]));  // open: Qn, preset, reset
  Multiplexer multiplexer_16 (.in0(S[27]), .in1(E[27]), .out(multiplexer_16_out), .sel(W));
  Multiplexer multiplexer_17 (.in0(S[4]), .in1(E[4]), .out(multiplexer_17_out), .sel(W));
  Multiplexer multiplexer_18 (.in0(S[12]), .in1(E[12]), .out(multiplexer_18_out), .sel(W));
  Multiplexer multiplexer_19 (.in0(S[20]), .in1(E[20]), .out(multiplexer_19_out), .sel(W));
  Multiplexer multiplexer_20 (.in0(S[28]), .in1(E[28]), .out(multiplexer_20_out), .sel(W));
  D_Flip_Flop d_ff_17 (.D(multiplexer_17_out), .clk(CLK), .Q(S[4]));  // open: Qn, preset, reset
  D_Flip_Flop d_ff_18 (.D(multiplexer_18_out), .clk(CLK), .Q(S[12]));  // open: Qn, preset, reset
  D_Flip_Flop d_ff_19 (.D(multiplexer_19_out), .clk(CLK), .Q(S[20]));  // open: Qn, preset, reset
  D_Flip_Flop d_ff_20 (.D(multiplexer_20_out), .clk(CLK), .Q(S[28]));  // open: Qn, preset, reset
  D_Flip_Flop d_ff_21 (.D(multiplexer_21_out), .clk(CLK), .Q(S[5]));  // open: Qn, preset, reset
  Multiplexer multiplexer_21 (.in0(S[5]), .in1(E[5]), .out(multiplexer_21_out), .sel(W));
  D_Flip_Flop d_ff_22 (.D(multiplexer_22_out), .clk(CLK), .Q(S[13]));  // open: Qn, preset, reset
  Multiplexer multiplexer_22 (.in0(S[13]), .in1(E[13]), .out(multiplexer_22_out), .sel(W));
  D_Flip_Flop d_ff_23 (.D(multiplexer_23_out), .clk(CLK), .Q(S[21]));  // open: Qn, preset, reset
  Multiplexer multiplexer_23 (.in0(S[21]), .in1(E[21]), .out(multiplexer_23_out), .sel(W));
  D_Flip_Flop d_ff_24 (.D(multiplexer_24_out), .clk(CLK), .Q(S[29]));  // open: Qn, preset, reset
  Multiplexer multiplexer_24 (.in0(S[29]), .in1(E[29]), .out(multiplexer_24_out), .sel(W));
  Multiplexer multiplexer_25 (.in0(S[6]), .in1(E[6]), .out(multiplexer_25_out), .sel(W));
  Multiplexer multiplexer_26 (.in0(S[14]), .in1(E[14]), .out(multiplexer_26_out), .sel(W));
  Multiplexer multiplexer_27 (.in0(S[22]), .in1(E[22]), .out(multiplexer_27_out), .sel(W));
  Multiplexer multiplexer_28 (.in0(S[30]), .in1(E[30]), .out(multiplexer_28_out), .sel(W));
  D_Flip_Flop d_ff_25 (.D(multiplexer_25_out), .clk(CLK), .Q(S[6]));  // open: Qn, preset, reset
  D_Flip_Flop d_ff_26 (.D(multiplexer_26_out), .clk(CLK), .Q(S[14]));  // open: Qn, preset, reset
  D_Flip_Flop d_ff_27 (.D(multiplexer_27_out), .clk(CLK), .Q(S[22]));  // open: Qn, preset, reset
  D_Flip_Flop d_ff_28 (.D(multiplexer_28_out), .clk(CLK), .Q(S[30]));  // open: Qn, preset, reset
  D_Flip_Flop d_ff_29 (.D(multiplexer_29_out), .clk(CLK), .Q(S[7]));  // open: Qn, preset, reset
  Multiplexer multiplexer_29 (.in0(S[7]), .in1(E[7]), .out(multiplexer_29_out), .sel(W));
  D_Flip_Flop d_ff_30 (.D(multiplexer_30_out), .clk(CLK), .Q(S[15]));  // open: Qn, preset, reset
  Multiplexer multiplexer_30 (.in0(S[15]), .in1(E[15]), .out(multiplexer_30_out), .sel(W));
  D_Flip_Flop d_ff_31 (.D(multiplexer_31_out), .clk(CLK), .Q(S[23]));  // open: Qn, preset, reset
  Multiplexer multiplexer_31 (.in0(S[23]), .in1(E[23]), .out(multiplexer_31_out), .sel(W));
  D_Flip_Flop d_ff_32 (.D(multiplexer_32_out), .clk(CLK), .Q(S[31]));  // open: Qn, preset, reset
  Multiplexer multiplexer_32 (.in0(S[31]), .in1(E[31]), .out(multiplexer_32_out), .sel(W));

  // Other names for the same wires on the sheet: D0 = E[0]; D1 = E[1]; D2 = E[2]; D3 = E[3]; D4 = E[4]; D5 = E[5];
  //   D6 = E[6]; D7 = E[7]; D8 = E[8]; D9 = E[9]; D10 = E[10]; D11 = E[11]; D12 = E[12]; D13 = E[13]; D14 = E[14];
  //   D15 = E[15]; D16 = E[16]; D17 = E[17]; D18 = E[18]; D19 = E[19]; D20 = E[20]; D21 = E[21]; D22 = E[22];
  //   D23 = E[23]; D24 = E[24]; D25 = E[25]; D26 = E[26]; D27 = E[27]; D28 = E[28]; D29 = E[29]; D30 = E[30];
  //   D31 = E[31]

  // Notes on the sheet:
  //   CLK
  //   W0 (enable)
  //   Dados (saida)
endmodule

module Shifter_1bit (
  input  [31:0] Entrada,
  output [31:0] Saida
);


  assign Saida = {Entrada[30:0], 1'b0};

  // Other names for the same wires on the sheet: B31 = Entrada[31]; B0 = Entrada[0]; B1 = Entrada[1]; B2 = Entrada[2];
  //   B3 = Entrada[3]; B4 = Entrada[4]; B5 = Entrada[5]; B6 = Entrada[6]; B7 = Entrada[7]; B8 = Entrada[8];
  //   B9 = Entrada[9]; B10 = Entrada[10]; B11 = Entrada[11]; B12 = Entrada[12]; B13 = Entrada[13]; B14 = Entrada[14];
  //   B15 = Entrada[15]; B16 = Entrada[16]; B17 = Entrada[17]; B18 = Entrada[18]; B19 = Entrada[19];
  //   B20 = Entrada[20]; B21 = Entrada[21]; B22 = Entrada[22]; B23 = Entrada[23]; B24 = Entrada[24];
  //   B25 = Entrada[25]; B26 = Entrada[26]; B27 = Entrada[27]; B28 = Entrada[28]; B29 = Entrada[29];
  //   B30 = Entrada[30]
endmodule

module Shifter_2bit (
  input  [31:0] Entrada,
  output [31:0] Saida
);


  assign Saida = {Entrada[29:0], 2'b00};

  // Other names for the same wires on the sheet: B30 = Entrada[30]; B31 = Entrada[31]; B0 = Entrada[0];
  //   B1 = Entrada[1]; B2 = Entrada[2]; B3 = Entrada[3]; B4 = Entrada[4]; B5 = Entrada[5]; B6 = Entrada[6];
  //   B7 = Entrada[7]; B8 = Entrada[8]; B9 = Entrada[9]; B10 = Entrada[10]; B11 = Entrada[11]; B12 = Entrada[12];
  //   B13 = Entrada[13]; B14 = Entrada[14]; B15 = Entrada[15]; B16 = Entrada[16]; B17 = Entrada[17];
  //   B18 = Entrada[18]; B19 = Entrada[19]; B20 = Entrada[20]; B21 = Entrada[21]; B22 = Entrada[22];
  //   B23 = Entrada[23]; B24 = Entrada[24]; B25 = Entrada[25]; B26 = Entrada[26]; B27 = Entrada[27];
  //   B28 = Entrada[28]; B29 = Entrada[29]
endmodule

module Shifter_4bit (
  input  [31:0] Entrada,
  output [31:0] Saida
);


  assign Saida = {Entrada[27:0], 4'b0000};

  // Other names for the same wires on the sheet: B28 = Entrada[28]; B29 = Entrada[29]; B30 = Entrada[30];
  //   B31 = Entrada[31]; B0 = Entrada[0]; B1 = Entrada[1]; B2 = Entrada[2]; B3 = Entrada[3]; B4 = Entrada[4];
  //   B5 = Entrada[5]; B6 = Entrada[6]; B7 = Entrada[7]; B8 = Entrada[8]; B9 = Entrada[9]; B10 = Entrada[10];
  //   B11 = Entrada[11]; B12 = Entrada[12]; B13 = Entrada[13]; B14 = Entrada[14]; B15 = Entrada[15];
  //   B16 = Entrada[16]; B17 = Entrada[17]; B18 = Entrada[18]; B19 = Entrada[19]; B20 = Entrada[20];
  //   B21 = Entrada[21]; B22 = Entrada[22]; B23 = Entrada[23]; B24 = Entrada[24]; B25 = Entrada[25];
  //   B26 = Entrada[26]; B27 = Entrada[27]
endmodule

module Shifter_8bit (
  input  [31:0] Entrada,
  output [31:0] Saida
);


  assign Saida = {Entrada[23:0], {8{1'b0}}};

  // Other names for the same wires on the sheet: B24 = Entrada[24]; B25 = Entrada[25]; B26 = Entrada[26];
  //   B27 = Entrada[27]; B28 = Entrada[28]; B29 = Entrada[29]; B30 = Entrada[30]; B31 = Entrada[31]; B0 = Entrada[0];
  //   B1 = Entrada[1]; B2 = Entrada[2]; B3 = Entrada[3]; B4 = Entrada[4]; B5 = Entrada[5]; B6 = Entrada[6];
  //   B7 = Entrada[7]; B8 = Entrada[8]; B9 = Entrada[9]; B10 = Entrada[10]; B11 = Entrada[11]; B12 = Entrada[12];
  //   B13 = Entrada[13]; B14 = Entrada[14]; B15 = Entrada[15]; B16 = Entrada[16]; B17 = Entrada[17];
  //   B18 = Entrada[18]; B19 = Entrada[19]; B20 = Entrada[20]; B21 = Entrada[21]; B22 = Entrada[22];
  //   B23 = Entrada[23]
endmodule

module Shifter_16bits (
  input  [31:0] Entrada,
  output [31:0] Saida
);


  assign Saida = {Entrada[15:0], {16{1'b0}}};

  // Other names for the same wires on the sheet: B16 = Entrada[16]; B17 = Entrada[17]; B18 = Entrada[18];
  //   B19 = Entrada[19]; B20 = Entrada[20]; B21 = Entrada[21]; B22 = Entrada[22]; B23 = Entrada[23];
  //   B24 = Entrada[24]; B25 = Entrada[25]; B26 = Entrada[26]; B27 = Entrada[27]; B28 = Entrada[28];
  //   B29 = Entrada[29]; B30 = Entrada[30]; B31 = Entrada[31]; B0 = Entrada[0]; B1 = Entrada[1]; B2 = Entrada[2];
  //   B3 = Entrada[3]; B4 = Entrada[4]; B5 = Entrada[5]; B6 = Entrada[6]; B7 = Entrada[7]; B8 = Entrada[8];
  //   B9 = Entrada[9]; B10 = Entrada[10]; B11 = Entrada[11]; B12 = Entrada[12]; B13 = Entrada[13]; B14 = Entrada[14];
  //   B15 = Entrada[15]
endmodule
